// Logisim project 数据重定向 - 气泡.circ as structural Verilog
// ALU
module \ALU16位运算器  (
  input  [15:0] \输入A ,
  input  [15:0] \输入B ,
  input  [3:0] \控制信息C ,
  output \进位 ,
  output \零 ,
  output \溢出 ,
  output [15:0] \输出F 
);

  wire bit_extender_2_out, \flag_取一个数的最高位_1_flag_value的最高位 , \flag_取一个数的最高位_2_flag_value的最高位 ,
       \flag_取一个数的最高位_3_flag_value的最高位 , \flag_取一个数的最高位_4_flag_value的最高位 , \flag_取一个数的最高位_5_flag_value的最高位 ,
       \flag_取一个数的最高位_6_flag_value的最高位 , \减法溢出_1_overflow_溢出 , \加法溢出_1_overflow_溢出 ;
  wire [3:0] bit_extender_1_out;
  wire [15:0] adder_1_out, and_1_out, divider_1_out, multiplier_1_out, not_1_out, or_1_out, shifter_1_out,
       shifter_2_out, shifter_3_out, subtractor_1_out, xor_1_out;

  Bit_Extender #(.in_width(16), .out_width(4)) bit_extender_1 (.in(\输入B ), .out(bit_extender_1_out));
  \Flag_取一个数的最高位  \flag_取一个数的最高位_1  (.\value_输入的值 (\输入A ), .\flag_value的最高位 (\flag_取一个数的最高位_1_flag_value的最高位 ));
  \Flag_取一个数的最高位  \flag_取一个数的最高位_2  (.\value_输入的值 (\输入B ), .\flag_value的最高位 (\flag_取一个数的最高位_2_flag_value的最高位 ));
  \Flag_取一个数的最高位  \flag_取一个数的最高位_3  (.\value_输入的值 (adder_1_out), .\flag_value的最高位 (\flag_取一个数的最高位_3_flag_value的最高位 ));
  \Flag_取一个数的最高位  \flag_取一个数的最高位_4  (.\value_输入的值 (\输入A ), .\flag_value的最高位 (\flag_取一个数的最高位_4_flag_value的最高位 ));
  \Flag_取一个数的最高位  \flag_取一个数的最高位_5  (.\value_输入的值 (\输入B ), .\flag_value的最高位 (\flag_取一个数的最高位_5_flag_value的最高位 ));
  Adder #(.width(16)) adder_1 (.a(\输入A ), .b(\输入B ), .out(adder_1_out), .cin(1'b0));  // open: cout
  \加法溢出  \u_加法溢出_1  (
    .Flag_A(\flag_取一个数的最高位_1_flag_value的最高位 ), .Flag_B(\flag_取一个数的最高位_2_flag_value的最高位 ),
    .Flag_out(\flag_取一个数的最高位_3_flag_value的最高位 ), .\overflow_溢出 (\加法溢出_1_overflow_溢出 ));
  Subtractor #(.width(16)) subtractor_1 (.a(\输入A ), .b(\输入B ), .out(subtractor_1_out), .bin(1'b0));  // open: bout
  Multiplier #(.width(16)) multiplier_1 (.a(\输入A ), .b(\输入B ), .out(multiplier_1_out), .cin({16{1'b0}}));  // open: cout
  Divider #(.width(16)) divider_1 (.a(\输入A ), .b(\输入B ), .out(divider_1_out), .upper({16{1'b0}}));  // open: rem
  assign and_1_out = \输入A  & \输入B ;  // AND_Gate and_1, 16 bits wide
  assign or_1_out = \输入A  | \输入B ;  // OR_Gate or_1, 16 bits wide
  assign not_1_out = ~\输入A ;  // NOT_Gate not_1, 16 bits wide
  Shifter #(.width(16)) shifter_1 (.in(\输入A ), .\dist (bit_extender_1_out), .out(shifter_1_out));
  Shifter #(.width(16), .shift("lr")) shifter_2 (.in(\输入A ), .\dist (bit_extender_1_out), .out(shifter_2_out));
  Shifter #(.width(16), .shift("ar")) shifter_3 (.in(\输入A ), .\dist (bit_extender_1_out), .out(shifter_3_out));
  \减法溢出  \u_减法溢出_1  (
    .Flag_A(\flag_取一个数的最高位_4_flag_value的最高位 ), .Flag_B(\flag_取一个数的最高位_5_flag_value的最高位 ),
    .Flag_out(\flag_取一个数的最高位_6_flag_value的最高位 ), .\overflow_溢出 (\减法溢出_1_overflow_溢出 ));
  assign xor_1_out = \输入A  ^ \输入B ;  // XOR_Gate xor_1, 16 bits wide
  \Flag_取一个数的最高位  \flag_取一个数的最高位_6  (
    .\value_输入的值 (subtractor_1_out), .\flag_value的最高位 (\flag_取一个数的最高位_6_flag_value的最高位 ));
  Multiplexer multiplexer_1 (
    .in0(\加法溢出_1_overflow_溢出 ), .in1(\减法溢出_1_overflow_溢出 ), .out(\溢出 ), .sel(bit_extender_2_out), .en(1'b1));
  Bit_Extender #(.in_width(4), .out_width(1)) bit_extender_2 (.in(\控制信息C ), .out(bit_extender_2_out));
  Multiplexer #(.select(4), .width(16)) multiplexer_2 (
    .in0(adder_1_out), .in1(subtractor_1_out), .in2(multiplier_1_out), .in3(divider_1_out), .in4(and_1_out),
    .in5(or_1_out), .in6(not_1_out), .in7(xor_1_out), .in8(shifter_1_out), .in9(shifter_2_out),
    .in10(shifter_3_out), .out(\输出F ), .sel(\控制信息C ), .en(1'b1));  // open: in11, in12, in13, in14, in15
  Comparator #(.width(16), .mode("unsigned")) comparator_1 (.a(\输出F ), .b({16{1'b0}}), .eq(\零 ));  // open: gt, lt

  assign \进位  = \溢出 ;
endmodule

// 启停控制
module \启停控制电路  (
  input  \时钟 ,
  input  \重置信号 ,
  input  \启动_为1时启动 ,
  output \F_输出时钟 
);

  wire and_1_out, d_ff_1_q, nand_1_out, nand_2_out, not_1_out, not_2_out;

  not not_1 (not_1_out, \时钟 );
  nand nand_1 (nand_1_out, not_2_out, nand_2_out);
  not not_2 (not_2_out, \启动_为1时启动 );
  not not_3 (\F_输出时钟 , and_1_out);
  and and_1 (and_1_out, \时钟 , d_ff_1_q);
  D_Flip_Flop d_ff_1 (.clk(not_1_out), .D(nand_1_out), .Q(d_ff_1_q), .reset(\重置信号 ));  // open: Qn, preset, en
  nand nand_2 (nand_2_out, nand_1_out, 1'b1, \重置信号 );
endmodule

// 进制
module \进制转换器  (
  input  [15:0] \A_16位二进制数 ,
  output [3:0] \B0_转换成十进制后的0位 ,
  output [3:0] \B1_转换成十进制后的1位 ,
  output [3:0] \B2_转换成十进制后的2位 ,
  output [3:0] \B3_转换成十进制后的3位 ,
  output [3:0] \B4_转换成十进制后的4位 
);

  wire [15:0] divider_1_out, divider_1_rem, divider_2_out, divider_2_rem, divider_3_out, divider_3_rem,
       divider_4_out, divider_4_rem, divider_5_rem;

  Divider #(.width(16)) divider_1 (
    .a(\A_16位二进制数 ), .b(16'ha), .out(divider_1_out), .upper({16{1'b0}}), .rem(divider_1_rem));
  Bit_Extender #(.in_width(16), .out_width(4)) bit_extender_1 (.in(divider_1_rem), .out(\B0_转换成十进制后的0位 ));
  Divider #(.width(16)) divider_2 (
    .a(divider_1_out), .b(16'ha), .out(divider_2_out), .upper({16{1'b0}}), .rem(divider_2_rem));
  Bit_Extender #(.in_width(16), .out_width(4)) bit_extender_2 (.in(divider_2_rem), .out(\B1_转换成十进制后的1位 ));
  Divider #(.width(16)) divider_3 (
    .a(divider_2_out), .b(16'ha), .out(divider_3_out), .upper({16{1'b0}}), .rem(divider_3_rem));
  Bit_Extender #(.in_width(16), .out_width(4)) bit_extender_3 (.in(divider_3_rem), .out(\B2_转换成十进制后的2位 ));
  Divider #(.width(16)) divider_4 (
    .a(divider_3_out), .b(16'ha), .out(divider_4_out), .upper({16{1'b0}}), .rem(divider_4_rem));
  Bit_Extender #(.in_width(16), .out_width(4)) bit_extender_4 (.in(divider_4_rem), .out(\B3_转换成十进制后的3位 ));
  Divider #(.width(16)) divider_5 (.a(divider_4_out), .b(16'ha), .upper({16{1'b0}}), .rem(divider_5_rem));  // open: out
  Bit_Extender #(.in_width(16), .out_width(4)) bit_extender_5 (.in(divider_5_rem), .out(\B4_转换成十进制后的4位 ));
endmodule

// RF
module \RF_寄存器堆  (
  input  [1:0] W,
  input  \RegWrite_寄存器写控制信号 ,
  input  [15:0] Din,
  input  \CP_时钟输入 ,
  input  [1:0] rs,
  input  [1:0] rt,
  input  \ClR_清零信号 ,
  output [15:0] Do1,
  output [15:0] Do2,
  output [31:0] R1R0,
  output [31:0] R3R2
);

  wire and_1_out, and_2_out, and_3_out, and_4_out, decoder_1_out0, decoder_1_out1, decoder_1_out2,
       decoder_1_out3;

  Decoder #(.select(2)) decoder_1 (
    .out0(decoder_1_out0), .out1(decoder_1_out1), .out2(decoder_1_out2), .out3(decoder_1_out3), .sel(W),
    .en(1'b1));
  // Probe on Din
  and and_1 (and_1_out, decoder_1_out0, \RegWrite_寄存器写控制信号 );
  and and_2 (and_2_out, decoder_1_out1, \RegWrite_寄存器写控制信号 );
  and and_3 (and_3_out, decoder_1_out2, \RegWrite_寄存器写控制信号 );
  and and_4 (and_4_out, decoder_1_out3, \RegWrite_寄存器写控制信号 );
  Register #(.width(16), .trigger("falling")) R0 (
    .D(Din), .en(and_1_out), .Q(R1R0[15:0]), .clk(\CP_时钟输入 ), .clr(\ClR_清零信号 ));
  Register #(.width(16), .trigger("falling")) R1 (
    .D(Din), .en(and_2_out), .Q(R1R0[31:16]), .clk(\CP_时钟输入 ), .clr(\ClR_清零信号 ));
  Register #(.width(16), .trigger("falling")) R2 (
    .D(Din), .en(and_3_out), .Q(R3R2[15:0]), .clk(\CP_时钟输入 ), .clr(\ClR_清零信号 ));
  Register #(.width(16), .trigger("falling")) R3 (
    .D(Din), .en(and_4_out), .Q(R3R2[31:16]), .clk(\CP_时钟输入 ), .clr(\ClR_清零信号 ));
  Multiplexer #(.select(2), .width(16), .enable("false")) multiplexer_1 (
    .in0(R1R0[15:0]), .in1(R1R0[31:16]), .in2(R3R2[15:0]), .in3(R3R2[31:16]), .out(Do1), .sel(rs));
  Multiplexer #(.select(2), .width(16), .enable("false")) multiplexer_2 (
    .in0(R1R0[15:0]), .in1(R1R0[31:16]), .in2(R3R2[15:0]), .in3(R3R2[31:16]), .out(Do2), .sel(rt));
endmodule

module \RF_寄存器堆_测试  (
  input  [15:0] in_1,
  input  [1:0] in_2,
  input  [1:0] in_3,
  input  [1:0] in_4,
  input  in_5,
  input  in_6,
  output [15:0] out_7,
  output [15:0] out_8,
  output [15:0] out_9,
  output [15:0] out_10,
  output [15:0] out_11,
  output [15:0] out_12,
  output [15:0] out_13,
  output [15:0] out_14,
  output [15:0] out_15,
  output [15:0] out_16,
  output [15:0] out_17,
  output [15:0] out_18
);

  wire CP;

  Button button_1 (.out(CP));
  \RF_寄存器堆  \rf_寄存器堆_1  (
    .Din(in_1), .\CP_时钟输入 (CP), .Do1(out_17), .rs(in_2), .Do2(out_18), .rt(in_3), .R1R0({out_13, out_14}),
    .R3R2({out_11, out_12}), .W(in_4), .\RegWrite_寄存器写控制信号 (in_5), .\ClR_清零信号 (in_6));
  \RF_寄存器堆2  \rf_寄存器堆2_1  (
    .\CP_时钟输入 (CP), .Do1(out_15), .Do2(out_16), .R1R0({out_9, out_10}), .R3R2({out_7, out_8}), .Din(in_1),
    .rs(in_2), .rt(in_3), .W(in_4), .\RrgWrite_寄存器写控制信号 (in_5));

  // Other names for the same wires on the sheet: Din[15:0] = in_1; RegWrite = in_5; rs[1:0] = in_2; rt[1:0] = in_3;
  //   w[1:0] = in_4
endmodule

// IDecoder
module \IDecoder_指令译码器  (
  input  [15:0] \Instruction_指令 ,
  output [2:0] Funct,
  output [2:0] P,
  output [1:0] rd,
  output [1:0] rt,
  output [1:0] rs,
  output [3:0] OP,
  output [7:0] immediate,
  output [11:0] jump_address
);


  assign Funct = \Instruction_指令 [2:0];
  assign immediate = \Instruction_指令 [7:0];
  assign jump_address = \Instruction_指令 [11:0];
  assign OP = \Instruction_指令 [15:12];
  assign P = \Instruction_指令 [5:3];
  assign rd = \Instruction_指令 [7:6];
  assign rs = \Instruction_指令 [11:10];
  assign rt = \Instruction_指令 [9:8];
endmodule

module \指令译码器测试电路  (
  input  [15:0] in_1,
  output [2:0] out_2,
  output [2:0] out_3,
  output [1:0] out_4,
  output [1:0] out_5,
  output [1:0] out_6,
  output [3:0] out_7,
  output [7:0] out_8,
  output [11:0] out_9
);

  \IDecoder_指令译码器  \idecoder_指令译码器_1  (
    .\Instruction_指令 (in_1), .Funct(out_2), .P(out_3), .rd(out_6), .rt(out_5), .rs(out_4), .OP(out_7),
    .immediate(out_8), .jump_address(out_9));
endmodule

module \ALUop译码  (
  input  [2:0] \Funct_指令的Funct字段_3位 ,
  input  [3:0] \OP_指令的操作码字段_4位 ,
  output [3:0] \ALUop_ALU操作码_4位 
);

  wire or_1_out;
  wire [3:0] funct_aluop_1_aluop, \op_aluop_1_aluop_alu操作码 ;

  Funct__ALUop funct_aluop_1 (.Funct(\Funct_指令的Funct字段_3位 ), .ALUop(funct_aluop_1_aluop));
  OP__ALUop op_aluop_1 (.\OP_操作码 (\OP_指令的操作码字段_4位 ), .\ALUop_ALU操作码 (\op_aluop_1_aluop_alu操作码 ));
  or or_1 (or_1_out, \OP_指令的操作码字段_4位 [0], \OP_指令的操作码字段_4位 [1], \OP_指令的操作码字段_4位 [2], \OP_指令的操作码字段_4位 [3]);
  Multiplexer #(.width(4), .enable("false")) multiplexer_1 (
    .in0(funct_aluop_1_aluop), .in1(\op_aluop_1_aluop_alu操作码 ), .out(\ALUop_ALU操作码_4位 ), .sel(or_1_out));
endmodule

module Funct__ALUop (
  input  [2:0] Funct,
  output [3:0] ALUop
);

  wire and_1_out, and_2_out, and_3_out, and_6_out, and_7_out, and_8_out, and_9_out, not_1_out, not_2_out,
       not_3_out, not_4_out, not_5_out, not_6_out, not_7_out, not_8_out, or_2_out;

  not not_1 (not_1_out, Funct[1]);
  not not_2 (not_2_out, Funct[0]);
  not not_3 (not_3_out, Funct[2]);
  not not_4 (not_4_out, Funct[1]);
  and and_1 (and_1_out, Funct[2], Funct[1]);
  not not_5 (not_5_out, Funct[0]);
  not not_6 (not_6_out, Funct[2]);
  not not_7 (not_7_out, Funct[1]);
  and and_2 (and_2_out, Funct[2], not_1_out);
  and and_3 (and_3_out, Funct[2], not_2_out);
  and and_4 (ALUop[2], not_3_out, not_4_out);
  and and_5 (ALUop[1], and_1_out, not_5_out);
  and and_6 (and_6_out, not_6_out, not_7_out);
  not not_8 (not_8_out, Funct[0]);
  or or_1 (ALUop[3], and_2_out, and_3_out);
  and and_7 (and_7_out, and_6_out, not_8_out);
  and and_8 (and_8_out, Funct[1], Funct[0]);
  or or_2 (or_2_out, and_7_out, and_8_out);
  and and_9 (and_9_out, Funct[2], Funct[0]);
  or or_3 (ALUop[0], or_2_out, and_9_out);
endmodule

module OP__ALUop (
  input  [3:0] \OP_操作码 ,
  output [3:0] \ALUop_ALU操作码 
);

  wire and_1_out, and_3_out, and_4_out, and_5_out, and_6_out, and_7_out, and_8_out, and_9_out, and_10_out,
       and_11_out, and_12_out, not_1_out, not_2_out, not_3_out, not_4_out, not_5_out, not_6_out, not_7_out,
       not_8_out, not_9_out, or_1_out, or_2_out, or_3_out;

  not not_1 (not_1_out, \OP_操作码 [1]);
  not not_2 (not_2_out, \OP_操作码 [3]);
  not not_3 (not_3_out, \OP_操作码 [1]);
  not not_4 (not_4_out, \OP_操作码 [2]);
  and and_1 (and_1_out, \OP_操作码 [2], not_1_out);
  and and_2 (\ALUop_ALU操作码 [3], and_1_out, \OP_操作码 [0]);
  and and_3 (and_3_out, not_2_out, not_3_out);
  and and_4 (and_4_out, and_3_out, not_5_out);
  not not_5 (not_5_out, \OP_操作码 [0]);
  and and_5 (and_5_out, \OP_操作码 [2], not_6_out);
  not not_6 (not_6_out, \OP_操作码 [0]);
  and and_6 (and_6_out, \OP_操作码 [2], \OP_操作码 [1]);
  and and_7 (and_7_out, \OP_操作码 [3], \OP_操作码 [1]);
  and and_8 (and_8_out, and_7_out, \OP_操作码 [0]);
  not not_7 (not_7_out, \OP_操作码 [3]);
  and and_9 (and_9_out, not_7_out, not_8_out);
  not not_8 (not_8_out, \OP_操作码 [2]);
  and and_10 (and_10_out, not_4_out, \OP_操作码 [1]);
  and and_11 (and_11_out, and_10_out, \OP_操作码 [0]);
  not not_9 (not_9_out, \OP_操作码 [0]);
  or or_1 (or_1_out, and_4_out, and_5_out);
  or or_2 (or_2_out, and_6_out, and_8_out);
  or or_3 (or_3_out, and_9_out, and_11_out);
  and and_12 (and_12_out, \OP_操作码 [2], not_9_out);
  or or_4 (\ALUop_ALU操作码 [2], or_1_out, or_2_out);
  or or_5 (\ALUop_ALU操作码 [0], or_3_out, and_12_out);

  assign \ALUop_ALU操作码 [1] = 1'b0;
endmodule

module \OP__ALUop_可分析  (
  input  OP3,
  input  OP2,
  input  OP1,
  input  OP0,
  output ALUop3,
  output ALUop2,
  output ALUop1,
  output ALUop0
);

  wire and_1_out, and_3_out, and_4_out, and_5_out, and_6_out, and_7_out, and_8_out, and_9_out, and_10_out,
       and_11_out, and_12_out, not_1_out, not_2_out, not_3_out, not_4_out, not_5_out, not_6_out, not_7_out,
       not_8_out, not_9_out, or_1_out, or_2_out, or_3_out;

  not not_1 (not_1_out, OP1);
  not not_2 (not_2_out, OP3);
  not not_3 (not_3_out, OP1);
  not not_4 (not_4_out, OP2);
  and and_1 (and_1_out, OP2, not_1_out);
  and and_2 (ALUop3, and_1_out, OP0);
  and and_3 (and_3_out, not_2_out, not_3_out);
  and and_4 (and_4_out, and_3_out, not_5_out);
  not not_5 (not_5_out, OP0);
  and and_5 (and_5_out, OP2, not_6_out);
  not not_6 (not_6_out, OP0);
  and and_6 (and_6_out, OP2, OP1);
  and and_7 (and_7_out, OP3, OP1);
  and and_8 (and_8_out, and_7_out, OP0);
  not not_7 (not_7_out, OP3);
  and and_9 (and_9_out, not_7_out, not_8_out);
  not not_8 (not_8_out, OP2);
  and and_10 (and_10_out, not_4_out, OP1);
  and and_11 (and_11_out, and_10_out, OP0);
  not not_9 (not_9_out, OP0);
  or or_1 (or_1_out, and_4_out, and_5_out);
  or or_2 (or_2_out, and_6_out, and_8_out);
  or or_3 (or_3_out, and_9_out, and_11_out);
  and and_12 (and_12_out, OP2, not_9_out);
  or or_4 (ALUop2, or_1_out, or_2_out);
  or or_5 (ALUop0, or_3_out, and_12_out);

  assign ALUop1 = 1'b0;
endmodule

module \OP__ALUop_测试  (
  input  [3:0] OP,
  output [3:0] ALUop
);

  OP__ALUop op_aluop_1 (.\OP_操作码 (OP), .\ALUop_ALU操作码 (ALUop));
endmodule

module \Funct__ALUop_可分析  (
  input  Funct2,
  input  Funct1,
  input  Funct0,
  output ALUop3,
  output ALUop2,
  output ALUop1,
  output ALUop0
);

  wire and_1_out, and_2_out, and_3_out, and_6_out, and_7_out, and_8_out, and_9_out, not_1_out, not_2_out,
       not_3_out, not_4_out, not_5_out, not_6_out, not_7_out, not_8_out, or_2_out;

  not not_1 (not_1_out, Funct1);
  not not_2 (not_2_out, Funct0);
  not not_3 (not_3_out, Funct2);
  not not_4 (not_4_out, Funct1);
  and and_1 (and_1_out, Funct2, Funct1);
  not not_5 (not_5_out, Funct0);
  not not_6 (not_6_out, Funct2);
  not not_7 (not_7_out, Funct1);
  and and_2 (and_2_out, Funct2, not_1_out);
  and and_3 (and_3_out, Funct2, not_2_out);
  and and_4 (ALUop2, not_3_out, not_4_out);
  and and_5 (ALUop1, and_1_out, not_5_out);
  and and_6 (and_6_out, not_6_out, not_7_out);
  not not_8 (not_8_out, Funct0);
  or or_1 (ALUop3, and_2_out, and_3_out);
  and and_7 (and_7_out, and_6_out, not_8_out);
  and and_8 (and_8_out, Funct1, Funct0);
  or or_2 (or_2_out, and_7_out, and_8_out);
  and and_9 (and_9_out, Funct2, Funct0);
  or or_3 (ALUop0, or_2_out, and_9_out);
endmodule

// Funct
module \Funct__ALUop_测试  (
  input  [2:0] Funct,
  output [3:0] ALUop
);

  Funct__ALUop funct_aluop_1 (.Funct(Funct), .ALUop(ALUop));
endmodule

module \单周期电路总框架  (
  input  \为1时启动 ,
  output [2:0] out_2,
  output [3:0] out_3,
  output [15:0] R3,
  output [15:0] R2,
  output [15:0] R1,
  output [15:0] R0,
  output [15:0] R0_2,
  output [15:0] out_9,
  output [3:0] out_10,
  output [15:0] R0_3
);

  wire \alu16位运算器_1_溢出 , \alu16位运算器_1_零 , ALUsrc, and_1_out, branch, CK, clock, clr, disp, disp_color,
       \flag_取一个数的最高位_1_flag_value的最高位 , halt, lui, MemtoReg, MemWriet, not_1_out, part_1_out_3, RegDst,
       RegWrite, slt, slt_0_1_1_slt_0_1;
  wire [1:0] \idecoder_指令译码器_1_rd , \idecoder_指令译码器_1_rs , \idecoder_指令译码器_1_rt , multiplexer_2_out;
  wire [3:0] \跳转地址形成部件_1_jump_address , \跳转地址形成部件_1_jump_address_2 , \跳转地址形成部件_1_jump_address_3 ;
  wire [7:1] \idecoder_指令译码器_1_immediate ;
  wire [11:0] counter_1_q, \idecoder_指令译码器_1_jump_address ;
  wire [15:0] adder_1_out, bit_extender_1_out, DISP_0, DISP_1, \extend_立即数符号扩展_1_extended_value_扩展结果 ,
       multiplexer_1_out, multiplexer_3_out, multiplexer_4_out, multiplexer_5_out, multiplexer_6_out,
       multiplexer_7_out, ram_1_data, \rf_寄存器堆_1_do1 , \rf_寄存器堆_1_do2 , rom_1_data;
  wire [15:12] \跳转地址形成部件_1_jump_address_4 ;

  Counter #(.width(12), .max('hfff), .trigger("falling")) counter_1 (
    .count(1'b1), .Q(counter_1_q), .clk(clock), .clr(clr));  // open: load, D, carry
  Multiplexer #(.width(16), .enable("false")) multiplexer_1 (
    .in0(adder_1_out),
    .in1({\跳转地址形成部件_1_jump_address_4 , \跳转地址形成部件_1_jump_address_3 , \跳转地址形成部件_1_jump_address_2 , \跳转地址形成部件_1_jump_address }),
    .out(multiplexer_1_out), .sel(branch));
  Register #(.width(16), .trigger("falling")) PC (.D(multiplexer_1_out), .en(1'b1), .Q(out_9), .clk(clock), .clr(clr));
  Hex_Digit_Display hex_digit_display_1 (.value(\跳转地址形成部件_1_jump_address_3 ));  // open: dp
  Hex_Digit_Display hex_digit_display_2 (.value(\跳转地址形成部件_1_jump_address_4 ));  // open: dp
  \控制器  \u_控制器_1  (
    .\OP_操作码 (out_3), .Funct(out_2), .RegDst(RegDst), .\lui_lui指令产生的单一控制信号 (lui), .MemWrite(MemWriet),
    .MemtoReg(MemtoReg), .RegWrite(RegWrite), .ALUSrc(ALUsrc), .ALUop(out_10), .disp(disp),
    .\halt_停机控制信号 (halt), .\slt_slt控制信号 (slt));
  // Probe on counter_1_q
  Adder #(.width(16)) adder_1 (.a(16'h1), .b(out_9), .out(adder_1_out), .cin(1'b0));  // open: cout
  Hex_Digit_Display hex_digit_display_3 (.value(\跳转地址形成部件_1_jump_address_2 ));  // open: dp
  Hex_Digit_Display hex_digit_display_4 (.value(\跳转地址形成部件_1_jump_address ));  // open: dp
  and and_1 (and_1_out, \为1时启动 , not_1_out);
  not not_1 (not_1_out, halt);
  \启停控制电路  \u_启停控制电路_1  (.\F_输出时钟 (clock), .\时钟 (CK), .\启动_为1时启动 (and_1_out), .\重置信号 (clr));
  Clock \u_时钟  (.out(CK));
  \IDecoder_指令译码器  \idecoder_指令译码器_1  (
    .\Instruction_指令 (rom_1_data), .Funct(out_2), .rd(\idecoder_指令译码器_1_rd ), .rt(\idecoder_指令译码器_1_rt ),
    .rs(\idecoder_指令译码器_1_rs ), .OP(out_3), .immediate({\idecoder_指令译码器_1_immediate , disp_color}),
    .jump_address(\idecoder_指令译码器_1_jump_address ));  // open: P
  ROM #(.addrWidth(16), .dataWidth(16)) rom_1 (.addr(out_9), .data(rom_1_data));  // open: sel
  \跳转地址形成部件  \u_跳转地址形成部件_1  (
    .\Offset_条件跳转地址_8位 ({\idecoder_指令译码器_1_immediate , disp_color}), .\PC_1_顺序下地址 (adder_1_out),
    .\jump_address_无条件跳转地址_12位 (\idecoder_指令译码器_1_jump_address ), .\OP_操作码_4位 (out_3),
    .jump_address({\跳转地址形成部件_1_jump_address_4 , \跳转地址形成部件_1_jump_address_3 , \跳转地址形成部件_1_jump_address_2 , \跳转地址形成部件_1_jump_address }));
  Button \u_重置信号  (.out(clr));
  Hex_Digit_Display hex_digit_display_5 (.value(DISP_0[11:8]));  // open: dp
  Hex_Digit_Display hex_digit_display_6 (.value(DISP_0[15:12]));  // open: dp
  DISP u_disp_1 (
    .R3R2({R3, R2}), .R1R0({R1, R0}), .\r_num_rs__寄存器编号 (\idecoder_指令译码器_1_rs ),
    .\DISP_disp控制信号_用于更新寄存器的值 (disp), .\disp_color_颜色选择信号 (disp_color), .\CLK_时钟信号 (clock), .DISP_0(DISP_0),
    .DISP1(DISP_1), .\CLR_清零信号 (clr));
  Multiplexer #(.width(2), .enable("false")) multiplexer_2 (
    .in0(\idecoder_指令译码器_1_rt ), .in1(\idecoder_指令译码器_1_rd ), .out(multiplexer_2_out), .sel(RegDst));
  Hex_Digit_Display hex_digit_display_7 (.value(DISP_0[3:0]));  // open: dp
  Hex_Digit_Display hex_digit_display_8 (.value(DISP_0[7:4]));  // open: dp
  \Extend_立即数符号扩展  \extend_立即数符号扩展_1  (
    .\immidiate_立即数 ({\idecoder_指令译码器_1_immediate , disp_color}), .\OP_操作码 (out_3),
    .\Extended_value_扩展结果 (\extend_立即数符号扩展_1_extended_value_扩展结果 ));
  Hex_Digit_Display hex_digit_display_9 (.value(DISP_1[11:8]));  // open: dp
  Hex_Digit_Display hex_digit_display_10 (.value(DISP_1[15:12]));  // open: dp
  \RF_寄存器堆  \rf_寄存器堆_1  (
    .Din(multiplexer_6_out), .\CP_时钟输入 (clock), .Do1(\rf_寄存器堆_1_do1 ), .rs(\idecoder_指令译码器_1_rs ),
    .Do2(\rf_寄存器堆_1_do2 ), .rt(\idecoder_指令译码器_1_rt ), .R1R0({R1, R0}), .R3R2({R3, R2}),
    .W(multiplexer_2_out), .\RegWrite_寄存器写控制信号 (RegWrite), .\ClR_清零信号 (clr));
  Hex_Digit_Display hex_digit_display_11 (.value(DISP_1[7:4]));  // open: dp
  Hex_Digit_Display hex_digit_display_12 (.value(DISP_1[3:0]));  // open: dp
  Multiplexer #(.width(16), .enable("false")) multiplexer_3 (
    .in0(\rf_寄存器堆_1_do2 ), .in1(\extend_立即数符号扩展_1_extended_value_扩展结果 ), .out(multiplexer_3_out), .sel(ALUsrc));
  // Probe on multiplexer_4_out
  Multiplexer #(.width(16), .enable("false")) multiplexer_4 (
    .in0(\rf_寄存器堆_1_do1 ), .in1(\extend_立即数符号扩展_1_extended_value_扩展结果 ), .out(multiplexer_4_out), .sel(lui));
  Multiplexer #(.width(16), .enable("false")) multiplexer_5 (
    .in0(multiplexer_3_out), .in1(16'h8), .out(multiplexer_5_out), .sel(lui));
  Multiplexer #(.width(16), .enable("false")) multiplexer_6 (
    .in0(multiplexer_7_out), .in1(bit_extender_1_out), .out(multiplexer_6_out), .sel(slt));
  // Probe on multiplexer_5_out
  \Flag_取一个数的最高位  \flag_取一个数的最高位_1  (.\value_输入的值 (R0_2), .\flag_value的最高位 (\flag_取一个数的最高位_1_flag_value的最高位 ));
  \ALU16位运算器  \alu16位运算器_1  (
    .\输入A (multiplexer_4_out), .\输入B (multiplexer_5_out), .\控制信息C (out_10), .\零 (\alu16位运算器_1_零 ),
    .\溢出 (\alu16位运算器_1_溢出 ), .\输出F (R0_2));  // open: 进位
  slt_0_1 slt_0_1_1 (
    .\falg_符号位 (\flag_取一个数的最高位_1_flag_value的最高位 ), .\overflow_溢出信号 (\alu16位运算器_1_溢出 ), .\Funct_函数字段 (out_2),
    .\OP_操作码 (out_3), .slt_0_1(slt_0_1_1_slt_0_1));
  // Probe on bit_extender_1_out
  assign bit_extender_1_out = {{15{1'b0}}, slt_0_1_1_slt_0_1};  // Bit_Extender bit_extender_1
  circuit part_1 (
    .\falg_符号位 (\flag_取一个数的最高位_1_flag_value的最高位 ), .\overflow_溢出信号 (\alu16位运算器_1_溢出 ), .out_3(part_1_out_3));
  \Branch_控制部件  \branch_控制部件_1  (
    .\OP_操作码 (out_3), .\zero_零标志位 (\alu16位运算器_1_零 ), .\正负性 (part_1_out_3), .\branch_是否跳转的控制信号 (branch));
  RAM #(.addrWidth(16), .dataWidth(16), .bus("separate")) ram_1 (
    .addr(R0_2), .din(\rf_寄存器堆_1_do2 ), .data(ram_1_data), .str(MemWriet), .clk(clock), .ld(1'b1));  // open: sel, clr
  Multiplexer #(.width(16), .enable("false")) multiplexer_7 (
    .in0(R0_2), .in1(ram_1_data), .out(multiplexer_7_out), .sel(MemtoReg));

  // Other names for the same wires on the sheet: ALUop[3:0] = out_10; Funct[2:0] = out_2; OP[3:0] = out_3;
  //   start = \为1时启动 

  // Notes on the sheet:
  //   contents of rom_1 (hex, n*v repeats v):
  //   5001 52ff 5101 5303 1204 1003 5101 5202 5303 4000 2504 2603 5101 5202 5303 4001 3a04 3e03 5101 5202
  //   5303 4c00 c000
endmodule

// PCBranch
module \跳转地址形成部件  (
  input  [7:0] \Offset_条件跳转地址_8位 ,
  input  [15:0] \PC_1_顺序下地址 ,
  input  [11:0] \jump_address_无条件跳转地址_12位 ,
  input  [3:0] \OP_操作码_4位 ,
  output [15:0] jump_address
);

  wire and_2_out, not_1_out;
  wire [15:0] adder_1_out, and_1_out, bit_extender_1_out, bit_extender_2_out, bit_extender_3_out,
       multiplexer_1_out, or_1_out, subtractor_1_out;

  assign bit_extender_1_out = {{8{1'b0}}, \Offset_条件跳转地址_8位 };  // Bit_Extender bit_extender_1
  assign bit_extender_2_out = {{8{1'b1}}, \Offset_条件跳转地址_8位 };  // Bit_Extender bit_extender_2
  Multiplexer #(.width(16), .enable("false")) multiplexer_1 (
    .in0(bit_extender_1_out), .in1(bit_extender_2_out), .out(multiplexer_1_out), .sel(\Offset_条件跳转地址_8位 [7]));
  Subtractor #(.width(16)) subtractor_1 (.a(\PC_1_顺序下地址 ), .b(16'h1), .out(subtractor_1_out));  // open: bin, bout
  not not_1 (not_1_out, \OP_操作码_4位 [2]);
  assign and_1_out = subtractor_1_out & 16'hf000;  // AND_Gate and_1, 16 bits wide
  assign bit_extender_3_out = {{4{1'b0}}, \jump_address_无条件跳转地址_12位 };  // Bit_Extender bit_extender_3
  and and_2 (and_2_out, \OP_操作码_4位 [0], \OP_操作码_4位 [1], not_1_out, \OP_操作码_4位 [3]);
  Adder #(.width(16)) adder_1 (.a(multiplexer_1_out), .b(\PC_1_顺序下地址 ), .out(adder_1_out));  // open: cin, cout
  assign or_1_out = and_1_out | bit_extender_3_out;  // OR_Gate or_1, 16 bits wide
  Multiplexer #(.width(16), .enable("false")) multiplexer_2 (
    .in0(adder_1_out), .in1(or_1_out), .out(jump_address), .sel(and_2_out));
endmodule

module \寄存器对更新电路  (
  input  [1:0] in_1,
  input  [1:0] in_2,
  input  [1:0] in_3,
  input  [15:0] in_4,
  input  RegWrite,
  input  \为1时启动 ,
  output [15:0] R3,
  output [15:0] R2,
  output [15:0] R1,
  output [15:0] R0,
  output [15:0] R0_2,
  output [15:0] R0_3
);

  wire clock, clr, \时钟_out ;

  Clock \u_时钟  (.out(\时钟_out ));
  // RF_寄存器堆 rf_寄存器堆_1: pin names not known; wires that end beside it: in_1, in_2, in_3, in_4, {R3, R2}, 1'b1, {R1, R0}, clock, R0_2, R0_3
  \启停控制电路  \u_启停控制电路_1  (.\F_输出时钟 (clock), .\时钟 (\时钟_out ), .\启动_为1时启动 (\为1时启动 ), .\重置信号 (clr));
  Button \u_重置信号  (.out(clr));
endmodule

// RegWrit_Ctrl
module \RegWrite_控制部件  (
  input  [3:0] \OP_操作码 ,
  output out_2
);

  wire and_1_out, and_2_out, and_3_out, and_4_out, and_5_out, and_6_out, not_1_out, not_2_out, not_3_out,
       not_4_out, not_5_out, not_6_out, not_7_out, not_8_out, not_9_out, not_10_out, not_11_out, not_12_out,
       not_13_out, not_14_out;

  not not_1 (not_1_out, \OP_操作码 [0]);
  not not_2 (not_2_out, \OP_操作码 [1]);
  not not_3 (not_3_out, \OP_操作码 [2]);
  not not_4 (not_4_out, \OP_操作码 [3]);
  not not_5 (not_5_out, \OP_操作码 [3]);
  not not_6 (not_6_out, \OP_操作码 [1]);
  not not_7 (not_7_out, \OP_操作码 [3]);
  not not_8 (not_8_out, \OP_操作码 [0]);
  not not_9 (not_9_out, \OP_操作码 [3]);
  not not_10 (not_10_out, \OP_操作码 [2]);
  not not_11 (not_11_out, \OP_操作码 [1]);
  not not_12 (not_12_out, \OP_操作码 [0]);
  not not_13 (not_13_out, \OP_操作码 [2]);
  not not_14 (not_14_out, \OP_操作码 [1]);
  and and_1 (and_1_out, not_1_out, not_2_out, not_3_out, not_4_out);
  and and_2 (and_2_out, not_5_out, \OP_操作码 [2], not_6_out, \OP_操作码 [0]);
  and and_3 (and_3_out, not_7_out, \OP_操作码 [2], \OP_操作码 [1], not_8_out);
  and and_4 (and_4_out, not_9_out, \OP_操作码 [2], \OP_操作码 [1], \OP_操作码 [0]);
  and and_5 (and_5_out, \OP_操作码 [3], not_10_out, not_11_out, not_12_out);
  and and_6 (and_6_out, \OP_操作码 [3], not_13_out, not_14_out, \OP_操作码 [0]);
  or or_1 (out_2, and_1_out, and_2_out, and_3_out, and_4_out, and_5_out, and_6_out);
endmodule

// RegDst_Ctrl
module \RegDst_控制部件  (
  input  [3:0] \OP_操作码 ,
  output RegDst
);

  wire not_1_out, not_2_out, not_3_out, not_4_out;

  not not_1 (not_1_out, \OP_操作码 [0]);
  not not_2 (not_2_out, \OP_操作码 [1]);
  not not_3 (not_3_out, \OP_操作码 [2]);
  not not_4 (not_4_out, \OP_操作码 [3]);
  and and_1 (RegDst, not_1_out, not_2_out, not_3_out, not_4_out);
endmodule

// Ex_imm
module \Extend_立即数符号扩展  (
  input  [7:0] \immidiate_立即数 ,
  input  [3:0] \OP_操作码 ,
  output [15:0] \Extended_value_扩展结果 
);

  wire and_1_out, and_2_out, not_1_out, not_2_out, not_3_out, not_4_out, or_1_out;
  wire [15:0] bit_extender_1_out, bit_extender_2_out, multiplexer_1_out;

  not not_1 (not_1_out, \OP_操作码 [2]);
  not not_2 (not_2_out, \OP_操作码 [1]);
  not not_3 (not_3_out, \OP_操作码 [2]);
  not not_4 (not_4_out, \OP_操作码 [0]);
  assign bit_extender_1_out = {{8{1'b0}}, \immidiate_立即数 };  // Bit_Extender bit_extender_1
  assign bit_extender_2_out = {{8{1'b1}}, \immidiate_立即数 };  // Bit_Extender bit_extender_2
  and and_1 (and_1_out, \OP_操作码 [3], not_1_out, not_2_out);
  and and_2 (and_2_out, \OP_操作码 [3], not_3_out, not_4_out);
  Multiplexer #(.width(16), .enable("false")) multiplexer_1 (
    .in0(bit_extender_1_out), .in1(bit_extender_2_out), .out(multiplexer_1_out), .sel(\immidiate_立即数 [7]));
  or or_1 (or_1_out, and_1_out, and_2_out);
  Multiplexer #(.width(16), .enable("false")) multiplexer_2 (
    .in0(bit_extender_1_out), .in1(multiplexer_1_out), .out(\Extended_value_扩展结果 ), .sel(or_1_out));
endmodule

module \立即数选择  (
  input  OP3,
  input  OP2,
  input  OP1,
  input  OP0,
  output Choose
);

  wire and_1_out, and_2_out, not_1_out, not_2_out, not_3_out, not_4_out;

  not not_1 (not_1_out, OP2);
  not not_2 (not_2_out, OP1);
  not not_3 (not_3_out, OP2);
  not not_4 (not_4_out, OP0);
  and and_1 (and_1_out, OP3, not_1_out, not_2_out);
  and and_2 (and_2_out, OP3, not_3_out, not_4_out);
  or or_1 (Choose, and_1_out, and_2_out);
endmodule

// ALUSrc
module \ALUSrc_控制部件  (
  input  [3:0] \OP_操作码 ,
  output ALUSrc
);

  wire and_1_out, and_2_out, and_3_out, not_1_out, not_2_out, not_3_out, not_4_out, not_5_out;

  not not_1 (not_1_out, \OP_操作码 [3]);
  and and_1 (and_1_out, not_1_out, \OP_操作码 [2], \OP_操作码 [1]);
  not not_2 (not_2_out, \OP_操作码 [2]);
  and and_2 (and_2_out, \OP_操作码 [3], not_2_out, not_3_out);
  not not_3 (not_3_out, \OP_操作码 [1]);
  not not_4 (not_4_out, \OP_操作码 [2]);
  and and_3 (and_3_out, \OP_操作码 [3], not_4_out, not_5_out);
  not not_5 (not_5_out, \OP_操作码 [0]);
  or or_1 (ALUSrc, and_1_out, and_2_out, and_3_out);
endmodule

// lui
module \lui_控制部件  (
  input  [3:0] \OP_操作码 ,
  output lui
);

  wire not_1_out, not_2_out;

  not not_1 (not_1_out, \OP_操作码 [3]);
  not not_2 (not_2_out, \OP_操作码 [1]);
  and and_1 (lui, not_1_out, \OP_操作码 [2], not_2_out, \OP_操作码 [0]);
endmodule

// MemWrite
module \MemWrite_控制部件  (
  input  [3:0] \OP_操作码 ,
  output MemWrite
);

  wire not_1_out, not_2_out;

  not not_1 (not_1_out, \OP_操作码 [2]);
  not not_2 (not_2_out, \OP_操作码 [0]);
  and and_1 (MemWrite, \OP_操作码 [3], not_1_out, \OP_操作码 [1], not_2_out);
endmodule

// MemtoReg_ctrl
module \MemtoReg_控制部件  (
  input  [3:0] \OP_操作码 ,
  output MemtoReg
);

  wire not_1_out, not_2_out;

  not not_1 (not_1_out, \OP_操作码 [2]);
  not not_2 (not_2_out, \OP_操作码 [1]);
  and and_1 (MemtoReg, \OP_操作码 [3], not_1_out, not_2_out, \OP_操作码 [0]);
endmodule

// Branch
module \Branch_控制部件  (
  input  [3:0] \OP_操作码 ,
  input  \zero_零标志位 ,
  input  \正负性 ,
  output \branch_是否跳转的控制信号 
);

  wire and_1_out, and_2_out, and_3_out, and_4_out, beq_out, bnq_out, jump_out, not_1_out, not_2_out,
       not_3_out, not_4_out, not_5_out, not_6_out, not_7_out, not_8_out, not_9_out, not_10_out, not_11_out,
       not_12_out;

  not not_1 (not_1_out, \OP_操作码 [2]);
  not not_2 (not_2_out, \OP_操作码 [3]);
  not not_3 (not_3_out, \OP_操作码 [2]);
  not not_4 (not_4_out, \OP_操作码 [1]);
  not not_5 (not_5_out, \OP_操作码 [3]);
  not not_6 (not_6_out, \OP_操作码 [2]);
  not not_7 (not_7_out, \OP_操作码 [0]);
  not not_8 (not_8_out, \OP_操作码 [3]);
  not not_9 (not_9_out, \OP_操作码 [2]);
  and jump (jump_out, \OP_操作码 [3], not_1_out, \OP_操作码 [1], \OP_操作码 [0]);
  and beq (beq_out, not_2_out, not_3_out, not_4_out, \OP_操作码 [0]);
  not not_10 (not_10_out, \zero_零标志位 );
  and bnq (bnq_out, not_5_out, not_6_out, \OP_操作码 [1], not_7_out);
  not not_11 (not_11_out, \正负性 );
  and and_1 (and_1_out, not_8_out, not_9_out, \OP_操作码 [1], \OP_操作码 [0]);
  and and_2 (and_2_out, \zero_零标志位 , beq_out);
  and and_3 (and_3_out, not_10_out, bnq_out);
  not not_12 (not_12_out, \zero_零标志位 );
  and and_4 (and_4_out, not_12_out, not_11_out, and_1_out);
  or or_1 (\branch_是否跳转的控制信号 , jump_out, and_2_out, and_3_out, and_4_out);
endmodule

module \Branch_控制部件_可分析  (
  input  [3:0] \OP_操作码 ,
  output Branch
);

  wire and_1_out, and_2_out, and_3_out, not_1_out, not_2_out, not_3_out, not_4_out, not_5_out;

  not not_1 (not_1_out, \OP_操作码 [3]);
  and and_1 (and_1_out, not_1_out, not_2_out, \OP_操作码 [0]);
  not not_2 (not_2_out, \OP_操作码 [2]);
  not not_3 (not_3_out, \OP_操作码 [3]);
  not not_4 (not_4_out, \OP_操作码 [2]);
  and and_2 (and_2_out, not_3_out, not_4_out, \OP_操作码 [1]);
  not not_5 (not_5_out, \OP_操作码 [2]);
  and and_3 (and_3_out, not_5_out, \OP_操作码 [1], \OP_操作码 [0]);
  or or_1 (Branch, and_1_out, and_2_out, and_3_out);
endmodule

// ControlUnit
module \控制器  (
  input  [3:0] \OP_操作码 ,
  input  [2:0] Funct,
  output \slt_slt控制信号 ,
  output disp,
  output RegDst,
  output \lui_lui指令产生的单一控制信号 ,
  output MemWrite,
  output \halt_停机控制信号 ,
  output MemtoReg,
  output RegWrite,
  output ALUSrc,
  output [3:0] ALUop
);

  \slt_控制部件  \slt_控制部件_1  (.\OP_操作码 (\OP_操作码 ), .Funct(Funct), .\slt_slt控制信号 (\slt_slt控制信号 ));
  \RegDst_控制部件  \regdst_控制部件_1  (.\OP_操作码 (\OP_操作码 ), .RegDst(RegDst));
  \MemWrite_控制部件  \memwrite_控制部件_1  (.\OP_操作码 (\OP_操作码 ), .MemWrite(MemWrite));
  \MemtoReg_控制部件  \memtoreg_控制部件_1  (.\OP_操作码 (\OP_操作码 ), .MemtoReg(MemtoReg));
  \ALUSrc_控制部件  \alusrc_控制部件_1  (.\OP_操作码 (\OP_操作码 ), .ALUSrc(ALUSrc));
  \ALUop译码  \aluop译码_1  (.\Funct_指令的Funct字段_3位 (Funct), .\OP_指令的操作码字段_4位 (\OP_操作码 ), .\ALUop_ALU操作码_4位 (ALUop));
  \DISP_控制部件  \disp_控制部件_1  (.\OP_操作码 (\OP_操作码 ), .disp(disp));
  \lui_控制部件  \lui_控制部件_1  (.\OP_操作码 (\OP_操作码 ), .lui(\lui_lui指令产生的单一控制信号 ));
  \halt_控制部件  \halt_控制部件_1  (.\OP_操作码 (\OP_操作码 ), .MemtoReg(\halt_停机控制信号 ));
  \RegWrite_控制部件  \regwrite_控制部件_1  (.\OP_操作码 (\OP_操作码 ), .out_2(RegWrite));
endmodule

module DISP (
  input  [31:0] R1R0,
  input  [31:0] R3R2,
  input  [1:0] \r_num_rs__寄存器编号 ,
  input  \CLK_时钟信号 ,
  input  \disp_color_颜色选择信号 ,
  input  \DISP_disp控制信号_用于更新寄存器的值 ,
  input  \CLR_清零信号 ,
  output [15:0] DISP_0,
  output [15:0] DISP1
);

  wire and_1_out, and_2_out, not_1_out;
  wire [15:0] multiplexer_1_out, multiplexer_2_out;

  not not_1 (not_1_out, \disp_color_颜色选择信号 );
  Multiplexer #(.select(2), .width(16), .enable("false")) multiplexer_1 (
    .in0(R1R0[15:0]), .in1(R1R0[31:16]), .in2(R3R2[15:0]), .in3(R3R2[31:16]), .out(multiplexer_1_out),
    .sel(\r_num_rs__寄存器编号 ));
  Multiplexer #(.select(2), .width(16), .enable("false")) multiplexer_2 (
    .in0(R1R0[15:0]), .in1(R1R0[31:16]), .in2(R3R2[15:0]), .in3(R3R2[31:16]), .out(multiplexer_2_out),
    .sel(\r_num_rs__寄存器编号 ));
  and and_1 (and_1_out, not_1_out, \DISP_disp控制信号_用于更新寄存器的值 );
  and and_2 (and_2_out, \DISP_disp控制信号_用于更新寄存器的值 , \disp_color_颜色选择信号 );
  Register #(.width(16), .trigger("falling")) register_1 (
    .D(multiplexer_1_out), .en(and_1_out), .Q(DISP_0), .clk(\CLK_时钟信号 ), .clr(\CLR_清零信号 ));
  Register #(.width(16), .trigger("falling")) register_2 (
    .D(multiplexer_2_out), .en(and_2_out), .Q(DISP1), .clk(\CLK_时钟信号 ), .clr(\CLR_清零信号 ));
endmodule

module \DISP_测试  (
  input  [15:0] in_1,
  input  [15:0] in_2,
  input  [15:0] in_3,
  input  [15:0] in_4,
  input  [1:0] num,
  input  disp,
  input  color
);

  wire button_1_out;
  wire [15:0] disp_1_p9, disp_1_p10, disp_2_1_disp_0, disp_2_1_disp_1;

  Button button_1 (.out(button_1_out));
  DISP_2 disp_2_1 (
    .R3(in_1), .R2(in_2), .\r_num_寄存器编号 (num), .R1(in_3), .R0(in_4), .\DISP_disp控制信号_用于更新寄存器的值 (disp),
    .\disp_color_颜色选择信号 (color), .\CLK_时钟信号 (button_1_out), .DISP_0(disp_2_1_disp_0), .DISP_1(disp_2_1_disp_1));
  // DISP disp_1: pin names not known; wires that end beside it: in_1, in_2, in_3, in_4, num, disp, color, button_1_out, disp_1_p9, disp_1_p10
  Hex_Digit_Display hex_digit_display_1 (.value(disp_2_1_disp_0[11:8]));  // open: dp
  Hex_Digit_Display hex_digit_display_2 (.value(disp_2_1_disp_0[15:12]));  // open: dp
  Hex_Digit_Display hex_digit_display_3 (.value(disp_1_p9[11:8]));  // open: dp
  Hex_Digit_Display hex_digit_display_4 (.value(disp_1_p9[15:12]));  // open: dp
  Hex_Digit_Display hex_digit_display_5 (.value(disp_2_1_disp_0[7:4]));  // open: dp
  Hex_Digit_Display hex_digit_display_6 (.value(disp_2_1_disp_0[3:0]));  // open: dp
  Hex_Digit_Display hex_digit_display_7 (.value(disp_1_p9[7:4]));  // open: dp
  Hex_Digit_Display hex_digit_display_8 (.value(disp_1_p9[3:0]));  // open: dp
  Hex_Digit_Display hex_digit_display_9 (.value(disp_2_1_disp_1[15:12]));  // open: dp
  Hex_Digit_Display hex_digit_display_10 (.value(disp_2_1_disp_1[11:8]));  // open: dp
  Hex_Digit_Display hex_digit_display_11 (.value(disp_1_p10[15:12]));  // open: dp
  Hex_Digit_Display hex_digit_display_12 (.value(disp_2_1_disp_1[3:0]));  // open: dp
  Hex_Digit_Display hex_digit_display_13 (.value(disp_2_1_disp_1[7:4]));  // open: dp
  Hex_Digit_Display hex_digit_display_14 (.value(disp_1_p10[7:4]));  // open: dp
  Hex_Digit_Display hex_digit_display_15 (.value(disp_1_p10[11:8]));  // open: dp
  Hex_Digit_Display hex_digit_display_16 (.value(disp_1_p10[3:0]));  // open: dp
endmodule

// disp-ctrl
module \DISP_控制部件  (
  input  [3:0] \OP_操作码 ,
  output disp
);

  wire not_1_out, not_2_out, not_3_out;

  not not_1 (not_1_out, \OP_操作码 [3]);
  not not_2 (not_2_out, \OP_操作码 [1]);
  not not_3 (not_3_out, \OP_操作码 [0]);
  and and_1 (disp, not_1_out, \OP_操作码 [2], not_2_out, not_3_out);
endmodule

// flag
module \Flag_取一个数的最高位  (
  input  [15:0] \value_输入的值 ,
  output \flag_value的最高位 
);


  assign \flag_value的最高位  = \value_输入的值 [15];
endmodule

// halt
module \halt_控制部件  (
  input  [3:0] \OP_操作码 ,
  output MemtoReg
);

  wire not_1_out, not_2_out;

  not not_1 (not_1_out, \OP_操作码 [1]);
  not not_2 (not_2_out, \OP_操作码 [0]);
  and and_1 (MemtoReg, \OP_操作码 [3], \OP_操作码 [2], not_1_out, not_2_out);
endmodule

// slt-ctrl
module \slt_控制部件  (
  input  [3:0] \OP_操作码 ,
  input  [2:0] Funct,
  output \slt_slt控制信号 
);

  wire and_1_out, and_2_out, not_1_out, not_2_out, not_3_out, not_4_out;

  not not_1 (not_1_out, \OP_操作码 [3]);
  not not_2 (not_2_out, \OP_操作码 [2]);
  not not_3 (not_3_out, \OP_操作码 [1]);
  not not_4 (not_4_out, \OP_操作码 [0]);
  and and_1 (and_1_out, not_1_out, not_2_out, not_3_out, not_4_out);
  and and_2 (and_2_out, Funct[2], Funct[1], Funct[0]);
  and and_3 (\slt_slt控制信号 , and_1_out, and_2_out);
endmodule

// RF：2
module \RF_寄存器堆2  (
  input  [1:0] W,
  input  \RrgWrite_寄存器写控制信号 ,
  input  \CP_时钟输入 ,
  input  [15:0] Din,
  input  [1:0] rs,
  input  [1:0] rt,
  output [15:0] Do1,
  output [15:0] Do2,
  output [31:0] R1R0,
  output [31:0] R3R2
);

  wire and_1_out, and_2_out, and_3_out, and_4_out, decoder_1_out0, decoder_1_out1, decoder_1_out2,
       decoder_1_out3;

  Decoder #(.select(2)) decoder_1 (
    .out0(decoder_1_out0), .out1(decoder_1_out1), .out2(decoder_1_out2), .out3(decoder_1_out3), .sel(W),
    .en(1'b1));
  and and_1 (and_1_out, decoder_1_out0, \RrgWrite_寄存器写控制信号 );
  and and_2 (and_2_out, decoder_1_out1, \RrgWrite_寄存器写控制信号 );
  and and_3 (and_3_out, decoder_1_out2, \RrgWrite_寄存器写控制信号 );
  and and_4 (and_4_out, decoder_1_out3, \RrgWrite_寄存器写控制信号 );
  Register #(.width(16), .trigger("falling")) R0 (
    .D(Din), .en(and_1_out), .Q(R1R0[15:0]), .clk(\CP_时钟输入 ));  // open: clr
  Register #(.width(16), .trigger("falling")) R1 (
    .D(Din), .en(and_2_out), .Q(R1R0[31:16]), .clk(\CP_时钟输入 ));  // open: clr
  Register #(.width(16), .trigger("falling")) R2 (
    .D(Din), .en(and_3_out), .Q(R3R2[15:0]), .clk(\CP_时钟输入 ));  // open: clr
  Register #(.width(16), .trigger("falling")) R3 (
    .D(Din), .en(and_4_out), .Q(R3R2[31:16]), .clk(\CP_时钟输入 ));  // open: clr
  Multiplexer #(.select(2), .width(16), .enable("false")) multiplexer_1 (
    .in0(R1R0[15:0]), .in1(R1R0[31:16]), .in2(R3R2[15:0]), .in3(R3R2[31:16]), .out(Do1), .sel(rs));
  Multiplexer #(.select(2), .width(16), .enable("false")) multiplexer_2 (
    .in0(R1R0[15:0]), .in1(R1R0[31:16]), .in2(R3R2[15:0]), .in3(R3R2[31:16]), .out(Do2), .sel(rt));
endmodule

module DISP_2 (
  input  [15:0] R3,
  input  [15:0] R2,
  input  [15:0] R1,
  input  [15:0] R0,
  input  [1:0] \r_num_寄存器编号 ,
  input  \CLK_时钟信号 ,
  input  \DISP_disp控制信号_用于更新寄存器的值 ,
  input  \disp_color_颜色选择信号 ,
  output [15:0] DISP_0,
  output [15:0] DISP_1
);

  wire and_1_out, and_2_out, not_1_out, undriven, undriven_7, undriven_8;
  wire [1:0] undriven_2;
  wire [15:0] multiplexer_1_out, multiplexer_2_out, undriven_3, undriven_4, undriven_5, undriven_6;

  not not_1 (not_1_out, undriven);
  Multiplexer #(.select(2), .width(16), .enable("false")) multiplexer_1 (
    .in0(undriven_3), .in1(undriven_4), .in2(undriven_5), .in3(undriven_6), .out(multiplexer_1_out),
    .sel(undriven_2));
  Multiplexer #(.select(2), .width(16), .enable("false")) multiplexer_2 (
    .in0(undriven_3), .in1(undriven_4), .in2(undriven_5), .in3(undriven_6), .out(multiplexer_2_out),
    .sel(undriven_2));
  and and_1 (and_1_out, not_1_out, undriven_7);
  and and_2 (and_2_out, undriven_7, undriven);
  Register #(.width(16), .trigger("falling")) register_1 (
    .D(multiplexer_1_out), .en(and_1_out), .clk(undriven_8));  // open: Q, clr
  Register #(.width(16), .trigger("falling")) register_2 (
    .D(multiplexer_2_out), .en(and_2_out), .clk(undriven_8));  // open: Q, clr
endmodule

module \补码加减器  (
  input  [15:0] A,
  input  [15:0] B,
  output [15:0] out_3
);

  wire \flag_取一个数的最高位_1_flag_value的最高位 , \flag_取一个数的最高位_2_flag_value的最高位 ;
  wire [15:0] multiplexer_2_out, not_1_out, not_2_out, subtractor_1_out, subtractor_2_out;

  Subtractor #(.width(16)) subtractor_1 (.a(A), .b(16'h1), .out(subtractor_1_out));  // open: bin, bout
  \Flag_取一个数的最高位  \flag_取一个数的最高位_1  (.\value_输入的值 (A), .\flag_value的最高位 (\flag_取一个数的最高位_1_flag_value的最高位 ));
  Subtractor #(.width(16)) subtractor_2 (.a(B), .b(16'h1), .out(subtractor_2_out));  // open: bin, bout
  \Flag_取一个数的最高位  \flag_取一个数的最高位_2  (.\value_输入的值 (B), .\flag_value的最高位 (\flag_取一个数的最高位_2_flag_value的最高位 ));
  Multiplexer #(.width(16), .enable("false")) multiplexer_1 (
    .in0(A), .in1(not_1_out), .out(out_3), .sel(\flag_取一个数的最高位_1_flag_value的最高位 ));
  assign not_1_out = ~subtractor_1_out;  // NOT_Gate not_1, 16 bits wide
  Multiplexer #(.width(16), .enable("false")) multiplexer_2 (
    .in0(B), .in1(not_2_out), .out(multiplexer_2_out), .sel(\flag_取一个数的最高位_2_flag_value的最高位 ));
  assign not_2_out = ~subtractor_2_out;  // NOT_Gate not_2, 16 bits wide
endmodule

// 负补
module \补__负补  (
  input  [15:0] \补码 ,
  output [15:0] \负补码 
);

  Subtractor #(.width(16)) subtractor_1 (.a({16{1'b0}}), .b(\补码 ), .out(\负补码 ));  // open: bin, bout
endmodule

// slt:0?1
module slt_0_1 (
  input  \falg_符号位 ,
  input  \overflow_溢出信号 ,
  input  [3:0] \OP_操作码 ,
  input  [2:0] \Funct_函数字段 ,
  output slt_0_1
);

  wire and_1_out, and_2_out, and_3_out, multiplexer_1_out, not_1_out, not_2_out, not_3_out, not_4_out,
       not_5_out;

  not not_1 (not_1_out, \OP_操作码 [0]);
  not not_2 (not_2_out, \OP_操作码 [1]);
  not not_3 (not_3_out, \OP_操作码 [2]);
  not not_4 (not_4_out, \OP_操作码 [3]);
  Multiplexer #(.enable("false")) multiplexer_1 (
    .in0(\falg_符号位 ), .in1(not_5_out), .out(multiplexer_1_out), .sel(\overflow_溢出信号 ));
  not not_5 (not_5_out, \falg_符号位 );
  and and_1 (and_1_out, not_1_out, not_2_out, not_3_out, not_4_out);
  and and_2 (and_2_out, \Funct_函数字段 [0], \Funct_函数字段 [1], \Funct_函数字段 [2]);
  Multiplexer #(.enable("false")) multiplexer_2 (.in0(1'b0), .in1(multiplexer_1_out), .out(slt_0_1), .sel(and_3_out));
  and and_3 (and_3_out, and_1_out, and_2_out);
endmodule

module \补__原  (
  input  [15:0] \补 ,
  output [15:0] \原 
);

  wire [15:0] not_1_out, subtractor_1_out;

  Subtractor #(.width(16)) subtractor_1 (.a(\补 ), .b(16'h1), .out(subtractor_1_out));  // open: bin, bout
  assign not_1_out = ~subtractor_1_out;  // NOT_Gate not_1, 16 bits wide
  Multiplexer #(.width(16), .enable("false")) multiplexer_1 (
    .in0(\补 ), .in1({\补 [15], not_1_out[14:0]}), .out(\原 ), .sel(\补 [15]));
endmodule

module \原__补  (
  input  [15:0] \补 ,
  output [15:0] \原 
);

  wire [14:0] undriven;
  wire [15:0] not_1_out;

  assign not_1_out = ~\补 ;  // NOT_Gate not_1, 16 bits wide
  Adder #(.width(16)) adder_1 (.a(not_1_out), .b(16'h1));  // open: out, cin, cout
  Multiplexer #(.width(16), .enable("false")) multiplexer_1 (
    .in0(\补 ), .in1({\补 [15], undriven}), .out(\原 ), .sel(\补 [15]));
endmodule

// -over
module \减法溢出  (
  input  Flag_A,
  input  Flag_B,
  input  Flag_out,
  output \overflow_溢出 
);

  wire and_1_out, and_2_out, not_1_out, not_2_out, not_3_out;

  not not_1 (not_1_out, Flag_out);
  not not_2 (not_2_out, Flag_A);
  not not_3 (not_3_out, Flag_B);
  and and_1 (and_1_out, not_2_out, Flag_B, Flag_out);
  and and_2 (and_2_out, Flag_A, not_3_out, not_1_out);
  or or_1 (\overflow_溢出 , and_1_out, and_2_out);
endmodule

module circuit (
  input  \falg_符号位 ,
  input  \overflow_溢出信号 ,
  output out_3
);

  wire not_1_out;

  Multiplexer #(.enable("false")) multiplexer_1 (.in0(\falg_符号位 ), .in1(not_1_out), .out(out_3), .sel(\overflow_溢出信号 ));
  not not_1 (not_1_out, \falg_符号位 );
endmodule

// +over
module \加法溢出  (
  input  Flag_A,
  input  Flag_B,
  input  Flag_out,
  output \overflow_溢出 
);

  wire and_1_out, and_2_out, not_1_out, not_2_out, not_3_out;

  not not_1 (not_1_out, Flag_out);
  not not_2 (not_2_out, Flag_A);
  not not_3 (not_3_out, Flag_B);
  and and_1 (and_1_out, Flag_A, Flag_B, not_1_out);
  and and_2 (and_2_out, not_2_out, not_3_out, Flag_out);
  or or_1 (\overflow_溢出 , and_1_out, and_2_out);
endmodule

module \理想流水  (
  input  \为1时启动 
);

  wire \alu16位运算器_1_溢出 , \alu16位运算器_1_零 , and_1_out, \branch_控制部件_1_branch_是否跳转的控制信号 , CK, clock, clr, color,
       \EX_MEM_over_溢出标志位_2 , \EX_MEM_zero_0标志位_2 , \flag_取一个数的最高位_1_flag_value的最高位 ,
       \flag_取一个数的最高位_2_flag_value的最高位 , MEM_WB_alusrc_2, MEM_WB_disp_2, MEM_WB_halt_2, MEM_WB_lui_2,
       MEM_WB_memtoreg_2, MEM_WB_memwrite_2, \MEM_WB_over_溢出标志位_2 , MEM_WB_regdst_2, MEM_WB_regwrite_2,
       MEM_WB_slt_2, \MEM_WB_zero_0标志位_2 , not_1_out, part_1_out_3, \启停控制电路_1_f_输出时钟 ;
  wire [1:0] \idecoder_指令译码器_1_rd , \idecoder_指令译码器_1_rs , \idecoder_指令译码器_1_rt , \idecoder_指令译码器_3_rd ,
       \idecoder_指令译码器_3_rt , multiplexer_2_out, num;
  wire [2:0] \idecoder_指令译码器_1_funct , \idecoder_指令译码器_1_p , \idecoder_指令译码器_2_funct ;
  wire [3:0] EX_MEM_aluop_2, ID_EX_aluop_2, \ID_EX_op_操作码_2 , \idecoder_指令译码器_1_op , \idecoder_指令译码器_2_op ,
       \idecoder_指令译码器_3_op , MEM_WB_aluop_2, \控制器_1_aluop ;
  wire [7:0] ID_EX_offset_2, \idecoder_指令译码器_1_immediate ;
  wire [8:0] EX_MEM_alusrc_2, ID_EX_alusrc_2, \控制器_1_alusrc ;
  wire [11:0] counter_1_q, ID_EX_jump_2, \idecoder_指令译码器_1_jump_address ;
  wire [15:0] adder_1_out, \alu16位运算器_1_输出f , DISP_0, DISP_1, EX_MEM_aluout_2, EX_MEM_instruction_2,
       \EX_MEM_jump_address_跳转地址_2 , EX_MEM_pc_2, EX_MEM_rt_2, \extend_立即数符号扩展_1_extended_value_扩展结果 ,
       \ID_EX_immediate_扩展后的立即数_2 , ID_EX_instruction_2, ID_EX_pc_1_2, ID_EX_pc_2, ID_EX_rs_2, ID_EX_rt_2,
       \if_id_1_instruction_指令输出 , \if_id_1_instruction_指令输出_2 , \if_id_1_pc_1_输出 , if_id_1_pc_2,
       MEM_WB_aluout_2, MEM_WB_instruction_2, \MEM_WB_jump_address_跳转地址_2 , MEM_WB_memout_2,
       multiplexer_1_out, multiplexer_3_out, multiplexer_4_out, multiplexer_5_out, multiplexer_6_out,
       multiplexer_7_out, PC_q, ram_1_data, \rf_寄存器堆_1_do1 , \rf_寄存器堆_1_do2 , rom_1_data, slt_0_1_1_slt_0_1,
       \跳转地址形成部件_1_jump_address ;
  wire [31:0] EX_MEM_r1r0_2, EX_MEM_r3r2_2, ID_EX_r1r0_2, ID_EX_r3r2_2, R1R0, R3R2, \rf_寄存器堆_1_r1r0 ,
       \rf_寄存器堆_1_r3r2 ;

  // Probe on R3R2
  Multiplexer #(.width(16), .enable("false")) multiplexer_1 (
    .in0(adder_1_out), .in1(\MEM_WB_jump_address_跳转地址_2 ), .out(multiplexer_1_out),
    .sel(\branch_控制部件_1_branch_是否跳转的控制信号 ));
  Counter #(.width(12), .max('hfff), .trigger("falling")) counter_1 (
    .count(1'b1), .Q(counter_1_q), .clk(clock), .clr(clr));  // open: load, D, carry
  // Probe on R1R0
  Register #(.width(16)) PC (.D(multiplexer_1_out), .Q(PC_q), .clk(clock), .clr(clr));  // open: en
  // Probe on counter_1_q
  DISP u_disp_1 (
    .R3R2(R3R2), .R1R0(R1R0), .\r_num_rs__寄存器编号 (num), .\DISP_disp控制信号_用于更新寄存器的值 (MEM_WB_disp_2),
    .\disp_color_颜色选择信号 (color), .\CLK_时钟信号 (clock), .DISP_0(DISP_0), .DISP1(DISP_1), .\CLR_清零信号 (clr));
  Adder #(.width(16)) adder_1 (.a(16'h1), .b(PC_q), .out(adder_1_out), .cin(1'b0));  // open: cout
  Clock \u_时钟  (.out(CK));
  not not_1 (not_1_out, MEM_WB_halt_2);
  ROM #(.addrWidth(16), .dataWidth(16)) rom_1 (.addr(PC_q), .data(rom_1_data));  // open: sel
  \启停控制电路  \u_启停控制电路_1  (.\F_输出时钟 (\启停控制电路_1_f_输出时钟 ), .\时钟 (CK), .\启动_为1时启动 (and_1_out), .\重置信号 (clr));
  and and_1 (and_1_out, \为1时启动 , not_1_out);
  Button \u_重置信号  (.out(clr));
  not not_2 (clock, \启停控制电路_1_f_输出时钟 );
  IF_ID if_id_1 (
    .PC_1(adder_1_out), .\instruction_指令 (rom_1_data), .\clock_时钟信号 (clock), .\clear_清零信号 (clr),
    .\PC_1_输出 (\if_id_1_pc_1_输出 ), .\instruction_指令输出_2 (\if_id_1_instruction_指令输出_2 ), .\en_使能信号 (1'b1),
    .PC(PC_q), .PC_2(if_id_1_pc_2), .\instruction_指令输出 (\if_id_1_instruction_指令输出 ));  // open: 同步清零
  Bit_Extender #(.out_width(1)) bit_extender_1 (.in(\idecoder_指令译码器_1_immediate ), .out(color));
  \控制器  \u_控制器_1  (
    .\OP_操作码 (\idecoder_指令译码器_1_op ), .Funct(\idecoder_指令译码器_1_funct ), .RegDst(\控制器_1_alusrc [8]),
    .\lui_lui指令产生的单一控制信号 (\控制器_1_alusrc [6]), .MemWrite(\控制器_1_alusrc [4]), .MemtoReg(\控制器_1_alusrc [2]),
    .RegWrite(\控制器_1_alusrc [1]), .ALUSrc(\控制器_1_alusrc [0]), .ALUop(\控制器_1_aluop ),
    .disp(\控制器_1_alusrc [7]), .\halt_停机控制信号 (\控制器_1_alusrc [3]), .\slt_slt控制信号 (\控制器_1_alusrc [5]));
  \IDecoder_指令译码器  \idecoder_指令译码器_1  (
    .\Instruction_指令 (\if_id_1_instruction_指令输出_2 ), .Funct(\idecoder_指令译码器_1_funct ),
    .P(\idecoder_指令译码器_1_p ), .rd(\idecoder_指令译码器_1_rd ), .rt(\idecoder_指令译码器_1_rt ),
    .rs(\idecoder_指令译码器_1_rs ), .OP(\idecoder_指令译码器_1_op ), .immediate(\idecoder_指令译码器_1_immediate ),
    .jump_address(\idecoder_指令译码器_1_jump_address ));
  Hex_Digit_Display hex_digit_display_1 (.value(DISP_0[15:12]));  // open: dp
  Multiplexer #(.width(2), .enable("false")) multiplexer_2 (
    .in0(\idecoder_指令译码器_3_rt ), .in1(\idecoder_指令译码器_3_rd ), .out(multiplexer_2_out), .sel(MEM_WB_regdst_2));
  Hex_Digit_Display hex_digit_display_2 (.value(DISP_0[7:4]));  // open: dp
  Hex_Digit_Display hex_digit_display_3 (.value(DISP_0[11:8]));  // open: dp
  // Probe on \if_id_1_instruction_指令输出 
  \RF_寄存器堆  \rf_寄存器堆_1  (
    .Din(multiplexer_7_out), .\CP_时钟输入 (clock), .Do1(\rf_寄存器堆_1_do1 ), .rs(\idecoder_指令译码器_1_rs ),
    .Do2(\rf_寄存器堆_1_do2 ), .rt(\idecoder_指令译码器_1_rt ), .R1R0(\rf_寄存器堆_1_r1r0 ), .R3R2(\rf_寄存器堆_1_r3r2 ),
    .W(multiplexer_2_out), .\RegWrite_寄存器写控制信号 (MEM_WB_regwrite_2), .\ClR_清零信号 (clr));
  // Probe on multiplexer_7_out
  Hex_Digit_Display hex_digit_display_4 (.value(DISP_0[3:0]));  // open: dp
  \Extend_立即数符号扩展  \extend_立即数符号扩展_1  (
    .\immidiate_立即数 (\idecoder_指令译码器_1_immediate ), .\OP_操作码 (\idecoder_指令译码器_1_op ),
    .\Extended_value_扩展结果 (\extend_立即数符号扩展_1_extended_value_扩展结果 ));
  Hex_Digit_Display hex_digit_display_5 (.value(DISP_1[15:12]));  // open: dp
  Hex_Digit_Display hex_digit_display_6 (.value(DISP_1[11:8]));  // open: dp
  ID_EX ID_EX (
    .PC(if_id_1_pc_2), .PC_2(ID_EX_pc_2), .instruction(\if_id_1_instruction_指令输出 ),
    .instruction_2(ID_EX_instruction_2), .ALUop(\控制器_1_aluop ), .ALUop_2(ID_EX_aluop_2),
    .ALUSrc(\控制器_1_alusrc [0]), .ALUSrc_2(ID_EX_alusrc_2[0]), .RegWrite(\控制器_1_alusrc [1]),
    .RegWrite_2(ID_EX_alusrc_2[1]), .MemtoReg(\控制器_1_alusrc [2]), .MemtoReg_2(ID_EX_alusrc_2[2]),
    .halt(\控制器_1_alusrc [3]), .halt_2(ID_EX_alusrc_2[3]), .MemWrite(\控制器_1_alusrc [4]),
    .MemWrite_2(ID_EX_alusrc_2[4]), .slt(\控制器_1_alusrc [5]), .slt_2(ID_EX_alusrc_2[5]),
    .lui(\控制器_1_alusrc [6]), .lui_2(ID_EX_alusrc_2[6]), .disp(\控制器_1_alusrc [7]), .disp_2(ID_EX_alusrc_2[7]),
    .RegDst(\控制器_1_alusrc [8]), .RegDst_2(ID_EX_alusrc_2[8]), .offset(\idecoder_指令译码器_1_immediate ),
    .offset_2(ID_EX_offset_2), .jump(\idecoder_指令译码器_1_jump_address ), .jump_2(ID_EX_jump_2),
    .\OP_操作码 (\idecoder_指令译码器_1_op ), .\OP_操作码_2 (\ID_EX_op_操作码_2 ), .PC_1(\if_id_1_pc_1_输出 ),
    .PC_1_2(ID_EX_pc_1_2), .rs(\rf_寄存器堆_1_do1 ), .rs_2(ID_EX_rs_2), .rt(\rf_寄存器堆_1_do2 ), .rt_2(ID_EX_rt_2),
    .\immediate_扩展后的立即数 (\extend_立即数符号扩展_1_extended_value_扩展结果 ),
    .\immediate_扩展后的立即数_2 (\ID_EX_immediate_扩展后的立即数_2 ), .\en_寄存器使能信号 (1'b1), .\clock_时钟信号 (clock),
    .\clear_清零信号 (clr), .R3R2_2(ID_EX_r3r2_2), .R1R0(\rf_寄存器堆_1_r1r0 ), .R1R0_2(ID_EX_r1r0_2),
    .R3R2(\rf_寄存器堆_1_r3r2 ));  // open: 同步清空
  Hex_Digit_Display hex_digit_display_7 (.value(DISP_1[3:0]));  // open: dp
  Hex_Digit_Display hex_digit_display_8 (.value(DISP_1[7:4]));  // open: dp
  // Probe on multiplexer_3_out
  Multiplexer #(.width(16), .enable("false")) multiplexer_3 (
    .in0(ID_EX_rt_2), .in1(\ID_EX_immediate_扩展后的立即数_2 ), .out(multiplexer_3_out), .sel(ID_EX_alusrc_2[0]));
  // Probe on multiplexer_5_out
  Multiplexer #(.width(16), .enable("false")) multiplexer_4 (
    .in0(ID_EX_rs_2), .in1(\ID_EX_immediate_扩展后的立即数_2 ), .out(multiplexer_4_out), .sel(ID_EX_alusrc_2[6]));
  Multiplexer #(.width(16), .enable("false")) multiplexer_5 (
    .in0(multiplexer_3_out), .in1(16'h8), .out(multiplexer_5_out), .sel(ID_EX_alusrc_2[6]));
  \IDecoder_指令译码器  \idecoder_指令译码器_2  (
    .\Instruction_指令 (ID_EX_instruction_2), .Funct(\idecoder_指令译码器_2_funct ), .OP(\idecoder_指令译码器_2_op ));  // open: P, rd, rt, rs, immediate, jump_address
  \跳转地址形成部件  \u_跳转地址形成部件_1  (
    .\Offset_条件跳转地址_8位 (ID_EX_offset_2), .\PC_1_顺序下地址 (ID_EX_pc_1_2),
    .\jump_address_无条件跳转地址_12位 (ID_EX_jump_2), .\OP_操作码_4位 (\ID_EX_op_操作码_2 ),
    .jump_address(\跳转地址形成部件_1_jump_address ));
  \Flag_取一个数的最高位  \flag_取一个数的最高位_1  (
    .\value_输入的值 (\alu16位运算器_1_输出f ), .\flag_value的最高位 (\flag_取一个数的最高位_1_flag_value的最高位 ));
  \ALU16位运算器  \alu16位运算器_1  (
    .\输入A (multiplexer_4_out), .\输入B (multiplexer_5_out), .\控制信息C (ID_EX_aluop_2), .\零 (\alu16位运算器_1_零 ),
    .\溢出 (\alu16位运算器_1_溢出 ), .\输出F (\alu16位运算器_1_输出f ));  // open: 进位
  // Probe on ID_EX_instruction_2
  slt_0_1_2 slt_0_1_1 (
    .\falg_符号位 (\flag_取一个数的最高位_1_flag_value的最高位 ), .\overflow_溢出信号 (\alu16位运算器_1_溢出 ),
    .\OP_操作码 (\idecoder_指令译码器_2_op ), .\Funct_函数字段 (\idecoder_指令译码器_2_funct ), .slt_0_1(slt_0_1_1_slt_0_1));
  Multiplexer #(.width(16), .enable("false")) multiplexer_6 (
    .in0(\alu16位运算器_1_输出f ), .in1(slt_0_1_1_slt_0_1), .out(multiplexer_6_out), .sel(ID_EX_alusrc_2[5]));
  // Probe on multiplexer_6_out
  EX_MEM EX_MEM (
    .PC(ID_EX_pc_2), .PC_2(EX_MEM_pc_2), .instruction(ID_EX_instruction_2),
    .instruction_2(EX_MEM_instruction_2), .ALUop(ID_EX_aluop_2), .ALUop_2(EX_MEM_aluop_2),
    .ALUSrc(ID_EX_alusrc_2[0]), .ALUSrc_2(EX_MEM_alusrc_2[0]), .RegWrite(ID_EX_alusrc_2[1]),
    .RegWrite_2(EX_MEM_alusrc_2[1]), .MemtoReg(ID_EX_alusrc_2[2]), .MemtoReg_2(EX_MEM_alusrc_2[2]),
    .halt(ID_EX_alusrc_2[3]), .halt_2(EX_MEM_alusrc_2[3]), .MemWrite(ID_EX_alusrc_2[4]),
    .MemWrite_2(EX_MEM_alusrc_2[4]), .slt(ID_EX_alusrc_2[5]), .slt_2(EX_MEM_alusrc_2[5]),
    .lui(ID_EX_alusrc_2[6]), .lui_2(EX_MEM_alusrc_2[6]), .disp(ID_EX_alusrc_2[7]),
    .disp_2(EX_MEM_alusrc_2[7]), .RegDst(ID_EX_alusrc_2[8]), .RegDst_2(EX_MEM_alusrc_2[8]),
    .\jump_address_跳转地址 (\跳转地址形成部件_1_jump_address ), .\jump_address_跳转地址_2 (\EX_MEM_jump_address_跳转地址_2 ),
    .\zero_0标志位 (\alu16位运算器_1_零 ), .\zero_0标志位_2 (\EX_MEM_zero_0标志位_2 ), .\over_溢出标志位 (\alu16位运算器_1_溢出 ),
    .\over_溢出标志位_2 (\EX_MEM_over_溢出标志位_2 ), .ALUout(multiplexer_6_out), .ALUout_2(EX_MEM_aluout_2),
    .rt(ID_EX_rt_2), .rt_2(EX_MEM_rt_2), .\en_寄存器使能信号 (1'b1), .\clock_时钟信号 (clock), .\clear_清零信号 (clr),
    .R3R2(ID_EX_r3r2_2), .R3R2_2(EX_MEM_r3r2_2), .R1R0(ID_EX_r1r0_2), .R1R0_2(EX_MEM_r1r0_2));  // open: 同步清零
  // Probe on EX_MEM_instruction_2
  RAM #(.addrWidth(16), .dataWidth(16), .bus("separate")) ram_1 (
    .addr(EX_MEM_aluout_2), .din(EX_MEM_rt_2), .data(ram_1_data), .str(EX_MEM_alusrc_2[4]), .clk(clock),
    .ld(1'b1), .clr(clr));  // open: sel
  MEM_WB MEM_WB (
    .PC(EX_MEM_pc_2), .instruction(EX_MEM_instruction_2), .instruction_2(MEM_WB_instruction_2),
    .ALUop(EX_MEM_aluop_2), .ALUop_2(MEM_WB_aluop_2), .ALUSrc(EX_MEM_alusrc_2[0]),
    .ALUSrc_2(MEM_WB_alusrc_2), .RegWrite(EX_MEM_alusrc_2[1]), .RegWrite_2(MEM_WB_regwrite_2),
    .MemtoReg(EX_MEM_alusrc_2[2]), .MemtoReg_2(MEM_WB_memtoreg_2), .halt(EX_MEM_alusrc_2[3]),
    .halt_2(MEM_WB_halt_2), .MemWrite(EX_MEM_alusrc_2[4]), .MemWrite_2(MEM_WB_memwrite_2),
    .slt(EX_MEM_alusrc_2[5]), .slt_2(MEM_WB_slt_2), .lui(EX_MEM_alusrc_2[6]), .lui_2(MEM_WB_lui_2),
    .disp(EX_MEM_alusrc_2[7]), .disp_2(MEM_WB_disp_2), .RegDst(EX_MEM_alusrc_2[8]),
    .RegDst_2(MEM_WB_regdst_2), .\zero_0标志位 (\EX_MEM_zero_0标志位_2 ), .\zero_0标志位_2 (\MEM_WB_zero_0标志位_2 ),
    .\over_溢出标志位 (\EX_MEM_over_溢出标志位_2 ), .\over_溢出标志位_2 (\MEM_WB_over_溢出标志位_2 ), .ALUout(EX_MEM_aluout_2),
    .ALUout_2(MEM_WB_aluout_2), .MemOut(ram_1_data), .MemOut_2(MEM_WB_memout_2), .\en_寄存器使能信号 (1'b1),
    .\clock_时钟信号 (clock), .\clear_清零信号 (clr), .\jump_address_跳转地址 (\EX_MEM_jump_address_跳转地址_2 ),
    .\jump_address_跳转地址_2 (\MEM_WB_jump_address_跳转地址_2 ), .R3R2(EX_MEM_r3r2_2), .R3R2_2(R3R2),
    .R1R0(EX_MEM_r1r0_2), .R1R0_2(R1R0));  // open: PC_2
  \Branch_控制部件  \branch_控制部件_1  (
    .\OP_操作码 (\idecoder_指令译码器_3_op ), .\zero_零标志位 (\MEM_WB_zero_0标志位_2 ), .\正负性 (part_1_out_3),
    .\branch_是否跳转的控制信号 (\branch_控制部件_1_branch_是否跳转的控制信号 ));
  // Probe on MEM_WB_halt_2
  Multiplexer #(.width(16), .enable("false")) multiplexer_7 (
    .in0(MEM_WB_aluout_2), .in1(MEM_WB_memout_2), .out(multiplexer_7_out), .sel(MEM_WB_memtoreg_2));
  // Probe on multiplexer_7_out
  circuit part_1 (
    .\falg_符号位 (\flag_取一个数的最高位_2_flag_value的最高位 ), .\overflow_溢出信号 (\MEM_WB_over_溢出标志位_2 ),
    .out_3(part_1_out_3));
  \Flag_取一个数的最高位  \flag_取一个数的最高位_2  (
    .\value_输入的值 (MEM_WB_aluout_2), .\flag_value的最高位 (\flag_取一个数的最高位_2_flag_value的最高位 ));
  // Probe on MEM_WB_aluout_2
  // Probe on MEM_WB_instruction_2
  \IDecoder_指令译码器  \idecoder_指令译码器_3  (
    .\Instruction_指令 (MEM_WB_instruction_2), .rd(\idecoder_指令译码器_3_rd ), .rt(\idecoder_指令译码器_3_rt ),
    .rs(num), .OP(\idecoder_指令译码器_3_op ));  // open: Funct, P, immediate, jump_address

  // Other names for the same wires on the sheet: start = \为1时启动 

  // Notes on the sheet:
  //   contents of rom_1 (hex, n*v repeats v):
  //   5000 5100 5200 5300 6001 6502 6a03 6f04 4000 4400 4800 4c00 a000 a500 aa00 af00 c000
endmodule

module IF_ID (
  input  [15:0] PC,
  input  [15:0] PC_1,
  input  [15:0] \instruction_指令 ,
  input  \en_使能信号 ,
  input  \clock_时钟信号 ,
  input  \clear_清零信号 ,
  input  \同步清零 ,
  output [15:0] \instruction_指令输出 ,
  output [15:0] PC_2,
  output [15:0] \PC_1_输出 ,
  output [15:0] \instruction_指令输出_2 
);

  wire [15:0] multiplexer_1_out, multiplexer_2_out, multiplexer_3_out;

  // Probe on \instruction_指令 
  Multiplexer #(.width(16), .enable("false")) multiplexer_1 (
    .in0(PC), .in1({16{1'b0}}), .out(multiplexer_1_out), .sel(\同步清零 ));
  Multiplexer #(.width(16), .enable("false")) multiplexer_2 (
    .in0(PC_1), .in1({16{1'b0}}), .out(multiplexer_2_out), .sel(\同步清零 ));
  Multiplexer #(.width(16), .enable("false")) multiplexer_3 (
    .in0(\instruction_指令 ), .in1({16{1'b0}}), .out(multiplexer_3_out), .sel(\同步清零 ));
  Register #(.width(16)) u_PC (.D(multiplexer_1_out), .en(\en_使能信号 ), .Q(PC_2), .clk(\clock_时钟信号 ), .clr(\clear_清零信号 ));
  Register #(.width(16)) u_PC_1 (
    .D(multiplexer_2_out), .en(\en_使能信号 ), .Q(\PC_1_输出 ), .clk(\clock_时钟信号 ), .clr(\clear_清零信号 ));
  Register #(.width(16)) IR (
    .D(multiplexer_3_out), .en(\en_使能信号 ), .Q(\instruction_指令输出 ), .clk(\clock_时钟信号 ), .clr(\clear_清零信号 ));
  // Probe on \instruction_指令输出 

  assign \instruction_指令输出_2  = \instruction_指令输出 ;
endmodule

module ID_EX (
  input  [15:0] PC,
  input  [15:0] instruction,
  input  [3:0] ALUop,
  input  ALUSrc,
  input  RegWrite,
  input  MemtoReg,
  input  halt,
  input  MemWrite,
  input  slt,
  input  lui,
  input  disp,
  input  RegDst,
  input  [7:0] offset,
  input  [11:0] jump,
  input  [3:0] \OP_操作码 ,
  input  [15:0] PC_1,
  input  [15:0] rs,
  input  [15:0] rt,
  input  [15:0] \immediate_扩展后的立即数 ,
  input  [31:0] R3R2,
  input  [31:0] R1R0,
  input  \en_寄存器使能信号 ,
  input  \clock_时钟信号 ,
  input  \clear_清零信号 ,
  input  \同步清空 ,
  output [15:0] PC_2,
  output [15:0] instruction_2,
  output [3:0] ALUop_2,
  output ALUSrc_2,
  output RegWrite_2,
  output MemtoReg_2,
  output halt_2,
  output MemWrite_2,
  output slt_2,
  output lui_2,
  output disp_2,
  output RegDst_2,
  output [7:0] offset_2,
  output [11:0] jump_2,
  output [3:0] \OP_操作码_2 ,
  output [15:0] PC_1_2,
  output [15:0] rs_2,
  output [15:0] rt_2,
  output [15:0] \immediate_扩展后的立即数_2 ,
  output [31:0] R3R2_2,
  output [31:0] R1R0_2
);

  wire multiplexer_4_out, multiplexer_5_out, multiplexer_6_out, multiplexer_7_out, multiplexer_8_out,
       multiplexer_9_out, multiplexer_10_out, multiplexer_11_out, multiplexer_12_out;
  wire [3:0] multiplexer_3_out, multiplexer_15_out;
  wire [7:0] multiplexer_13_out;
  wire [11:0] multiplexer_14_out;
  wire [15:0] multiplexer_1_out, multiplexer_2_out, multiplexer_16_out, multiplexer_17_out,
       multiplexer_18_out, multiplexer_19_out;
  wire [31:0] multiplexer_20_out, multiplexer_21_out;

  Multiplexer #(.width(16), .enable("false")) multiplexer_1 (
    .in0(PC), .in1({16{1'b0}}), .out(multiplexer_1_out), .sel(\同步清空 ));
  Multiplexer #(.width(16), .enable("false")) multiplexer_2 (
    .in0(instruction), .in1({16{1'b0}}), .out(multiplexer_2_out), .sel(\同步清空 ));
  Multiplexer #(.width(4), .enable("false")) multiplexer_3 (
    .in0(ALUop), .in1(4'b0000), .out(multiplexer_3_out), .sel(\同步清空 ));
  Multiplexer #(.enable("false")) multiplexer_4 (.in0(ALUSrc), .in1(1'b0), .out(multiplexer_4_out), .sel(\同步清空 ));
  Multiplexer #(.enable("false")) multiplexer_5 (.in0(RegWrite), .in1(1'b0), .out(multiplexer_5_out), .sel(\同步清空 ));
  Multiplexer #(.enable("false")) multiplexer_6 (.in0(MemtoReg), .in1(1'b0), .out(multiplexer_6_out), .sel(\同步清空 ));
  Multiplexer #(.enable("false")) multiplexer_7 (.in0(halt), .in1(1'b0), .out(multiplexer_7_out), .sel(\同步清空 ));
  Multiplexer #(.enable("false")) multiplexer_8 (.in0(MemWrite), .in1(1'b0), .out(multiplexer_8_out), .sel(\同步清空 ));
  Multiplexer #(.enable("false")) multiplexer_9 (.in0(slt), .in1(1'b0), .out(multiplexer_9_out), .sel(\同步清空 ));
  Multiplexer #(.enable("false")) multiplexer_10 (.in0(lui), .in1(1'b0), .out(multiplexer_10_out), .sel(\同步清空 ));
  Multiplexer #(.enable("false")) multiplexer_11 (.in0(disp), .in1(1'b0), .out(multiplexer_11_out), .sel(\同步清空 ));
  Multiplexer #(.enable("false")) multiplexer_12 (.in0(RegDst), .in1(1'b0), .out(multiplexer_12_out), .sel(\同步清空 ));
  Multiplexer #(.width(8), .enable("false")) multiplexer_13 (
    .in0(offset), .in1({8{1'b0}}), .out(multiplexer_13_out), .sel(\同步清空 ));
  Multiplexer #(.width(12), .enable("false")) multiplexer_14 (
    .in0(jump), .in1({12{1'b0}}), .out(multiplexer_14_out), .sel(\同步清空 ));
  Multiplexer #(.width(4), .enable("false")) multiplexer_15 (
    .in0(\OP_操作码 ), .in1(4'b0000), .out(multiplexer_15_out), .sel(\同步清空 ));
  Multiplexer #(.width(16), .enable("false")) multiplexer_16 (
    .in0(PC_1), .in1({16{1'b0}}), .out(multiplexer_16_out), .sel(\同步清空 ));
  Multiplexer #(.width(16), .enable("false")) multiplexer_17 (
    .in0(rs), .in1({16{1'b0}}), .out(multiplexer_17_out), .sel(\同步清空 ));
  Multiplexer #(.width(16), .enable("false")) multiplexer_18 (
    .in0(rt), .in1({16{1'b0}}), .out(multiplexer_18_out), .sel(\同步清空 ));
  Multiplexer #(.width(16), .enable("false")) multiplexer_19 (
    .in0(\immediate_扩展后的立即数 ), .in1({16{1'b0}}), .out(multiplexer_19_out), .sel(\同步清空 ));
  Multiplexer #(.width(32), .enable("false")) multiplexer_20 (
    .in0(R3R2), .in1({32{1'b0}}), .out(multiplexer_20_out), .sel(\同步清空 ));
  Multiplexer #(.width(32), .enable("false")) multiplexer_21 (
    .in0(R1R0), .in1({32{1'b0}}), .out(multiplexer_21_out), .sel(\同步清空 ));
  Register #(.width(16), .trigger("falling")) u_PC (
    .D(multiplexer_1_out), .en(\en_寄存器使能信号 ), .Q(PC_2), .clk(\clock_时钟信号 ), .clr(\clear_清零信号 ));
  Register #(.width(16)) u_instruction (
    .D(multiplexer_2_out), .en(\en_寄存器使能信号 ), .Q(instruction_2), .clk(\clock_时钟信号 ), .clr(\clear_清零信号 ));
  Register #(.width(4)) u_ALUop (
    .D(multiplexer_3_out), .en(\en_寄存器使能信号 ), .Q(ALUop_2), .clk(\clock_时钟信号 ), .clr(\clear_清零信号 ));
  Register #(.width(1)) u_ALUSrc (
    .D(multiplexer_4_out), .en(\en_寄存器使能信号 ), .Q(ALUSrc_2), .clk(\clock_时钟信号 ), .clr(\clear_清零信号 ));
  Register #(.width(1)) u_RegWrite (
    .D(multiplexer_5_out), .en(\en_寄存器使能信号 ), .Q(RegWrite_2), .clk(\clock_时钟信号 ), .clr(\clear_清零信号 ));
  Register #(.width(1)) u_MemtoReg (
    .D(multiplexer_6_out), .en(\en_寄存器使能信号 ), .Q(MemtoReg_2), .clk(\clock_时钟信号 ), .clr(\clear_清零信号 ));
  Register #(.width(1)) u_halt (
    .D(multiplexer_7_out), .en(\en_寄存器使能信号 ), .Q(halt_2), .clk(\clock_时钟信号 ), .clr(\clear_清零信号 ));
  Register #(.width(1)) u_MemWrite (
    .D(multiplexer_8_out), .en(\en_寄存器使能信号 ), .Q(MemWrite_2), .clk(\clock_时钟信号 ), .clr(\clear_清零信号 ));
  Register #(.width(1)) u_slt (
    .D(multiplexer_9_out), .en(\en_寄存器使能信号 ), .Q(slt_2), .clk(\clock_时钟信号 ), .clr(\clear_清零信号 ));
  Register #(.width(1)) u_lui (
    .D(multiplexer_10_out), .en(\en_寄存器使能信号 ), .Q(lui_2), .clk(\clock_时钟信号 ), .clr(\clear_清零信号 ));
  Register #(.width(1)) u_disp (
    .D(multiplexer_11_out), .en(\en_寄存器使能信号 ), .Q(disp_2), .clk(\clock_时钟信号 ), .clr(\clear_清零信号 ));
  Register #(.width(1)) u_RegDst (
    .D(multiplexer_12_out), .en(\en_寄存器使能信号 ), .Q(RegDst_2), .clk(\clock_时钟信号 ), .clr(\clear_清零信号 ));
  Register u_offset (.D(multiplexer_13_out), .en(\en_寄存器使能信号 ), .Q(offset_2), .clk(\clock_时钟信号 ), .clr(\clear_清零信号 ));
  Register #(.width(12)) u_jump (
    .D(multiplexer_14_out), .en(\en_寄存器使能信号 ), .Q(jump_2), .clk(\clock_时钟信号 ), .clr(\clear_清零信号 ));
  Register #(.width(4)) OP (
    .D(multiplexer_15_out), .en(\en_寄存器使能信号 ), .Q(\OP_操作码_2 ), .clk(\clock_时钟信号 ), .clr(\clear_清零信号 ));
  Register #(.width(16)) u_PC_1 (
    .D(multiplexer_16_out), .en(\en_寄存器使能信号 ), .Q(PC_1_2), .clk(\clock_时钟信号 ), .clr(\clear_清零信号 ));
  Register #(.width(16)) D01 (
    .D(multiplexer_17_out), .en(\en_寄存器使能信号 ), .Q(rs_2), .clk(\clock_时钟信号 ), .clr(\clear_清零信号 ));
  Register #(.width(16)) D02 (
    .D(multiplexer_18_out), .en(\en_寄存器使能信号 ), .Q(rt_2), .clk(\clock_时钟信号 ), .clr(\clear_清零信号 ));
  Register #(.width(16)) \u_immediate_扩展后的立即数  (
    .D(multiplexer_19_out), .en(\en_寄存器使能信号 ), .Q(\immediate_扩展后的立即数_2 ), .clk(\clock_时钟信号 ),
    .clr(\clear_清零信号 ));
  Register #(.width(32)) u_R3R2 (
    .D(multiplexer_20_out), .en(\en_寄存器使能信号 ), .Q(R3R2_2), .clk(\clock_时钟信号 ), .clr(\clear_清零信号 ));
  Register #(.width(32)) u_R1R0 (
    .D(multiplexer_21_out), .en(\en_寄存器使能信号 ), .Q(R1R0_2), .clk(\clock_时钟信号 ), .clr(\clear_清零信号 ));
endmodule

module EX_MEM (
  input  [15:0] PC,
  input  [15:0] instruction,
  input  [3:0] ALUop,
  input  ALUSrc,
  input  RegWrite,
  input  MemtoReg,
  input  halt,
  input  MemWrite,
  input  slt,
  input  lui,
  input  disp,
  input  RegDst,
  input  [15:0] \jump_address_跳转地址 ,
  input  \zero_0标志位 ,
  input  \over_溢出标志位 ,
  input  [15:0] ALUout,
  input  [15:0] rt,
  input  [31:0] R3R2,
  input  [31:0] R1R0,
  input  \en_寄存器使能信号 ,
  input  \clock_时钟信号 ,
  input  \clear_清零信号 ,
  input  \同步清零 ,
  output [15:0] PC_2,
  output [15:0] instruction_2,
  output [3:0] ALUop_2,
  output ALUSrc_2,
  output RegWrite_2,
  output MemtoReg_2,
  output halt_2,
  output MemWrite_2,
  output slt_2,
  output lui_2,
  output disp_2,
  output RegDst_2,
  output [15:0] \jump_address_跳转地址_2 ,
  output \zero_0标志位_2 ,
  output \over_溢出标志位_2 ,
  output [15:0] ALUout_2,
  output [15:0] rt_2,
  output [31:0] R3R2_2,
  output [31:0] R1R0_2
);

  wire multiplexer_4_out, multiplexer_5_out, multiplexer_6_out, multiplexer_7_out, multiplexer_8_out,
       multiplexer_9_out, multiplexer_10_out, multiplexer_11_out, multiplexer_12_out, multiplexer_14_out,
       multiplexer_15_out;
  wire [3:0] multiplexer_3_out;
  wire [15:0] multiplexer_1_out, multiplexer_2_out, multiplexer_13_out, multiplexer_16_out,
       multiplexer_17_out;
  wire [31:0] multiplexer_18_out, multiplexer_19_out;

  Multiplexer #(.width(16), .enable("false")) multiplexer_1 (
    .in0(PC), .in1({16{1'b0}}), .out(multiplexer_1_out), .sel(\同步清零 ));
  Multiplexer #(.width(16), .enable("false")) multiplexer_2 (
    .in0(instruction), .in1({16{1'b0}}), .out(multiplexer_2_out), .sel(\同步清零 ));
  Multiplexer #(.width(4), .enable("false")) multiplexer_3 (
    .in0(ALUop), .in1(4'b0000), .out(multiplexer_3_out), .sel(\同步清零 ));
  Multiplexer #(.enable("false")) multiplexer_4 (.in0(ALUSrc), .in1(1'b0), .out(multiplexer_4_out), .sel(\同步清零 ));
  Multiplexer #(.enable("false")) multiplexer_5 (.in0(RegWrite), .in1(1'b0), .out(multiplexer_5_out), .sel(\同步清零 ));
  Multiplexer #(.enable("false")) multiplexer_6 (.in0(MemtoReg), .in1(1'b0), .out(multiplexer_6_out), .sel(\同步清零 ));
  Multiplexer #(.enable("false")) multiplexer_7 (.in0(halt), .in1(1'b0), .out(multiplexer_7_out), .sel(\同步清零 ));
  Multiplexer #(.enable("false")) multiplexer_8 (.in0(MemWrite), .in1(1'b0), .out(multiplexer_8_out), .sel(\同步清零 ));
  Multiplexer #(.enable("false")) multiplexer_9 (.in0(slt), .in1(1'b0), .out(multiplexer_9_out), .sel(\同步清零 ));
  Multiplexer #(.enable("false")) multiplexer_10 (.in0(lui), .in1(1'b0), .out(multiplexer_10_out), .sel(\同步清零 ));
  Multiplexer #(.enable("false")) multiplexer_11 (.in0(disp), .in1(1'b0), .out(multiplexer_11_out), .sel(\同步清零 ));
  Multiplexer #(.enable("false")) multiplexer_12 (.in0(RegDst), .in1(1'b0), .out(multiplexer_12_out), .sel(\同步清零 ));
  Multiplexer #(.width(16), .enable("false")) multiplexer_13 (
    .in0(\jump_address_跳转地址 ), .in1({16{1'b0}}), .out(multiplexer_13_out), .sel(\同步清零 ));
  Multiplexer #(.enable("false")) multiplexer_14 (
    .in0(\zero_0标志位 ), .in1(1'b0), .out(multiplexer_14_out), .sel(\同步清零 ));
  Multiplexer #(.enable("false")) multiplexer_15 (
    .in0(\over_溢出标志位 ), .in1(1'b0), .out(multiplexer_15_out), .sel(\同步清零 ));
  Multiplexer #(.width(16), .enable("false")) multiplexer_16 (
    .in0(ALUout), .in1({16{1'b0}}), .out(multiplexer_16_out), .sel(\同步清零 ));
  Multiplexer #(.width(16), .enable("false")) multiplexer_17 (
    .in0(rt), .in1({16{1'b0}}), .out(multiplexer_17_out), .sel(\同步清零 ));
  Multiplexer #(.width(32), .enable("false")) multiplexer_18 (
    .in0(R3R2), .in1({32{1'b0}}), .out(multiplexer_18_out), .sel(\同步清零 ));
  Multiplexer #(.width(32), .enable("false")) multiplexer_19 (
    .in0(R1R0), .in1({32{1'b0}}), .out(multiplexer_19_out), .sel(\同步清零 ));
  Register #(.width(16)) u_PC (
    .D(multiplexer_1_out), .en(\en_寄存器使能信号 ), .Q(PC_2), .clk(\clock_时钟信号 ), .clr(\clear_清零信号 ));
  Register #(.width(16)) u_instruction (
    .D(multiplexer_2_out), .en(\en_寄存器使能信号 ), .Q(instruction_2), .clk(\clock_时钟信号 ), .clr(\clear_清零信号 ));
  Register #(.width(4)) u_ALUop (
    .D(multiplexer_3_out), .en(\en_寄存器使能信号 ), .Q(ALUop_2), .clk(\clock_时钟信号 ), .clr(\clear_清零信号 ));
  Register #(.width(1)) u_ALUSrc (
    .D(multiplexer_4_out), .en(\en_寄存器使能信号 ), .Q(ALUSrc_2), .clk(\clock_时钟信号 ), .clr(\clear_清零信号 ));
  Register #(.width(1)) u_RegWrite (
    .D(multiplexer_5_out), .en(\en_寄存器使能信号 ), .Q(RegWrite_2), .clk(\clock_时钟信号 ), .clr(\clear_清零信号 ));
  Register #(.width(1)) u_MemtoReg (
    .D(multiplexer_6_out), .en(\en_寄存器使能信号 ), .Q(MemtoReg_2), .clk(\clock_时钟信号 ), .clr(\clear_清零信号 ));
  Register #(.width(1)) u_halt (
    .D(multiplexer_7_out), .en(\en_寄存器使能信号 ), .Q(halt_2), .clk(\clock_时钟信号 ), .clr(\clear_清零信号 ));
  Register #(.width(1)) u_MemWrite (
    .D(multiplexer_8_out), .en(\en_寄存器使能信号 ), .Q(MemWrite_2), .clk(\clock_时钟信号 ), .clr(\clear_清零信号 ));
  Register #(.width(1)) u_slt (
    .D(multiplexer_9_out), .en(\en_寄存器使能信号 ), .Q(slt_2), .clk(\clock_时钟信号 ), .clr(\clear_清零信号 ));
  Register #(.width(1)) u_lui (
    .D(multiplexer_10_out), .en(\en_寄存器使能信号 ), .Q(lui_2), .clk(\clock_时钟信号 ), .clr(\clear_清零信号 ));
  Register #(.width(1)) u_disp (
    .D(multiplexer_11_out), .en(\en_寄存器使能信号 ), .Q(disp_2), .clk(\clock_时钟信号 ), .clr(\clear_清零信号 ));
  Register #(.width(1)) u_RegDst (
    .D(multiplexer_12_out), .en(\en_寄存器使能信号 ), .Q(RegDst_2), .clk(\clock_时钟信号 ), .clr(\clear_清零信号 ));
  Register #(.width(16)) \u_jump_address_跳转地址  (
    .D(multiplexer_13_out), .en(\en_寄存器使能信号 ), .Q(\jump_address_跳转地址_2 ), .clk(\clock_时钟信号 ),
    .clr(\clear_清零信号 ));
  Register #(.width(1)) \u_zero_0标志位  (
    .D(multiplexer_14_out), .en(\en_寄存器使能信号 ), .Q(\zero_0标志位_2 ), .clk(\clock_时钟信号 ), .clr(\clear_清零信号 ));
  Register #(.width(1)) \u_over_溢出标志位  (
    .D(multiplexer_15_out), .en(\en_寄存器使能信号 ), .Q(\over_溢出标志位_2 ), .clk(\clock_时钟信号 ), .clr(\clear_清零信号 ));
  Register #(.width(16)) u_ALUout (
    .D(multiplexer_16_out), .en(\en_寄存器使能信号 ), .Q(ALUout_2), .clk(\clock_时钟信号 ), .clr(\clear_清零信号 ));
  Register #(.width(16)) u_rt (
    .D(multiplexer_17_out), .en(\en_寄存器使能信号 ), .Q(rt_2), .clk(\clock_时钟信号 ), .clr(\clear_清零信号 ));
  Register #(.width(32)) u_R3R2 (
    .D(multiplexer_18_out), .en(\en_寄存器使能信号 ), .Q(R3R2_2), .clk(\clock_时钟信号 ), .clr(\clear_清零信号 ));
  Register #(.width(32)) u_R1R0 (
    .D(multiplexer_19_out), .en(\en_寄存器使能信号 ), .Q(R1R0_2), .clk(\clock_时钟信号 ), .clr(\clear_清零信号 ));
endmodule

module MEM_WB (
  input  [15:0] PC,
  input  [15:0] instruction,
  input  [3:0] ALUop,
  input  ALUSrc,
  input  RegWrite,
  input  MemtoReg,
  input  halt,
  input  MemWrite,
  input  slt,
  input  lui,
  input  disp,
  input  RegDst,
  input  [15:0] \jump_address_跳转地址 ,
  input  \zero_0标志位 ,
  input  \over_溢出标志位 ,
  input  [15:0] ALUout,
  input  [15:0] MemOut,
  input  [31:0] R3R2,
  input  [31:0] R1R0,
  input  \en_寄存器使能信号 ,
  input  \clock_时钟信号 ,
  input  \clear_清零信号 ,
  output [15:0] PC_2,
  output [15:0] instruction_2,
  output [3:0] ALUop_2,
  output ALUSrc_2,
  output RegWrite_2,
  output MemtoReg_2,
  output halt_2,
  output MemWrite_2,
  output slt_2,
  output lui_2,
  output disp_2,
  output RegDst_2,
  output [15:0] \jump_address_跳转地址_2 ,
  output \zero_0标志位_2 ,
  output \over_溢出标志位_2 ,
  output [15:0] ALUout_2,
  output [15:0] MemOut_2,
  output [31:0] R3R2_2,
  output [31:0] R1R0_2
);

  Register #(.width(16)) u_PC (.D(PC), .en(\en_寄存器使能信号 ), .Q(PC_2), .clk(\clock_时钟信号 ), .clr(\clear_清零信号 ));
  Register #(.width(16)) u_instruction (
    .D(instruction), .en(\en_寄存器使能信号 ), .Q(instruction_2), .clk(\clock_时钟信号 ), .clr(\clear_清零信号 ));
  Register #(.width(4)) u_ALUop (.D(ALUop), .en(\en_寄存器使能信号 ), .Q(ALUop_2), .clk(\clock_时钟信号 ), .clr(\clear_清零信号 ));
  Register #(.width(1)) u_ALUSrc (.D(ALUSrc), .en(\en_寄存器使能信号 ), .Q(ALUSrc_2), .clk(\clock_时钟信号 ), .clr(\clear_清零信号 ));
  Register #(.width(1)) u_RegWrite (
    .D(RegWrite), .en(\en_寄存器使能信号 ), .Q(RegWrite_2), .clk(\clock_时钟信号 ), .clr(\clear_清零信号 ));
  Register #(.width(1)) u_MemtoReg (
    .D(MemtoReg), .en(\en_寄存器使能信号 ), .Q(MemtoReg_2), .clk(\clock_时钟信号 ), .clr(\clear_清零信号 ));
  Register #(.width(1)) u_halt (.D(halt), .en(\en_寄存器使能信号 ), .Q(halt_2), .clk(\clock_时钟信号 ), .clr(\clear_清零信号 ));
  Register #(.width(1)) u_MemWrite (
    .D(MemWrite), .en(\en_寄存器使能信号 ), .Q(MemWrite_2), .clk(\clock_时钟信号 ), .clr(\clear_清零信号 ));
  Register #(.width(1)) u_slt (.D(slt), .en(\en_寄存器使能信号 ), .Q(slt_2), .clk(\clock_时钟信号 ), .clr(\clear_清零信号 ));
  Register #(.width(1)) u_lui (.D(lui), .en(\en_寄存器使能信号 ), .Q(lui_2), .clk(\clock_时钟信号 ), .clr(\clear_清零信号 ));
  Register #(.width(1)) u_disp (.D(disp), .en(\en_寄存器使能信号 ), .Q(disp_2), .clk(\clock_时钟信号 ), .clr(\clear_清零信号 ));
  Register #(.width(1)) u_RegDst (.D(RegDst), .en(\en_寄存器使能信号 ), .Q(RegDst_2), .clk(\clock_时钟信号 ), .clr(\clear_清零信号 ));
  Register #(.width(16)) \u_jump_address_跳转地址  (
    .D(\jump_address_跳转地址 ), .en(\en_寄存器使能信号 ), .Q(\jump_address_跳转地址_2 ), .clk(\clock_时钟信号 ),
    .clr(\clear_清零信号 ));
  Register #(.width(1)) \u_zero_0标志位  (
    .D(\zero_0标志位 ), .en(\en_寄存器使能信号 ), .Q(\zero_0标志位_2 ), .clk(\clock_时钟信号 ), .clr(\clear_清零信号 ));
  Register #(.width(1)) \u_over_溢出标志位  (
    .D(\over_溢出标志位 ), .en(\en_寄存器使能信号 ), .Q(\over_溢出标志位_2 ), .clk(\clock_时钟信号 ), .clr(\clear_清零信号 ));
  Register #(.width(16)) u_ALUout (.D(ALUout), .en(\en_寄存器使能信号 ), .Q(ALUout_2), .clk(\clock_时钟信号 ), .clr(\clear_清零信号 ));
  Register #(.width(16)) u_MemOut (.D(MemOut), .en(\en_寄存器使能信号 ), .Q(MemOut_2), .clk(\clock_时钟信号 ), .clr(\clear_清零信号 ));
  Register #(.width(32)) u_R3R2 (.D(R3R2), .en(\en_寄存器使能信号 ), .Q(R3R2_2), .clk(\clock_时钟信号 ), .clr(\clear_清零信号 ));
  Register #(.width(32)) u_R1R0 (.D(R1R0), .en(\en_寄存器使能信号 ), .Q(R1R0_2), .clk(\clock_时钟信号 ), .clr(\clear_清零信号 ));
endmodule

module slt_0_1_2 (
  input  \falg_符号位 ,
  input  \overflow_溢出信号 ,
  input  [3:0] \OP_操作码 ,
  input  [2:0] \Funct_函数字段 ,
  output [15:0] slt_0_1
);

  wire and_1_out, and_2_out, and_3_out, multiplexer_1_out, multiplexer_2_out, not_1_out, not_2_out,
       not_3_out, not_4_out, not_5_out;

  not not_1 (not_1_out, \OP_操作码 [0]);
  not not_2 (not_2_out, \OP_操作码 [1]);
  not not_3 (not_3_out, \OP_操作码 [2]);
  not not_4 (not_4_out, \OP_操作码 [3]);
  Multiplexer #(.enable("false")) multiplexer_1 (
    .in0(\falg_符号位 ), .in1(not_5_out), .out(multiplexer_1_out), .sel(\overflow_溢出信号 ));
  not not_5 (not_5_out, \falg_符号位 );
  and and_1 (and_1_out, not_1_out, not_2_out, not_3_out, not_4_out);
  and and_2 (and_2_out, \Funct_函数字段 [0], \Funct_函数字段 [1], \Funct_函数字段 [2]);
  Multiplexer #(.enable("false")) multiplexer_2 (
    .in0(1'b0), .in1(multiplexer_1_out), .out(multiplexer_2_out), .sel(and_3_out));
  and and_3 (and_3_out, and_1_out, and_2_out);
  assign slt_0_1 = {{15{1'b0}}, multiplexer_2_out};  // Bit_Extender bit_extender_1
endmodule

// conflict
module \conflict_冲突检测  (
  input  [15:0] \instruction_0_当前指令 ,
  input  [15:0] \instruction_1_下一条指令 ,
  output \data_数据冲突 ,
  output \branch_分支冲突 ,
  output \conflict_为1时候冲突 
);

  wire _0_2_out, _0_3_out, _0_out, _1_2_out, _1_out, _2_2_out, _2_out, _3_2_out, _3_out, _5_out, _6_2_out,
       _6_3_out, _6_out, _7_2_out, _7_3_out, _7_out, _8_2_out, _8_3_out, _8_out, _9_2_out, _9_3_out, _9_out,
       _10_out, _11_out, and_1_out, and_2_out, and_3_out, comparator_1_eq, comparator_2_eq,
       multiplexer_2_out, nor_1_out, not_2_out, not_3_out, not_4_out, not_5_out, not_6_out, not_7_out,
       not_8_out, not_9_out, not_10_out, not_11_out, not_12_out, not_13_out, not_14_out, not_15_out,
       not_16_out, not_17_out, not_18_out, not_19_out, not_20_out, not_21_out, not_22_out, not_23_out,
       not_24_out, not_25_out, not_26_out, not_27_out, not_28_out, not_29_out, not_30_out, not_31_out,
       not_32_out, not_33_out, not_34_out, not_35_out, not_36_out, not_37_out, not_38_out, not_39_out,
       not_40_out, not_41_out, not_42_out, not_43_out, not_44_out, not_45_out, not_46_out, not_47_out,
       not_48_out, not_49_out, not_50_out, not_51_out, not_52_out, not_53_out, not_54_out, not_55_out,
       not_56_out, not_57_out, or_1_out, or_2_out, or_3_out, or_4_out, or_5_out, xnor_1_out, xnor_2_out,
       xnor_3_out, xnor_4_out, \加_4_out ;
  wire [1:0] \idecoder_指令译码器_1_rd , \idecoder_指令译码器_1_rt , \idecoder_指令译码器_2_rs , \idecoder_指令译码器_2_rt ,
       multiplexer_1_out;
  wire [3:0] \idecoder_指令译码器_1_op , \idecoder_指令译码器_2_op , \idecoder_指令译码器_3_op , \idecoder_指令译码器_4_op ,
       not_1_out;

  \IDecoder_指令译码器  \idecoder_指令译码器_1  (
    .\Instruction_指令 (\instruction_0_当前指令 ), .rd(\idecoder_指令译码器_1_rd ), .rt(\idecoder_指令译码器_1_rt ),
    .OP(\idecoder_指令译码器_1_op ));  // open: Funct, P, rs, immediate, jump_address
  assign not_1_out = ~\idecoder_指令译码器_1_op ;  // NOT_Gate not_1, 4 bits wide
  \IDecoder_指令译码器  \idecoder_指令译码器_2  (
    .\Instruction_指令 (\instruction_1_下一条指令 ), .rt(\idecoder_指令译码器_2_rt ), .rs(\idecoder_指令译码器_2_rs ),
    .OP(\idecoder_指令译码器_2_op ));  // open: Funct, P, rd, immediate, jump_address
  \IDecoder_指令译码器  \idecoder_指令译码器_3  (
    .\Instruction_指令 (\instruction_1_下一条指令 ), .OP(\idecoder_指令译码器_3_op ));  // open: Funct, P, rd, rt, rs, immediate, jump_address
  not not_2 (not_2_out, \idecoder_指令译码器_2_op [3]);
  not not_3 (not_3_out, \idecoder_指令译码器_2_op [0]);
  not not_4 (not_4_out, \idecoder_指令译码器_2_op [3]);
  not not_5 (not_5_out, \idecoder_指令译码器_2_op [2]);
  not not_6 (not_6_out, \idecoder_指令译码器_2_op [1]);
  not not_7 (not_7_out, \idecoder_指令译码器_2_op [0]);
  not not_8 (not_8_out, \idecoder_指令译码器_2_op [2]);
  not not_9 (not_9_out, \idecoder_指令译码器_2_op [1]);
  not not_10 (not_10_out, \idecoder_指令译码器_3_op [3]);
  not not_11 (not_11_out, \idecoder_指令译码器_3_op [2]);
  not not_12 (not_12_out, \idecoder_指令译码器_3_op [1]);
  not not_13 (not_13_out, \idecoder_指令译码器_3_op [0]);
  not not_14 (not_14_out, \idecoder_指令译码器_3_op [3]);
  not not_15 (not_15_out, \idecoder_指令译码器_3_op [2]);
  not not_16 (not_16_out, \idecoder_指令译码器_3_op [1]);
  not not_17 (not_17_out, \idecoder_指令译码器_3_op [3]);
  not not_18 (not_18_out, \idecoder_指令译码器_3_op [2]);
  not not_19 (not_19_out, \idecoder_指令译码器_3_op [0]);
  not not_20 (not_20_out, \idecoder_指令译码器_3_op [3]);
  not not_21 (not_21_out, \idecoder_指令译码器_3_op [2]);
  not not_22 (not_22_out, \idecoder_指令译码器_3_op [3]);
  not not_23 (not_23_out, \idecoder_指令译码器_3_op [0]);
  not not_24 (not_24_out, \idecoder_指令译码器_3_op [3]);
  not not_25 (not_25_out, \idecoder_指令译码器_3_op [2]);
  not not_26 (not_26_out, \idecoder_指令译码器_3_op [1]);
  not not_27 (not_27_out, \idecoder_指令译码器_3_op [0]);
  not not_28 (not_28_out, \idecoder_指令译码器_3_op [2]);
  not not_29 (not_29_out, \idecoder_指令译码器_3_op [1]);
  not not_30 (not_30_out, \idecoder_指令译码器_3_op [2]);
  not not_31 (not_31_out, \idecoder_指令译码器_3_op [0]);
  not not_32 (not_32_out, \idecoder_指令译码器_3_op [3]);
  not not_33 (not_33_out, \idecoder_指令译码器_3_op [1]);
  not not_34 (not_34_out, \idecoder_指令译码器_3_op [0]);
  Multiplexer #(.width(2), .enable("false")) multiplexer_1 (
    .in0(\idecoder_指令译码器_1_rt ), .in1(\idecoder_指令译码器_1_rd ), .out(multiplexer_1_out), .sel(_0_out));
  and _0 (_0_out, not_1_out[0], not_1_out[1], not_1_out[2], not_1_out[3]);
  and _6 (_6_out, not_2_out, \idecoder_指令译码器_2_op [2], \idecoder_指令译码器_2_op [1], not_3_out);
  and _7 (_7_out, not_4_out, \idecoder_指令译码器_2_op [2], \idecoder_指令译码器_2_op [1], \idecoder_指令译码器_2_op [0]);
  and _8 (_8_out, \idecoder_指令译码器_2_op [3], not_5_out, not_6_out, not_7_out);
  and _9 (_9_out, \idecoder_指令译码器_2_op [3], not_8_out, not_9_out, \idecoder_指令译码器_2_op [0]);
  and _0_2 (_0_2_out, not_10_out, not_11_out, not_12_out, not_13_out);
  and _1 (_1_out, not_14_out, not_15_out, not_16_out, \idecoder_指令译码器_3_op [0]);
  and _2 (_2_out, not_17_out, not_18_out, \idecoder_指令译码器_3_op [1], not_19_out);
  and _3 (_3_out, not_20_out, not_21_out, \idecoder_指令译码器_3_op [1], \idecoder_指令译码器_3_op [0]);
  and _6_2 (_6_2_out, not_22_out, \idecoder_指令译码器_3_op [2], \idecoder_指令译码器_3_op [1], not_23_out);
  and _7_2 (_7_2_out, not_24_out, \idecoder_指令译码器_3_op [2], \idecoder_指令译码器_3_op [1], \idecoder_指令译码器_3_op [0]);
  and _8_2 (_8_2_out, \idecoder_指令译码器_3_op [3], not_25_out, not_26_out, not_27_out);
  and _9_2 (_9_2_out, \idecoder_指令译码器_3_op [3], not_28_out, not_29_out, \idecoder_指令译码器_3_op [0]);
  and _10 (_10_out, \idecoder_指令译码器_3_op [3], not_30_out, \idecoder_指令译码器_3_op [1], not_31_out);
  and \u_加_4  (\加_4_out , not_32_out, \idecoder_指令译码器_3_op [2], not_33_out, not_34_out);
  or or_1 (or_1_out, _6_out, _7_out, _8_out, _9_out);
  \IDecoder_指令译码器  \idecoder_指令译码器_4  (
    .\Instruction_指令 (\instruction_0_当前指令 ), .OP(\idecoder_指令译码器_4_op ));  // open: Funct, P, rd, rt, rs, immediate, jump_address
  // Probe on multiplexer_1_out
  // Probe on multiplexer_1_out
  not not_35 (not_35_out, \idecoder_指令译码器_4_op [3]);
  not not_36 (not_36_out, \idecoder_指令译码器_4_op [2]);
  not not_37 (not_37_out, \idecoder_指令译码器_4_op [1]);
  not not_38 (not_38_out, \idecoder_指令译码器_4_op [0]);
  not not_39 (not_39_out, \idecoder_指令译码器_4_op [3]);
  not not_40 (not_40_out, \idecoder_指令译码器_4_op [1]);
  not not_41 (not_41_out, \idecoder_指令译码器_4_op [3]);
  not not_42 (not_42_out, \idecoder_指令译码器_4_op [0]);
  or or_2 (or_2_out, _0_2_out, _1_out, _2_out, _3_out, _6_2_out, _7_2_out, _8_2_out, _9_2_out, _10_out, \加_4_out );
  not not_43 (not_43_out, \idecoder_指令译码器_4_op [3]);
  not not_44 (not_44_out, \idecoder_指令译码器_4_op [2]);
  not not_45 (not_45_out, \idecoder_指令译码器_4_op [1]);
  not not_46 (not_46_out, \idecoder_指令译码器_4_op [0]);
  not not_47 (not_47_out, \idecoder_指令译码器_4_op [2]);
  not not_48 (not_48_out, \idecoder_指令译码器_4_op [1]);
  not not_49 (not_49_out, \idecoder_指令译码器_4_op [3]);
  not not_50 (not_50_out, \idecoder_指令译码器_4_op [2]);
  not not_51 (not_51_out, \idecoder_指令译码器_4_op [1]);
  not not_52 (not_52_out, \idecoder_指令译码器_4_op [3]);
  not not_53 (not_53_out, \idecoder_指令译码器_4_op [2]);
  not not_54 (not_54_out, \idecoder_指令译码器_4_op [0]);
  not not_55 (not_55_out, \idecoder_指令译码器_4_op [3]);
  not not_56 (not_56_out, \idecoder_指令译码器_4_op [2]);
  not not_57 (not_57_out, \idecoder_指令译码器_4_op [2]);
  // Probe on \idecoder_指令译码器_2_rs 
  // Probe on \idecoder_指令译码器_2_rt 
  and _0_3 (_0_3_out, not_35_out, not_36_out, not_37_out, not_38_out);
  and _5 (_5_out, not_39_out, \idecoder_指令译码器_4_op [2], not_40_out, \idecoder_指令译码器_4_op [0]);
  and _6_3 (_6_3_out, not_41_out, \idecoder_指令译码器_4_op [2], \idecoder_指令译码器_4_op [1], not_42_out);
  and _7_3 (_7_3_out, not_43_out, \idecoder_指令译码器_4_op [2], \idecoder_指令译码器_4_op [1], \idecoder_指令译码器_4_op [0]);
  and _8_3 (_8_3_out, \idecoder_指令译码器_4_op [3], not_44_out, not_45_out, not_46_out);
  and _9_3 (_9_3_out, \idecoder_指令译码器_4_op [3], not_47_out, not_48_out, \idecoder_指令译码器_4_op [0]);
  and _1_2 (_1_2_out, not_49_out, not_50_out, not_51_out, \idecoder_指令译码器_4_op [0]);
  and _2_2 (_2_2_out, not_52_out, not_53_out, \idecoder_指令译码器_4_op [1], not_54_out);
  and _3_2 (_3_2_out, not_55_out, not_56_out, \idecoder_指令译码器_4_op [1], \idecoder_指令译码器_4_op [0]);
  and _11 (_11_out, \idecoder_指令译码器_4_op [3], not_57_out, \idecoder_指令译码器_4_op [1], \idecoder_指令译码器_4_op [0]);
  or \u_分支冲突  (\branch_分支冲突 , _1_2_out, _2_2_out, _3_2_out, _11_out);
  xnor xnor_1 (xnor_1_out, multiplexer_1_out[0], \idecoder_指令译码器_2_rs [0]);
  and and_1 (and_1_out, xnor_1_out, xnor_2_out);
  xnor xnor_2 (xnor_2_out, \idecoder_指令译码器_2_rs [1], multiplexer_1_out[1]);
  xnor xnor_3 (xnor_3_out, multiplexer_1_out[0], \idecoder_指令译码器_2_rt [0]);
  and and_2 (and_2_out, xnor_3_out, xnor_4_out);
  xnor xnor_4 (xnor_4_out, \idecoder_指令译码器_2_rt [1], multiplexer_1_out[1]);
  or or_3 (or_3_out, _0_3_out, _5_out, _6_3_out, _7_3_out, _8_3_out, _9_3_out);
  or or_4 (or_4_out, and_1_out, and_2_out);
  Multiplexer #(.enable("false")) multiplexer_2 (
    .in0(or_4_out), .in1(and_1_out), .out(multiplexer_2_out), .sel(or_1_out));
  and \data冲突  (\data_数据冲突 , multiplexer_2_out, and_3_out);
  and and_3 (and_3_out, or_3_out, or_2_out);
  or or_5 (or_5_out, \data_数据冲突 , 1'b0);
  Comparator #(.width(16)) comparator_1 (
    .a(\instruction_0_当前指令 ), .b({16{1'b0}}), .eq(comparator_1_eq));  // open: gt, lt
  nor nor_1 (nor_1_out, comparator_1_eq, comparator_2_eq);
  Comparator #(.width(16)) comparator_2 (
    .a(\instruction_1_下一条指令 ), .b({16{1'b0}}), .eq(comparator_2_eq));  // open: gt, lt
  and and_4 (\conflict_为1时候冲突 , or_5_out, nor_1_out);
endmodule

// conflict
module \完全冲突检测  (
  input  [15:0] \next_下一条进入电路的指令 ,
  input  [15:0] ID,
  input  [15:0] EX,
  output \conflict_是否冲突 
);

  wire \conflict_冲突检测_1_conflict_为1时候冲突 , \conflict_冲突检测_2_conflict_为1时候冲突 ;

  or or_1 (\conflict_是否冲突 , \conflict_冲突检测_1_conflict_为1时候冲突 , \conflict_冲突检测_2_conflict_为1时候冲突 );
  \conflict_冲突检测  \conflict_冲突检测_1  (
    .\instruction_0_当前指令 (ID), .\instruction_1_下一条指令 (\next_下一条进入电路的指令 ),
    .\conflict_为1时候冲突 (\conflict_冲突检测_1_conflict_为1时候冲突 ));  // open: data_数据冲突, branch_分支冲突
  \conflict_冲突检测  \conflict_冲突检测_2  (
    .\instruction_0_当前指令 (EX), .\instruction_1_下一条指令 (\next_下一条进入电路的指令 ),
    .\conflict_为1时候冲突 (\conflict_冲突检测_2_conflict_为1时候冲突 ));  // open: data_数据冲突, branch_分支冲突
endmodule

// bubble
module \bubble_气泡控制信号传递  (
  input  \bubble_输入气泡 ,
  input  \en_使能信号 ,
  input  \clear_清零信号 ,
  input  \clock_时钟信号 ,
  output \bubble_输出气泡 
);

  wire bubble_2_q, bubble_3_q, bubble_q;

  Register #(.width(1)) bubble (
    .D(\bubble_输入气泡 ), .en(\en_使能信号 ), .Q(bubble_q), .clk(\clock_时钟信号 ), .clr(\clear_清零信号 ));
  Register #(.width(1)) bubble_2 (.D(bubble_q), .en(\en_使能信号 ), .Q(bubble_2_q), .clk(\clock_时钟信号 ), .clr(\clear_清零信号 ));
  Register #(.width(1)) bubble_3 (
    .D(bubble_2_q), .en(\en_使能信号 ), .Q(bubble_3_q), .clk(\clock_时钟信号 ), .clr(\clear_清零信号 ));
  Register #(.width(1)) bubble_4 (
    .D(bubble_3_q), .en(\en_使能信号 ), .Q(\bubble_输出气泡 ), .clk(\clock_时钟信号 ), .clr(\clear_清零信号 ));
endmodule
module \气泡  (
  input  \为1时启动 
);

  wire \alu16位运算器_1_溢出 , \alu16位运算器_1_零 , and_1_out, \branch_控制部件_1_branch_是否跳转的控制信号 , CK, clock, clr, color,
       \EX_MEM_over_溢出标志位_2 , \EX_MEM_zero_0标志位_2 , \flag_取一个数的最高位_1_flag_value的最高位 ,
       \flag_取一个数的最高位_2_flag_value的最高位 , MEM_WB_alusrc_2, MEM_WB_disp_2, MEM_WB_halt_2, MEM_WB_lui_2,
       MEM_WB_memtoreg_2, MEM_WB_memwrite_2, MEM_WB_regdst_2, MEM_WB_regwrite_2, MEM_WB_slt_2,
       \MEM_WB_zero_0标志位_2 , not_1_out, not_2_out, not_4_out, or_1_out, or_2_out, part_1_out_3, register_1_q,
       \启停控制电路_1_f_输出时钟 , \完全冲突检测_1_conflict_是否冲突 , \控制器_1_regwrite ;
  wire [1:0] \idecoder_指令译码器_1_rd , \idecoder_指令译码器_1_rs , \idecoder_指令译码器_1_rt , \idecoder_指令译码器_3_rd ,
       \idecoder_指令译码器_3_rt , multiplexer_2_out, num;
  wire [2:0] \idecoder_指令译码器_1_funct , \idecoder_指令译码器_1_p , \idecoder_指令译码器_2_funct ;
  wire [3:0] EX_MEM_aluop_2, ID_EX_aluop_2, \ID_EX_op_操作码_2 , \idecoder_指令译码器_1_op , \idecoder_指令译码器_2_op ,
       MEM_WB_aluop_2, \控制器_1_aluop ;
  wire [7:0] ID_EX_offset_2, \idecoder_指令译码器_1_immediate ;
  wire [8:0] EX_MEM_alusrc_2, ID_EX_alusrc_2, \控制器_1_alusrc ;
  wire [11:0] counter_1_q, ID_EX_jump_2, \idecoder_指令译码器_1_jump_address ;
  wire [15:0] adder_1_out, \alu16位运算器_1_输出f , DISP_0, DISP_1, EX_MEM_aluout_2, EX_MEM_instruction_2,
       \EX_MEM_jump_address_跳转地址_2 , EX_MEM_pc_2, EX_MEM_rt_2, \extend_立即数符号扩展_1_extended_value_扩展结果 ,
       \ID_EX_immediate_扩展后的立即数_2 , ID_EX_instruction_2, ID_EX_pc_1_2, ID_EX_pc_2, ID_EX_rs_2, ID_EX_rt_2,
       \if_id_1_instruction_指令输出 , \if_id_1_instruction_指令输出_2 , \if_id_1_pc_1_输出 , if_id_1_pc_2,
       MEM_WB_aluout_2, MEM_WB_instruction_2, MEM_WB_memout_2, MEM_WB_pc_2, multiplexer_1_out,
       multiplexer_3_out, multiplexer_4_out, multiplexer_5_out, multiplexer_6_out, multiplexer_7_out, PC_q,
       ram_1_data, \rf_寄存器堆_1_do1 , \rf_寄存器堆_1_do2 , rom_1_data, slt_0_1_1_slt_0_1, \跳转地址形成部件_1_jump_address ;
  wire [31:0] R1R0, R3R2;

  // Probe on R3R2
  // Probe on R1R0
  // Probe on \跳转地址形成部件_1_jump_address 
  not not_1 (not_1_out, \完全冲突检测_1_conflict_是否冲突 );
  or or_1 (or_1_out, \branch_控制部件_1_branch_是否跳转的控制信号 , not_1_out);
  Multiplexer #(.width(16), .enable("false")) multiplexer_1 (
    .in0(adder_1_out), .in1(\跳转地址形成部件_1_jump_address ), .out(multiplexer_1_out),
    .sel(\branch_控制部件_1_branch_是否跳转的控制信号 ));
  Counter #(.width(12), .max('hfff), .trigger("falling")) counter_1 (
    .count(1'b1), .Q(counter_1_q), .clk(clock), .clr(clr));  // open: load, D, carry
  DISP u_disp_1 (
    .R3R2(R3R2), .R1R0(R1R0), .\r_num_rs__寄存器编号 (num), .\DISP_disp控制信号_用于更新寄存器的值 (MEM_WB_disp_2),
    .\disp_color_颜色选择信号 (color), .\CLK_时钟信号 (clock), .DISP_0(DISP_0), .DISP1(DISP_1), .\CLR_清零信号 (clr));
  Register #(.width(16)) PC (.D(multiplexer_1_out), .en(or_1_out), .Q(PC_q), .clk(clock), .clr(clr));
  // Probe on counter_1_q
  Adder #(.width(16)) adder_1 (.a(16'h1), .b(PC_q), .out(adder_1_out), .cin(1'b0));  // open: cout
  not not_2 (not_2_out, MEM_WB_halt_2);
  ROM #(.addrWidth(16), .dataWidth(16)) rom_1 (.addr(PC_q), .data(rom_1_data));  // open: sel
  not not_3 (clock, \启停控制电路_1_f_输出时钟 );
  \启停控制电路  \u_启停控制电路_1  (.\F_输出时钟 (\启停控制电路_1_f_输出时钟 ), .\时钟 (CK), .\启动_为1时启动 (and_1_out), .\重置信号 (clr));
  and and_1 (and_1_out, \为1时启动 , not_2_out);
  Button \u_重置信号  (.out(clr));
  IF_ID if_id_1 (
    .PC_1(adder_1_out), .\instruction_指令 (rom_1_data), .\clock_时钟信号 (clock), .\clear_清零信号 (clr),
    .\PC_1_输出 (\if_id_1_pc_1_输出 ), .\instruction_指令输出_2 (\if_id_1_instruction_指令输出_2 ), .\en_使能信号 (1'b1),
    .PC(PC_q), .PC_2(if_id_1_pc_2), .\instruction_指令输出 (\if_id_1_instruction_指令输出 ), .\同步清零 (or_2_out));
  and and_2 (\控制器_1_alusrc [1], not_4_out, \控制器_1_regwrite );
  or or_2 (or_2_out, \完全冲突检测_1_conflict_是否冲突 , \branch_控制部件_1_branch_是否跳转的控制信号 );
  Bit_Extender #(.out_width(1)) bit_extender_1 (.in(\idecoder_指令译码器_1_immediate ), .out(color));
  \控制器  \u_控制器_1  (
    .\OP_操作码 (\idecoder_指令译码器_1_op ), .Funct(\idecoder_指令译码器_1_funct ), .RegDst(\控制器_1_alusrc [8]),
    .\lui_lui指令产生的单一控制信号 (\控制器_1_alusrc [6]), .MemWrite(\控制器_1_alusrc [4]), .MemtoReg(\控制器_1_alusrc [2]),
    .RegWrite(\控制器_1_regwrite ), .ALUSrc(\控制器_1_alusrc [0]), .ALUop(\控制器_1_aluop ), .disp(\控制器_1_alusrc [7]),
    .\halt_停机控制信号 (\控制器_1_alusrc [3]), .\slt_slt控制信号 (\控制器_1_alusrc [5]));
  \IDecoder_指令译码器  \idecoder_指令译码器_1  (
    .\Instruction_指令 (\if_id_1_instruction_指令输出_2 ), .Funct(\idecoder_指令译码器_1_funct ),
    .P(\idecoder_指令译码器_1_p ), .rd(\idecoder_指令译码器_1_rd ), .rt(\idecoder_指令译码器_1_rt ),
    .rs(\idecoder_指令译码器_1_rs ), .OP(\idecoder_指令译码器_1_op ), .immediate(\idecoder_指令译码器_1_immediate ),
    .jump_address(\idecoder_指令译码器_1_jump_address ));
  Hex_Digit_Display hex_digit_display_1 (.value(DISP_0[15:12]));  // open: dp
  Register #(.width(1)) register_1 (
    .D(\完全冲突检测_1_conflict_是否冲突 ), .Q(register_1_q), .clk(clock), .clr(clr));  // open: en
  Multiplexer #(.width(2), .enable("false")) multiplexer_2 (
    .in0(\idecoder_指令译码器_3_rt ), .in1(\idecoder_指令译码器_3_rd ), .out(multiplexer_2_out), .sel(MEM_WB_regdst_2));
  Hex_Digit_Display hex_digit_display_2 (.value(DISP_0[11:8]));  // open: dp
  Hex_Digit_Display hex_digit_display_3 (.value(DISP_0[7:4]));  // open: dp
  not not_4 (not_4_out, register_1_q);
  \完全冲突检测  \u_完全冲突检测_1  (
    .\next_下一条进入电路的指令 (rom_1_data), .\conflict_是否冲突 (\完全冲突检测_1_conflict_是否冲突 ),
    .ID(\if_id_1_instruction_指令输出 ), .EX(ID_EX_instruction_2));
  // Probe on \if_id_1_instruction_指令输出 
  \RF_寄存器堆  \rf_寄存器堆_1  (
    .Din(multiplexer_7_out), .\CP_时钟输入 (clock), .Do1(\rf_寄存器堆_1_do1 ), .rs(\idecoder_指令译码器_1_rs ),
    .Do2(\rf_寄存器堆_1_do2 ), .rt(\idecoder_指令译码器_1_rt ), .R1R0(R1R0), .R3R2(R3R2), .W(multiplexer_2_out),
    .\RegWrite_寄存器写控制信号 (MEM_WB_regwrite_2), .\ClR_清零信号 (clr));
  // Probe on multiplexer_7_out
  Hex_Digit_Display hex_digit_display_4 (.value(DISP_0[3:0]));  // open: dp
  // Probe on if_id_1_pc_2
  \Extend_立即数符号扩展  \extend_立即数符号扩展_1  (
    .\immidiate_立即数 (\idecoder_指令译码器_1_immediate ), .\OP_操作码 (\idecoder_指令译码器_1_op ),
    .\Extended_value_扩展结果 (\extend_立即数符号扩展_1_extended_value_扩展结果 ));
  Hex_Digit_Display hex_digit_display_5 (.value(DISP_1[15:12]));  // open: dp
  Hex_Digit_Display hex_digit_display_6 (.value(DISP_1[11:8]));  // open: dp
  ID_EX ID_EX (
    .PC(if_id_1_pc_2), .PC_2(ID_EX_pc_2), .instruction(\if_id_1_instruction_指令输出 ),
    .instruction_2(ID_EX_instruction_2), .ALUop(\控制器_1_aluop ), .ALUop_2(ID_EX_aluop_2),
    .ALUSrc(\控制器_1_alusrc [0]), .ALUSrc_2(ID_EX_alusrc_2[0]), .RegWrite(\控制器_1_alusrc [1]),
    .RegWrite_2(ID_EX_alusrc_2[1]), .MemtoReg(\控制器_1_alusrc [2]), .MemtoReg_2(ID_EX_alusrc_2[2]),
    .halt(\控制器_1_alusrc [3]), .halt_2(ID_EX_alusrc_2[3]), .MemWrite(\控制器_1_alusrc [4]),
    .MemWrite_2(ID_EX_alusrc_2[4]), .slt(\控制器_1_alusrc [5]), .slt_2(ID_EX_alusrc_2[5]),
    .lui(\控制器_1_alusrc [6]), .lui_2(ID_EX_alusrc_2[6]), .disp(\控制器_1_alusrc [7]), .disp_2(ID_EX_alusrc_2[7]),
    .RegDst(\控制器_1_alusrc [8]), .RegDst_2(ID_EX_alusrc_2[8]), .offset(\idecoder_指令译码器_1_immediate ),
    .offset_2(ID_EX_offset_2), .jump(\idecoder_指令译码器_1_jump_address ), .jump_2(ID_EX_jump_2),
    .\OP_操作码 (\idecoder_指令译码器_1_op ), .\OP_操作码_2 (\ID_EX_op_操作码_2 ), .PC_1(\if_id_1_pc_1_输出 ),
    .PC_1_2(ID_EX_pc_1_2), .rs(\rf_寄存器堆_1_do1 ), .rs_2(ID_EX_rs_2), .rt(\rf_寄存器堆_1_do2 ), .rt_2(ID_EX_rt_2),
    .\immediate_扩展后的立即数 (\extend_立即数符号扩展_1_extended_value_扩展结果 ),
    .\immediate_扩展后的立即数_2 (\ID_EX_immediate_扩展后的立即数_2 ), .\en_寄存器使能信号 (1'b1), .\clock_时钟信号 (clock),
    .\clear_清零信号 (clr), .\同步清空 (\branch_控制部件_1_branch_是否跳转的控制信号 ));  // open: R3R2_2, R1R0, R1R0_2, R3R2
  Hex_Digit_Display hex_digit_display_7 (.value(DISP_1[7:4]));  // open: dp
  Hex_Digit_Display hex_digit_display_8 (.value(DISP_1[3:0]));  // open: dp
  // Probe on multiplexer_3_out
  Multiplexer #(.width(16), .enable("false")) multiplexer_3 (
    .in0(ID_EX_rt_2), .in1(\ID_EX_immediate_扩展后的立即数_2 ), .out(multiplexer_3_out), .sel(ID_EX_alusrc_2[0]));
  Clock \u_时钟  (.out(CK));
  // Probe on multiplexer_5_out
  // Probe on ID_EX_instruction_2
  Multiplexer #(.width(16), .enable("false")) multiplexer_4 (
    .in0(ID_EX_rs_2), .in1(\ID_EX_immediate_扩展后的立即数_2 ), .out(multiplexer_4_out), .sel(ID_EX_alusrc_2[6]));
  Multiplexer #(.width(16), .enable("false")) multiplexer_5 (
    .in0(multiplexer_3_out), .in1(16'h8), .out(multiplexer_5_out), .sel(ID_EX_alusrc_2[6]));
  // Probe on ID_EX_aluop_2
  \IDecoder_指令译码器  \idecoder_指令译码器_2  (
    .\Instruction_指令 (ID_EX_instruction_2), .Funct(\idecoder_指令译码器_2_funct ), .OP(\idecoder_指令译码器_2_op ));  // open: P, rd, rt, rs, immediate, jump_address
  \跳转地址形成部件  \u_跳转地址形成部件_1  (
    .\Offset_条件跳转地址_8位 (ID_EX_offset_2), .\PC_1_顺序下地址 (ID_EX_pc_1_2),
    .\jump_address_无条件跳转地址_12位 (ID_EX_jump_2), .\OP_操作码_4位 (\ID_EX_op_操作码_2 ),
    .jump_address(\跳转地址形成部件_1_jump_address ));
  \Flag_取一个数的最高位  \flag_取一个数的最高位_1  (
    .\value_输入的值 (\alu16位运算器_1_输出f ), .\flag_value的最高位 (\flag_取一个数的最高位_1_flag_value的最高位 ));
  \ALU16位运算器  \alu16位运算器_1  (
    .\输入A (multiplexer_4_out), .\输入B (multiplexer_5_out), .\控制信息C (ID_EX_aluop_2), .\零 (\alu16位运算器_1_零 ),
    .\溢出 (\alu16位运算器_1_溢出 ), .\输出F (\alu16位运算器_1_输出f ));  // open: 进位
  \Branch_控制部件  \branch_控制部件_1  (
    .\OP_操作码 (\idecoder_指令译码器_2_op ), .\zero_零标志位 (\alu16位运算器_1_零 ), .\正负性 (part_1_out_3),
    .\branch_是否跳转的控制信号 (\branch_控制部件_1_branch_是否跳转的控制信号 ));
  circuit part_1 (
    .\falg_符号位 (\flag_取一个数的最高位_2_flag_value的最高位 ), .\overflow_溢出信号 (\alu16位运算器_1_溢出 ), .out_3(part_1_out_3));
  \Flag_取一个数的最高位  \flag_取一个数的最高位_2  (
    .\value_输入的值 (multiplexer_6_out), .\flag_value的最高位 (\flag_取一个数的最高位_2_flag_value的最高位 ));
  Multiplexer #(.width(16), .enable("false")) multiplexer_6 (
    .in0(\alu16位运算器_1_输出f ), .in1(slt_0_1_1_slt_0_1), .out(multiplexer_6_out), .sel(ID_EX_alusrc_2[5]));
  slt_0_1_2 slt_0_1_1 (
    .\falg_符号位 (\flag_取一个数的最高位_1_flag_value的最高位 ), .\overflow_溢出信号 (\alu16位运算器_1_溢出 ),
    .\OP_操作码 (\idecoder_指令译码器_2_op ), .\Funct_函数字段 (\idecoder_指令译码器_2_funct ), .slt_0_1(slt_0_1_1_slt_0_1));
  // Probe on ID_EX_pc_2
  // Probe on multiplexer_6_out
  EX_MEM EX_MEM (
    .PC(ID_EX_pc_2), .PC_2(EX_MEM_pc_2), .instruction(ID_EX_instruction_2),
    .instruction_2(EX_MEM_instruction_2), .ALUop(ID_EX_aluop_2), .ALUop_2(EX_MEM_aluop_2),
    .ALUSrc(ID_EX_alusrc_2[0]), .ALUSrc_2(EX_MEM_alusrc_2[0]), .RegWrite(ID_EX_alusrc_2[1]),
    .RegWrite_2(EX_MEM_alusrc_2[1]), .MemtoReg(ID_EX_alusrc_2[2]), .MemtoReg_2(EX_MEM_alusrc_2[2]),
    .halt(ID_EX_alusrc_2[3]), .halt_2(EX_MEM_alusrc_2[3]), .MemWrite(ID_EX_alusrc_2[4]),
    .MemWrite_2(EX_MEM_alusrc_2[4]), .slt(ID_EX_alusrc_2[5]), .slt_2(EX_MEM_alusrc_2[5]),
    .lui(ID_EX_alusrc_2[6]), .lui_2(EX_MEM_alusrc_2[6]), .disp(ID_EX_alusrc_2[7]),
    .disp_2(EX_MEM_alusrc_2[7]), .RegDst(ID_EX_alusrc_2[8]), .RegDst_2(EX_MEM_alusrc_2[8]),
    .\jump_address_跳转地址 (\跳转地址形成部件_1_jump_address ), .\jump_address_跳转地址_2 (\EX_MEM_jump_address_跳转地址_2 ),
    .\zero_0标志位 (\alu16位运算器_1_零 ), .\zero_0标志位_2 (\EX_MEM_zero_0标志位_2 ), .\over_溢出标志位 (\alu16位运算器_1_溢出 ),
    .\over_溢出标志位_2 (\EX_MEM_over_溢出标志位_2 ), .ALUout(multiplexer_6_out), .ALUout_2(EX_MEM_aluout_2),
    .rt(ID_EX_rt_2), .rt_2(EX_MEM_rt_2), .\en_寄存器使能信号 (1'b1), .\clock_时钟信号 (clock), .\clear_清零信号 (clr),
    .\同步清零 (1'b0));  // open: R3R2, R3R2_2, R1R0, R1R0_2
  // Probe on EX_MEM_instruction_2
  \Flag_取一个数的最高位  \flag_取一个数的最高位_3  (.\value_输入的值 (EX_MEM_aluout_2));  // open: flag_value的最高位
  // Probe on EX_MEM_pc_2
  // Probe on EX_MEM_aluout_2
  RAM #(.addrWidth(16), .dataWidth(16), .bus("separate")) ram_1 (
    .addr(EX_MEM_aluout_2), .din(EX_MEM_rt_2), .data(ram_1_data), .str(EX_MEM_alusrc_2[4]), .clk(clock),
    .ld(1'b1), .clr(clr));  // open: sel
  MEM_WB MEM_WB (
    .PC(EX_MEM_pc_2), .PC_2(MEM_WB_pc_2), .instruction(EX_MEM_instruction_2),
    .instruction_2(MEM_WB_instruction_2), .ALUop(EX_MEM_aluop_2), .ALUop_2(MEM_WB_aluop_2),
    .ALUSrc(EX_MEM_alusrc_2[0]), .ALUSrc_2(MEM_WB_alusrc_2), .RegWrite(EX_MEM_alusrc_2[1]),
    .RegWrite_2(MEM_WB_regwrite_2), .MemtoReg(EX_MEM_alusrc_2[2]), .MemtoReg_2(MEM_WB_memtoreg_2),
    .halt(EX_MEM_alusrc_2[3]), .halt_2(MEM_WB_halt_2), .MemWrite(EX_MEM_alusrc_2[4]),
    .MemWrite_2(MEM_WB_memwrite_2), .slt(EX_MEM_alusrc_2[5]), .slt_2(MEM_WB_slt_2), .lui(EX_MEM_alusrc_2[6]),
    .lui_2(MEM_WB_lui_2), .disp(EX_MEM_alusrc_2[7]), .disp_2(MEM_WB_disp_2), .RegDst(EX_MEM_alusrc_2[8]),
    .RegDst_2(MEM_WB_regdst_2), .\zero_0标志位 (\EX_MEM_zero_0标志位_2 ), .\zero_0标志位_2 (\MEM_WB_zero_0标志位_2 ),
    .\over_溢出标志位 (\EX_MEM_over_溢出标志位_2 ), .ALUout(EX_MEM_aluout_2), .ALUout_2(MEM_WB_aluout_2),
    .MemOut(ram_1_data), .MemOut_2(MEM_WB_memout_2), .\en_寄存器使能信号 (1'b1), .\clock_时钟信号 (clock),
    .\clear_清零信号 (clr), .\jump_address_跳转地址 (\EX_MEM_jump_address_跳转地址_2 ));  // open: over_溢出标志位_2, jump_address_跳转地址_2, R3R2, R3R2_2, R1R0, R1R0_2
  // Probe on MEM_WB_pc_2
  // Probe on MEM_WB_halt_2
  Multiplexer #(.width(16), .enable("false")) multiplexer_7 (
    .in0(MEM_WB_aluout_2), .in1(MEM_WB_memout_2), .out(multiplexer_7_out), .sel(MEM_WB_memtoreg_2));
  // Probe on MEM_WB_aluout_2
  // Probe on multiplexer_7_out
  // Probe on MEM_WB_instruction_2
  \IDecoder_指令译码器  \idecoder_指令译码器_3  (
    .\Instruction_指令 (MEM_WB_instruction_2), .rd(\idecoder_指令译码器_3_rd ), .rt(\idecoder_指令译码器_3_rt ), .rs(num));  // open: Funct, P, OP, immediate, jump_address
  // Probe on \idecoder_指令译码器_3_rt 

  // Other names for the same wires on the sheet: start = \为1时启动 

  // Notes on the sheet:
  //   contents of rom_1 (hex, n*v repeats v):
  //   7000 8000 7500 850f 4000 4401 9200 9700 3b02 a600 a300 85ff 21f7 b010 0 0 8001 7500 850f 21f0 c000
  //   7000 8400
endmodule

module \数据重定向  (
  input  \为1时启动 
);

  wire \alu16位运算器_1_溢出 , \alu16位运算器_1_零 , and_1_out, \branch_控制部件_1_branch_是否跳转的控制信号 , CK, clock, clr, color,
       \EX_MEM_over_溢出标志位_2 , \EX_MEM_zero_0标志位_2 , \flag_取一个数的最高位_1_flag_value的最高位 ,
       \flag_取一个数的最高位_2_flag_value的最高位 , MEM_WB_alusrc_2, MEM_WB_disp_2, MEM_WB_halt_2, MEM_WB_lui_2,
       MEM_WB_memtoreg_2, MEM_WB_memwrite_2, MEM_WB_regdst_2, MEM_WB_regwrite_2, MEM_WB_slt_2,
       \MEM_WB_zero_0标志位_2 , not_1_out, not_3_out, part_1_out_3, register_1_q, \sw_重定向_1_sw_con ,
       \sw_重定向_2_sw_con , \启停控制电路_1_f_输出时钟 , \控制器_1_regwrite ;
  wire [1:0] \idecoder_指令译码器_1_rd , \idecoder_指令译码器_1_rs , \idecoder_指令译码器_1_rt , \idecoder_指令译码器_3_rd ,
       \idecoder_指令译码器_3_rt , multiplexer_2_out, num;
  wire [2:0] \idecoder_指令译码器_1_funct , \idecoder_指令译码器_1_p , \idecoder_指令译码器_2_funct ;
  wire [3:0] EX_MEM_aluop_2, ID_EX_aluop_2, \ID_EX_op_操作码_2 , \idecoder_指令译码器_1_op , \idecoder_指令译码器_2_op ,
       MEM_WB_aluop_2, \控制器_1_aluop ;
  wire [7:0] ID_EX_offset_2, \idecoder_指令译码器_1_immediate , \idecoder_指令译码器_3_immediate ;
  wire [8:0] EX_MEM_alusrc_2, ID_EX_alusrc_2, \控制器_1_alusrc ;
  wire [11:0] counter_1_q, ID_EX_jump_2, \idecoder_指令译码器_1_jump_address ;
  wire [15:0] adder_1_out, \alu16位运算器_1_输出f , DISP_0, DISP_1, END_1, END_2, EX, \EX_MEM_jump_address_跳转地址_2 ,
       EX_MEM_pc_2, EX_MEM_rt_2, \extend_立即数符号扩展_1_extended_value_扩展结果 , \ID_EX_immediate_扩展后的立即数_2 ,
       ID_EX_pc_1_2, ID_EX_pc_2, ID_EX_rs_2, \if_id_1_instruction_指令输出 , \if_id_1_instruction_指令输出_2 ,
       \if_id_1_pc_1_输出 , if_id_1_pc_2, MEM, MEM_ALUout, MEM_MEMout, MEM_WB_aluout_2, MEM_WB_memout_2,
       MEM_WB_pc_2, multiplexer_1_out, multiplexer_3_out, multiplexer_6_out, multiplexer_7_out,
       multiplexer_8_out, orig_a, orig_b, PC_q, \rf_寄存器堆_1_do1 , rom_1_data, rt_1, rt_2, slt_0_1_1_slt_0_1,
       TO_A, TO_B, WB, WB_in, \跳转地址形成部件_1_jump_address ;
  wire [31:0] R1R0, R3R2;

  // Probe on R3R2
  // Probe on \跳转地址形成部件_1_jump_address 
  // Probe on R1R0
  // Probe on \跳转地址形成部件_1_jump_address 
  Multiplexer #(.width(16), .enable("false")) multiplexer_1 (
    .in0(adder_1_out), .in1(\跳转地址形成部件_1_jump_address ), .out(multiplexer_1_out),
    .sel(\branch_控制部件_1_branch_是否跳转的控制信号 ));
  Counter #(.width(12), .max('hfff), .trigger("falling")) counter_1 (
    .count(1'b1), .Q(counter_1_q), .clk(clock), .clr(clr));  // open: load, D, carry
  DISP u_disp_1 (
    .R3R2(R3R2), .R1R0(R1R0), .\r_num_rs__寄存器编号 (num), .\DISP_disp控制信号_用于更新寄存器的值 (MEM_WB_disp_2),
    .\disp_color_颜色选择信号 (color), .\CLK_时钟信号 (clock), .DISP_0(DISP_0), .DISP1(DISP_1), .\CLR_清零信号 (clr));
  Register #(.width(16)) PC (.D(multiplexer_1_out), .en(1'b1), .Q(PC_q), .clk(clock), .clr(clr));
  // Probe on counter_1_q
  Adder #(.width(16)) adder_1 (.a(16'h1), .b(PC_q), .out(adder_1_out), .cin(1'b0));  // open: cout
  not not_1 (not_1_out, MEM_WB_halt_2);
  // Probe on R3R2
  ROM #(.addrWidth(16), .dataWidth(16)) rom_1 (.addr(PC_q), .data(rom_1_data));  // open: sel
  not not_2 (clock, \启停控制电路_1_f_输出时钟 );
  \启停控制电路  \u_启停控制电路_1  (.\F_输出时钟 (\启停控制电路_1_f_输出时钟 ), .\时钟 (CK), .\启动_为1时启动 (and_1_out), .\重置信号 (clr));
  and and_1 (and_1_out, \为1时启动 , not_1_out);
  Button \u_重置信号  (.out(clr));
  // Probe on R1R0
  IF_ID if_id_1 (
    .PC_1(adder_1_out), .\instruction_指令 (rom_1_data), .\clock_时钟信号 (clock), .\clear_清零信号 (clr),
    .\PC_1_输出 (\if_id_1_pc_1_输出 ), .\instruction_指令输出_2 (\if_id_1_instruction_指令输出_2 ), .\en_使能信号 (1'b1),
    .PC(PC_q), .PC_2(if_id_1_pc_2), .\instruction_指令输出 (\if_id_1_instruction_指令输出 ),
    .\同步清零 (\branch_控制部件_1_branch_是否跳转的控制信号 ));
  and and_2 (\控制器_1_alusrc [1], not_3_out, \控制器_1_regwrite );
  \控制器  \u_控制器_1  (
    .\OP_操作码 (\idecoder_指令译码器_1_op ), .Funct(\idecoder_指令译码器_1_funct ), .RegDst(\控制器_1_alusrc [8]),
    .\lui_lui指令产生的单一控制信号 (\控制器_1_alusrc [6]), .MemWrite(\控制器_1_alusrc [4]), .MemtoReg(\控制器_1_alusrc [2]),
    .RegWrite(\控制器_1_regwrite ), .ALUSrc(\控制器_1_alusrc [0]), .ALUop(\控制器_1_aluop ), .disp(\控制器_1_alusrc [7]),
    .\halt_停机控制信号 (\控制器_1_alusrc [3]), .\slt_slt控制信号 (\控制器_1_alusrc [5]));
  \IDecoder_指令译码器  \idecoder_指令译码器_1  (
    .\Instruction_指令 (\if_id_1_instruction_指令输出_2 ), .Funct(\idecoder_指令译码器_1_funct ),
    .P(\idecoder_指令译码器_1_p ), .rd(\idecoder_指令译码器_1_rd ), .rt(\idecoder_指令译码器_1_rt ),
    .rs(\idecoder_指令译码器_1_rs ), .OP(\idecoder_指令译码器_1_op ), .immediate(\idecoder_指令译码器_1_immediate ),
    .jump_address(\idecoder_指令译码器_1_jump_address ));
  Hex_Digit_Display hex_digit_display_1 (.value(DISP_0[15:12]));  // open: dp
  Register #(.width(1)) register_1 (.D(1'b0), .Q(register_1_q), .clk(clock), .clr(clr));  // open: en
  Multiplexer #(.width(2), .enable("false")) multiplexer_2 (
    .in0(\idecoder_指令译码器_3_rt ), .in1(\idecoder_指令译码器_3_rd ), .out(multiplexer_2_out), .sel(MEM_WB_regdst_2));
  Hex_Digit_Display hex_digit_display_2 (.value(DISP_0[11:8]));  // open: dp
  Hex_Digit_Display hex_digit_display_3 (.value(DISP_0[7:4]));  // open: dp
  not not_3 (not_3_out, register_1_q);
  // 完全冲突检测 完全冲突检测_1: pin names not known; wires that end beside it: rom_1_data, MEM, EX, \if_id_1_instruction_指令输出 
  // Probe on \if_id_1_instruction_指令输出 
  \RF_寄存器堆  \rf_寄存器堆_1  (
    .Din(WB_in), .\CP_时钟输入 (clock), .Do1(\rf_寄存器堆_1_do1 ), .rs(\idecoder_指令译码器_1_rs ), .Do2(rt_1),
    .rt(\idecoder_指令译码器_1_rt ), .R1R0(R1R0), .R3R2(R3R2), .W(multiplexer_2_out),
    .\RegWrite_寄存器写控制信号 (MEM_WB_regwrite_2), .\ClR_清零信号 (clr));
  // Probe on WB_in
  Hex_Digit_Display hex_digit_display_4 (.value(DISP_0[3:0]));  // open: dp
  // Probe on if_id_1_pc_2
  \Extend_立即数符号扩展  \extend_立即数符号扩展_1  (
    .\immidiate_立即数 (\idecoder_指令译码器_1_immediate ), .\OP_操作码 (\idecoder_指令译码器_1_op ),
    .\Extended_value_扩展结果 (\extend_立即数符号扩展_1_extended_value_扩展结果 ));
  Hex_Digit_Display hex_digit_display_5 (.value(DISP_1[15:12]));  // open: dp
  Hex_Digit_Display hex_digit_display_6 (.value(DISP_1[11:8]));  // open: dp
  ID_EX ID_EX (
    .PC(if_id_1_pc_2), .PC_2(ID_EX_pc_2), .instruction(\if_id_1_instruction_指令输出 ), .instruction_2(EX),
    .ALUop(\控制器_1_aluop ), .ALUop_2(ID_EX_aluop_2), .ALUSrc(\控制器_1_alusrc [0]), .ALUSrc_2(ID_EX_alusrc_2[0]),
    .RegWrite(\控制器_1_alusrc [1]), .RegWrite_2(ID_EX_alusrc_2[1]), .MemtoReg(\控制器_1_alusrc [2]),
    .MemtoReg_2(ID_EX_alusrc_2[2]), .halt(\控制器_1_alusrc [3]), .halt_2(ID_EX_alusrc_2[3]),
    .MemWrite(\控制器_1_alusrc [4]), .MemWrite_2(ID_EX_alusrc_2[4]), .slt(\控制器_1_alusrc [5]),
    .slt_2(ID_EX_alusrc_2[5]), .lui(\控制器_1_alusrc [6]), .lui_2(ID_EX_alusrc_2[6]), .disp(\控制器_1_alusrc [7]),
    .disp_2(ID_EX_alusrc_2[7]), .RegDst(\控制器_1_alusrc [8]), .RegDst_2(ID_EX_alusrc_2[8]),
    .offset(\idecoder_指令译码器_1_immediate ), .offset_2(ID_EX_offset_2), .jump(\idecoder_指令译码器_1_jump_address ),
    .jump_2(ID_EX_jump_2), .\OP_操作码 (\idecoder_指令译码器_1_op ), .\OP_操作码_2 (\ID_EX_op_操作码_2 ),
    .PC_1(\if_id_1_pc_1_输出 ), .PC_1_2(ID_EX_pc_1_2), .rs(\rf_寄存器堆_1_do1 ), .rs_2(ID_EX_rs_2), .rt(rt_1),
    .rt_2(rt_2), .\immediate_扩展后的立即数 (\extend_立即数符号扩展_1_extended_value_扩展结果 ),
    .\immediate_扩展后的立即数_2 (\ID_EX_immediate_扩展后的立即数_2 ), .\en_寄存器使能信号 (1'b1), .\clock_时钟信号 (clock),
    .\clear_清零信号 (clr), .\同步清空 (\branch_控制部件_1_branch_是否跳转的控制信号 ));  // open: R3R2_2, R1R0, R1R0_2, R3R2
  Hex_Digit_Display hex_digit_display_7 (.value(DISP_1[3:0]));  // open: dp
  Hex_Digit_Display hex_digit_display_8 (.value(DISP_1[7:4]));  // open: dp
  // Probe on MEM_MEMout
  // Probe on multiplexer_3_out
  Multiplexer #(.width(16), .enable("false")) multiplexer_3 (
    .in0(rt_2), .in1(\ID_EX_immediate_扩展后的立即数_2 ), .out(multiplexer_3_out), .sel(ID_EX_alusrc_2[0]));
  Clock \u_时钟  (.out(CK));
  // Probe on orig_a
  // Probe on MEM_ALUout
  Multiplexer #(.width(16), .enable("false")) multiplexer_4 (
    .in0(ID_EX_rs_2), .in1(\ID_EX_immediate_扩展后的立即数_2 ), .out(orig_a), .sel(ID_EX_alusrc_2[6]));
  Multiplexer #(.width(16), .enable("false")) multiplexer_5 (
    .in0(multiplexer_3_out), .in1(16'h8), .out(orig_b), .sel(ID_EX_alusrc_2[6]));
  // Probe on ID_EX_aluop_2
  \Redirect_Unit_重定向单元  \redirect_unit_重定向单元_1  (
    .EX(EX), .MEM(MEM), .original_a(orig_a), .WB(WB), .Mem_ALUout(MEM_ALUout), .Mem_Memout(MEM_MEMout),
    .WB_in(WB_in), .original_b(orig_b), .TO_A(TO_A), .TO_B(TO_B));
  // Probe on orig_b
  // Probe on EX
  \跳转地址形成部件  \u_跳转地址形成部件_1  (
    .\Offset_条件跳转地址_8位 (ID_EX_offset_2), .\PC_1_顺序下地址 (ID_EX_pc_1_2),
    .\jump_address_无条件跳转地址_12位 (ID_EX_jump_2), .\OP_操作码_4位 (\ID_EX_op_操作码_2 ),
    .jump_address(\跳转地址形成部件_1_jump_address ));
  \ALU16位运算器  \alu16位运算器_1  (
    .\输入A (TO_A), .\输入B (TO_B), .\控制信息C (ID_EX_aluop_2), .\零 (\alu16位运算器_1_零 ), .\溢出 (\alu16位运算器_1_溢出 ),
    .\输出F (\alu16位运算器_1_输出f ));  // open: 进位
  // Probe on TO_A
  // Probe on TO_B
  \Branch_控制部件  \branch_控制部件_1  (
    .\OP_操作码 (\idecoder_指令译码器_2_op ), .\zero_零标志位 (\alu16位运算器_1_零 ), .\正负性 (part_1_out_3),
    .\branch_是否跳转的控制信号 (\branch_控制部件_1_branch_是否跳转的控制信号 ));
  \IDecoder_指令译码器  \idecoder_指令译码器_2  (
    .\Instruction_指令 (EX), .Funct(\idecoder_指令译码器_2_funct ), .OP(\idecoder_指令译码器_2_op ));  // open: P, rd, rt, rs, immediate, jump_address
  \Flag_取一个数的最高位  \flag_取一个数的最高位_1  (
    .\value_输入的值 (\alu16位运算器_1_输出f ), .\flag_value的最高位 (\flag_取一个数的最高位_1_flag_value的最高位 ));
  slt_0_1_2 slt_0_1_1 (
    .\falg_符号位 (\flag_取一个数的最高位_1_flag_value的最高位 ), .\overflow_溢出信号 (\alu16位运算器_1_溢出 ),
    .\OP_操作码 (\idecoder_指令译码器_2_op ), .\Funct_函数字段 (\idecoder_指令译码器_2_funct ), .slt_0_1(slt_0_1_1_slt_0_1));
  // Probe on ID_EX_pc_2
  circuit part_1 (
    .\falg_符号位 (\flag_取一个数的最高位_2_flag_value的最高位 ), .\overflow_溢出信号 (\alu16位运算器_1_溢出 ), .out_3(part_1_out_3));
  \Flag_取一个数的最高位  \flag_取一个数的最高位_2  (
    .\value_输入的值 (multiplexer_6_out), .\flag_value的最高位 (\flag_取一个数的最高位_2_flag_value的最高位 ));
  Multiplexer #(.width(16), .enable("false")) multiplexer_6 (
    .in0(\alu16位运算器_1_输出f ), .in1(slt_0_1_1_slt_0_1), .out(multiplexer_6_out), .sel(ID_EX_alusrc_2[5]));
  // Probe on multiplexer_6_out
  EX_MEM EX_MEM (
    .PC(ID_EX_pc_2), .PC_2(EX_MEM_pc_2), .instruction(EX), .instruction_2(MEM), .ALUop(ID_EX_aluop_2),
    .ALUop_2(EX_MEM_aluop_2), .ALUSrc(ID_EX_alusrc_2[0]), .ALUSrc_2(EX_MEM_alusrc_2[0]),
    .RegWrite(ID_EX_alusrc_2[1]), .RegWrite_2(EX_MEM_alusrc_2[1]), .MemtoReg(ID_EX_alusrc_2[2]),
    .MemtoReg_2(EX_MEM_alusrc_2[2]), .halt(ID_EX_alusrc_2[3]), .halt_2(EX_MEM_alusrc_2[3]),
    .MemWrite(ID_EX_alusrc_2[4]), .MemWrite_2(EX_MEM_alusrc_2[4]), .slt(ID_EX_alusrc_2[5]),
    .slt_2(EX_MEM_alusrc_2[5]), .lui(ID_EX_alusrc_2[6]), .lui_2(EX_MEM_alusrc_2[6]),
    .disp(ID_EX_alusrc_2[7]), .disp_2(EX_MEM_alusrc_2[7]), .RegDst(ID_EX_alusrc_2[8]),
    .RegDst_2(EX_MEM_alusrc_2[8]), .\jump_address_跳转地址 (\跳转地址形成部件_1_jump_address ),
    .\jump_address_跳转地址_2 (\EX_MEM_jump_address_跳转地址_2 ), .\zero_0标志位 (\alu16位运算器_1_零 ),
    .\zero_0标志位_2 (\EX_MEM_zero_0标志位_2 ), .\over_溢出标志位 (\alu16位运算器_1_溢出 ),
    .\over_溢出标志位_2 (\EX_MEM_over_溢出标志位_2 ), .ALUout(multiplexer_6_out), .ALUout_2(MEM_ALUout), .rt(rt_2),
    .rt_2(EX_MEM_rt_2), .\en_寄存器使能信号 (1'b1), .\clock_时钟信号 (clock), .\clear_清零信号 (clr), .\同步清零 (1'b0));  // open: R3R2, R3R2_2, R1R0, R1R0_2
  Multiplexer #(.width(16), .enable("false")) multiplexer_7 (
    .in0(EX_MEM_rt_2), .in1(rt_1), .out(multiplexer_7_out), .sel(\sw_重定向_1_sw_con ));
  \Flag_取一个数的最高位  \flag_取一个数的最高位_3  (.\value_输入的值 (MEM_ALUout));  // open: flag_value的最高位
  \sw_重定向  \sw_重定向_1  (.MEM(MEM), .WB(END_1), .sw_con(\sw_重定向_1_sw_con ));
  // Probe on MEM
  // Probe on MEM_ALUout
  RAM #(.addrWidth(16), .dataWidth(16), .bus("separate")) ram_1 (
    .addr(MEM_ALUout), .din(multiplexer_8_out), .data(MEM_MEMout), .str(EX_MEM_alusrc_2[4]), .clk(clock),
    .ld(1'b1), .clr(clr));  // open: sel
  // Probe on EX_MEM_pc_2
  Multiplexer #(.width(16), .enable("false")) multiplexer_8 (
    .in0(multiplexer_7_out), .in1(WB_in), .out(multiplexer_8_out), .sel(\sw_重定向_2_sw_con ));
  \sw_重定向  \sw_重定向_2  (.MEM(MEM), .WB(WB), .sw_con(\sw_重定向_2_sw_con ));
  // Probe on MEM_WB_halt_2
  MEM_WB MEM_WB (
    .PC(EX_MEM_pc_2), .PC_2(MEM_WB_pc_2), .instruction(MEM), .instruction_2(WB), .ALUop(EX_MEM_aluop_2),
    .ALUop_2(MEM_WB_aluop_2), .ALUSrc(EX_MEM_alusrc_2[0]), .ALUSrc_2(MEM_WB_alusrc_2),
    .RegWrite(EX_MEM_alusrc_2[1]), .RegWrite_2(MEM_WB_regwrite_2), .MemtoReg(EX_MEM_alusrc_2[2]),
    .MemtoReg_2(MEM_WB_memtoreg_2), .halt(EX_MEM_alusrc_2[3]), .halt_2(MEM_WB_halt_2),
    .MemWrite(EX_MEM_alusrc_2[4]), .MemWrite_2(MEM_WB_memwrite_2), .slt(EX_MEM_alusrc_2[5]),
    .slt_2(MEM_WB_slt_2), .lui(EX_MEM_alusrc_2[6]), .lui_2(MEM_WB_lui_2), .disp(EX_MEM_alusrc_2[7]),
    .disp_2(MEM_WB_disp_2), .RegDst(EX_MEM_alusrc_2[8]), .RegDst_2(MEM_WB_regdst_2),
    .\zero_0标志位 (\EX_MEM_zero_0标志位_2 ), .\zero_0标志位_2 (\MEM_WB_zero_0标志位_2 ),
    .\over_溢出标志位 (\EX_MEM_over_溢出标志位_2 ), .ALUout(MEM_ALUout), .ALUout_2(MEM_WB_aluout_2),
    .MemOut(MEM_MEMout), .MemOut_2(MEM_WB_memout_2), .\en_寄存器使能信号 (1'b1), .\clock_时钟信号 (clock),
    .\clear_清零信号 (clr), .\jump_address_跳转地址 (\EX_MEM_jump_address_跳转地址_2 ));  // open: over_溢出标志位_2, jump_address_跳转地址_2, R3R2, R3R2_2, R1R0, R1R0_2
  // Probe on MEM_WB_aluout_2
  // Probe on MEM_WB_pc_2
  Multiplexer #(.width(16), .enable("false")) multiplexer_9 (
    .in0(MEM_WB_aluout_2), .in1(MEM_WB_memout_2), .out(WB_in), .sel(MEM_WB_memtoreg_2));
  // Probe on WB_in
  // Probe on WB
  Bit_Extender #(.out_width(1)) bit_extender_1 (.in(\idecoder_指令译码器_3_immediate ), .out(color));
  \IDecoder_指令译码器  \idecoder_指令译码器_3  (
    .\Instruction_指令 (WB), .rd(\idecoder_指令译码器_3_rd ), .rt(\idecoder_指令译码器_3_rt ), .rs(num),
    .immediate(\idecoder_指令译码器_3_immediate ));  // open: Funct, P, OP, jump_address
  // Probe on \idecoder_指令译码器_3_rt 
  Register #(.width(16)) register_2 (.D(WB), .Q(END_1), .clk(clock), .clr(clr));  // open: en
  Register #(.width(16)) register_3 (.D(END_1), .Q(END_2), .clk(clock), .clr(clr));  // open: en

  // Other names for the same wires on the sheet: start = \为1时启动 

  // Notes on the sheet:
  //   contents of rom_1 (hex, n*v repeats v):
  //   7000 8001 7500 8501 7f00 8f01 4400 4c01 444 4400 dc2 4c01 487 1801 b008 7000 8001 7500 850f 443 442
  //   1c4 4c00 7500 8503 dc6 4c00 7500 8504 dc6 4c00 dc6 4c00 dc6 4c00 7000 8001 7500 850f 1c4 dc6 7000
  //   8000 7500 8504 520c 985 985 8001 700f dc4 cc0 4c00 dc4 cc0 4c00 dc4 cc0 4c00 dc4 cc0 4c00 8001 700f
  //   204 dc5 cc0 4c00 dc5 cc0 4c00 dc5 cc0 4c00 dc5 cc0 4c00 205 22e1 7000 8000 7500 850f 4000 4401 9200
  //   9700 3b02 a600 a300 85ff 21f7 b05f 0 0 8001 7500 850f 21f0 c000 7000 8400
endmodule

// Redrect_unit
module \Redirect_Unit_重定向单元  (
  input  [15:0] EX,
  input  [15:0] MEM,
  input  [15:0] original_a,
  input  [15:0] WB,
  input  [15:0] Mem_ALUout,
  input  [15:0] Mem_Memout,
  input  [15:0] WB_in,
  input  [15:0] original_b,
  output [15:0] TO_A,
  output [15:0] TO_B
);

  wire and_2_out, and_3_out, comparator_1_eq, comparator_2_eq, comparator_9_eq, comparator_10_eq,
       comparator_11_eq, comparator_12_eq, con_ex_mem, con_ex_wb, has_rt_out, MEM_wb__rs, MEM_wb__rt,
       MEM_wb__WB_wb, OP_9, Wb_wb__rs, Wb_wb__rt;
  wire [1:0] choose_a, choose_b, \idecoder_指令译码器_1_rd , \idecoder_指令译码器_1_rt , \idecoder_指令译码器_2_rd ,
       \idecoder_指令译码器_2_rt , \idecoder_指令译码器_4_rs , \idecoder_指令译码器_4_rt , multiplexer_1_out,
       multiplexer_2_out;
  wire [3:0] \idecoder_指令译码器_1_op , \idecoder_指令译码器_2_op , \idecoder_指令译码器_3_op , \idecoder_指令译码器_5_op ;

  \IDecoder_指令译码器  \idecoder_指令译码器_1  (
    .\Instruction_指令 (MEM), .rd(\idecoder_指令译码器_1_rd ), .rt(\idecoder_指令译码器_1_rt ), .OP(\idecoder_指令译码器_1_op ));  // open: Funct, P, rs, immediate, jump_address
  \IDecoder_指令译码器  \idecoder_指令译码器_2  (
    .\Instruction_指令 (WB), .rd(\idecoder_指令译码器_2_rd ), .rt(\idecoder_指令译码器_2_rt ), .OP(\idecoder_指令译码器_2_op ));  // open: Funct, P, rs, immediate, jump_address
  // AND_Gate and_1 is placed but not wired
  Multiplexer #(.width(2), .enable("false")) multiplexer_1 (
    .in0(\idecoder_指令译码器_1_rt ), .in1(\idecoder_指令译码器_1_rd ), .out(multiplexer_1_out), .sel(comparator_1_eq));
  Comparator #(.width(4)) comparator_1 (.a(\idecoder_指令译码器_1_op ), .b(4'b0000), .eq(comparator_1_eq));  // open: gt, lt
  Multiplexer #(.width(2), .enable("false")) multiplexer_2 (
    .in0(\idecoder_指令译码器_2_rt ), .in1(\idecoder_指令译码器_2_rd ), .out(multiplexer_2_out), .sel(comparator_2_eq));
  Comparator #(.width(4)) comparator_2 (.a(\idecoder_指令译码器_2_op ), .b(4'b0000), .eq(comparator_2_eq));  // open: gt, lt
  \conflict_冲突检测  \conflict_冲突检测_1  (
    .\instruction_0_当前指令 (MEM), .\instruction_1_下一条指令 (EX), .\conflict_为1时候冲突 (con_ex_mem));  // open: data_数据冲突, branch_分支冲突
  \IDecoder_指令译码器  \idecoder_指令译码器_3  (
    .\Instruction_指令 (MEM), .OP(\idecoder_指令译码器_3_op ));  // open: Funct, P, rd, rt, rs, immediate, jump_address
  \conflict_冲突检测  \conflict_冲突检测_2  (
    .\instruction_0_当前指令 (WB), .\instruction_1_下一条指令 (EX), .\conflict_为1时候冲突 (con_ex_wb));  // open: data_数据冲突, branch_分支冲突
  \IDecoder_指令译码器  \idecoder_指令译码器_4  (
    .\Instruction_指令 (EX), .rt(\idecoder_指令译码器_4_rt ), .rs(\idecoder_指令译码器_4_rs ));  // open: Funct, P, rd, OP, immediate, jump_address
  Comparator #(.width(4)) comparator_3 (.a(\idecoder_指令译码器_3_op ), .b(4'b1001), .eq(OP_9));  // open: gt, lt
  Comparator #(.width(2)) comparator_4 (
    .a(multiplexer_1_out), .b(\idecoder_指令译码器_4_rs ), .eq(MEM_wb__rs));  // open: gt, lt
  Comparator #(.width(2)) comparator_5 (
    .a(\idecoder_指令译码器_4_rs ), .b(multiplexer_2_out), .eq(Wb_wb__rs));  // open: gt, lt
  Comparator #(.width(2)) comparator_6 (
    .a(multiplexer_1_out), .b(\idecoder_指令译码器_4_rt ), .eq(MEM_wb__rt));  // open: gt, lt
  Comparator #(.width(2)) comparator_7 (
    .a(\idecoder_指令译码器_4_rt ), .b(multiplexer_2_out), .eq(Wb_wb__rt));  // open: gt, lt
  Comparator #(.width(2)) comparator_8 (
    .a(multiplexer_1_out), .b(multiplexer_2_out), .eq(MEM_wb__WB_wb));  // open: gt, lt
  \IDecoder_指令译码器  \idecoder_指令译码器_5  (
    .\Instruction_指令 (EX), .OP(\idecoder_指令译码器_5_op ));  // open: Funct, P, rd, rt, rs, immediate, jump_address
  Comparator #(.width(4)) comparator_9 (.a(\idecoder_指令译码器_5_op ), .b(4'b0000), .eq(comparator_9_eq));  // open: gt, lt
  Comparator #(.width(4)) comparator_10 (
    .a(\idecoder_指令译码器_5_op ), .b(4'b0001), .eq(comparator_10_eq));  // open: gt, lt
  Comparator #(.width(4)) comparator_11 (
    .a(\idecoder_指令译码器_5_op ), .b(4'b0010), .eq(comparator_11_eq));  // open: gt, lt
  Comparator #(.width(4)) comparator_12 (
    .a(\idecoder_指令译码器_5_op ), .b(4'b0011), .eq(comparator_12_eq));  // open: gt, lt
  or has_rt (has_rt_out, comparator_9_eq, comparator_10_eq, comparator_11_eq, comparator_12_eq);
  and and_2 (and_2_out, MEM_wb__rt, has_rt_out);
  and and_3 (and_3_out, Wb_wb__rt, has_rt_out);
  Choose_A choose_a_1 (
    .ex_mem_conf(con_ex_mem), .ex_wb_conf(con_ex_wb), .op_9(OP_9), .MEM_wb__WB_wb(MEM_wb__WB_wb),
    .MEM_wb__rs(MEM_wb__rs), .WB_wb__rs(Wb_wb__rs), .choose_A(choose_a));
  Choose_A choose_a_2 (
    .ex_mem_conf(con_ex_mem), .ex_wb_conf(con_ex_wb), .op_9(OP_9), .MEM_wb__WB_wb(MEM_wb__WB_wb),
    .MEM_wb__rs(and_2_out), .WB_wb__rs(and_3_out), .choose_A(choose_b));
  Multiplexer #(.select(2), .width(16), .enable("false")) multiplexer_3 (
    .in0(original_a), .in1(Mem_ALUout), .in2(Mem_Memout), .in3(WB_in), .out(TO_A), .sel(choose_a));
  Multiplexer #(.select(2), .width(16), .enable("false")) multiplexer_4 (
    .in0(original_b), .in1(Mem_ALUout), .in2(Mem_Memout), .in3(WB_in), .out(TO_B), .sel(choose_b));

  // Other names for the same wires on the sheet: the_EX[15:0] = EX
endmodule

module choose_a (
  input  ex_mem_conf,
  input  ex_wb_conf,
  input  op_9,
  input  eq_wb_rs,
  output choose_a_1,
  output choose_a_0
);

  wire and_1_out, and_2_out, and_3_out, and_4_out, not_1_out, not_2_out, not_3_out;

  not not_1 (not_1_out, ex_mem_conf);
  and and_1 (and_1_out, not_1_out, ex_wb_conf, eq_wb_rs);
  and and_2 (and_2_out, ex_mem_conf, op_9, eq_wb_rs);
  not not_2 (not_2_out, ex_mem_conf);
  and and_3 (and_3_out, not_2_out, ex_wb_conf, eq_wb_rs);
  and and_4 (and_4_out, ex_mem_conf, not_3_out, eq_wb_rs);
  not not_3 (not_3_out, op_9);
  or or_1 (choose_a_1, and_1_out, and_2_out);
  or or_2 (choose_a_0, and_3_out, and_4_out);
endmodule

module choose_b (
  input  ex_mem_conf,
  input  ex_wb_conf,
  input  op_9,
  input  eq_wb_rt,
  output choose_a_1,
  output choose_a_0
);

  wire and_1_out, and_2_out, and_3_out, and_4_out, not_1_out, not_2_out, not_3_out;

  not not_1 (not_1_out, ex_mem_conf);
  and and_1 (and_1_out, not_1_out, ex_wb_conf, eq_wb_rt);
  and and_2 (and_2_out, ex_mem_conf, op_9, eq_wb_rt);
  not not_2 (not_2_out, ex_mem_conf);
  and and_3 (and_3_out, not_2_out, ex_wb_conf, eq_wb_rt);
  not not_3 (not_3_out, op_9);
  and and_4 (and_4_out, ex_mem_conf, not_3_out, eq_wb_rt);
  or or_1 (choose_a_1, and_1_out, and_2_out);
  or or_2 (choose_a_0, and_3_out, and_4_out);
endmodule

module Choose_A (
  input  ex_mem_conf,
  input  ex_wb_conf,
  input  op_9,
  input  MEM_wb__WB_wb,
  input  MEM_wb__rs,
  input  WB_wb__rs,
  output [1:0] choose_A
);

  wire comparator_6_eq, comparator_7_eq, comparator_25_eq, MEM_alu_out, MEM_Mem_out, WB_out;
  wire [5:0] comparator_1_eq;
  wire [6:0] comparator_8_eq;
  wire [9:0] comparator_15_eq;

  Comparator #(.width(6)) comparator_1 (
    .a({ex_mem_conf, ex_wb_conf, op_9, MEM_wb__WB_wb, MEM_wb__rs, WB_wb__rs}), .b(6'b100010),
    .eq(comparator_1_eq[0]));  // open: gt, lt
  Comparator #(.width(6)) comparator_2 (
    .a({ex_mem_conf, ex_wb_conf, op_9, MEM_wb__WB_wb, MEM_wb__rs, WB_wb__rs}), .b(6'b100011),
    .eq(comparator_1_eq[1]));  // open: gt, lt
  Comparator #(.width(6)) comparator_3 (
    .a({ex_mem_conf, ex_wb_conf, op_9, MEM_wb__WB_wb, MEM_wb__rs, WB_wb__rs}), .b(6'b100110),
    .eq(comparator_1_eq[2]));  // open: gt, lt
  Comparator #(.width(6)) comparator_4 (
    .a({ex_mem_conf, ex_wb_conf, op_9, MEM_wb__WB_wb, MEM_wb__rs, WB_wb__rs}), .b(6'b100111),
    .eq(comparator_1_eq[3]));  // open: gt, lt
  Comparator #(.width(6)) comparator_5 (
    .a({ex_mem_conf, ex_wb_conf, op_9, MEM_wb__WB_wb, MEM_wb__rs, WB_wb__rs}), .b(6'b110110),
    .eq(comparator_1_eq[4]));  // open: gt, lt
  Comparator #(.width(6)) comparator_6 (
    .a({ex_mem_conf, ex_wb_conf, op_9, MEM_wb__WB_wb, MEM_wb__rs, WB_wb__rs}), .b(6'b110111),
    .eq(comparator_6_eq));  // open: gt, lt
  Comparator #(.width(6)) comparator_7 (
    .a({ex_mem_conf, ex_wb_conf, op_9, MEM_wb__WB_wb, MEM_wb__rs, WB_wb__rs}), .b(6'b110010),
    .eq(comparator_7_eq));  // open: gt, lt
  Comparator #(.width(6)) comparator_8 (
    .a({ex_mem_conf, ex_wb_conf, op_9, MEM_wb__WB_wb, MEM_wb__rs, WB_wb__rs}), .b(6'b101010),
    .eq(comparator_8_eq[0]));  // open: gt, lt
  Comparator #(.width(6)) comparator_9 (
    .a({ex_mem_conf, ex_wb_conf, op_9, MEM_wb__WB_wb, MEM_wb__rs, WB_wb__rs}), .b(6'b101011),
    .eq(comparator_8_eq[1]));  // open: gt, lt
  Comparator #(.width(6)) comparator_10 (
    .a({ex_mem_conf, ex_wb_conf, op_9, MEM_wb__WB_wb, MEM_wb__rs, WB_wb__rs}), .b(6'b101100),
    .eq(comparator_8_eq[2]));  // open: gt, lt
  Comparator #(.width(6)) comparator_11 (
    .a({ex_mem_conf, ex_wb_conf, op_9, MEM_wb__WB_wb, MEM_wb__rs, WB_wb__rs}), .b(6'b101101),
    .eq(comparator_8_eq[3]));  // open: gt, lt
  Comparator #(.width(6)) comparator_12 (
    .a({ex_mem_conf, ex_wb_conf, op_9, MEM_wb__WB_wb, MEM_wb__rs, WB_wb__rs}), .b(6'b111010),
    .eq(comparator_8_eq[4]));  // open: gt, lt
  Comparator #(.width(6)) comparator_13 (
    .a({ex_mem_conf, ex_wb_conf, op_9, MEM_wb__WB_wb, MEM_wb__rs, WB_wb__rs}), .b(6'b111110),
    .eq(comparator_8_eq[5]));  // open: gt, lt
  Comparator #(.width(6)) comparator_14 (
    .a({ex_mem_conf, ex_wb_conf, op_9, MEM_wb__WB_wb, MEM_wb__rs, WB_wb__rs}), .b({6{1'b1}}),
    .eq(comparator_8_eq[6]));  // open: gt, lt
  Comparator #(.width(6)) comparator_15 (
    .a({ex_mem_conf, ex_wb_conf, op_9, MEM_wb__WB_wb, MEM_wb__rs, WB_wb__rs}), .b(6'b010001),
    .eq(comparator_15_eq[0]));  // open: gt, lt
  Comparator #(.width(6)) comparator_16 (
    .a({ex_mem_conf, ex_wb_conf, op_9, MEM_wb__WB_wb, MEM_wb__rs, WB_wb__rs}), .b(6'b010011),
    .eq(comparator_15_eq[1]));  // open: gt, lt
  Comparator #(.width(6)) comparator_17 (
    .a({ex_mem_conf, ex_wb_conf, op_9, MEM_wb__WB_wb, MEM_wb__rs, WB_wb__rs}), .b(6'b010101),
    .eq(comparator_15_eq[2]));  // open: gt, lt
  Comparator #(.width(6)) comparator_18 (
    .a({ex_mem_conf, ex_wb_conf, op_9, MEM_wb__WB_wb, MEM_wb__rs, WB_wb__rs}), .b(6'b010111),
    .eq(comparator_15_eq[3]));  // open: gt, lt
  Comparator #(.width(6)) comparator_19 (
    .a({ex_mem_conf, ex_wb_conf, op_9, MEM_wb__WB_wb, MEM_wb__rs, WB_wb__rs}), .b(6'b011001),
    .eq(comparator_15_eq[4]));  // open: gt, lt
  Comparator #(.width(6)) comparator_20 (
    .a({ex_mem_conf, ex_wb_conf, op_9, MEM_wb__WB_wb, MEM_wb__rs, WB_wb__rs}), .b(6'b011011),
    .eq(comparator_15_eq[5]));  // open: gt, lt
  Comparator #(.width(6)) comparator_21 (
    .a({ex_mem_conf, ex_wb_conf, op_9, MEM_wb__WB_wb, MEM_wb__rs, WB_wb__rs}), .b(6'b011110),
    .eq(comparator_15_eq[6]));  // open: gt, lt
  Comparator #(.width(6)) comparator_22 (
    .a({ex_mem_conf, ex_wb_conf, op_9, MEM_wb__WB_wb, MEM_wb__rs, WB_wb__rs}), .b(6'b011111),
    .eq(comparator_15_eq[7]));  // open: gt, lt
  Comparator #(.width(6)) comparator_23 (
    .a({ex_mem_conf, ex_wb_conf, op_9, MEM_wb__WB_wb, MEM_wb__rs, WB_wb__rs}), .b(6'b110001),
    .eq(comparator_15_eq[8]));  // open: gt, lt
  Comparator #(.width(6)) comparator_24 (
    .a({ex_mem_conf, ex_wb_conf, op_9, MEM_wb__WB_wb, MEM_wb__rs, WB_wb__rs}), .b(6'b111001),
    .eq(comparator_15_eq[9]));  // open: gt, lt
  or or_1 (comparator_1_eq[5], comparator_6_eq, comparator_7_eq);
  or u_MEM_alu_out (MEM_alu_out, comparator_1_eq[0], comparator_1_eq[1], comparator_1_eq[2], comparator_1_eq[3], comparator_1_eq[4], comparator_1_eq[5]);
  or u_MEM_Mem_out (MEM_Mem_out, comparator_8_eq[0], comparator_8_eq[1], comparator_8_eq[2], comparator_8_eq[3], comparator_8_eq[4], comparator_8_eq[5], comparator_8_eq[6]);
  or u_WB_out (WB_out, comparator_15_eq[0], comparator_15_eq[1], comparator_15_eq[2], comparator_15_eq[3], comparator_15_eq[4], comparator_15_eq[5], comparator_15_eq[6], comparator_15_eq[7], comparator_15_eq[8], comparator_15_eq[9]);
  Comparator #(.width(3)) comparator_25 (
    .a({WB_out, MEM_Mem_out, MEM_alu_out}), .b(3'b000), .eq(comparator_25_eq));  // open: gt, lt
  Priority_Encoder #(.select(2)) priority_encoder_1 (
    .in0(comparator_25_eq), .in1(MEM_alu_out), .in2(MEM_Mem_out), .in3(WB_out), .out(choose_A), .en_in(1'b1));  // open: gs, en_out
endmodule

module Choose_B (
  input  ex_mem_conf,
  input  ex_wb_conf,
  input  op_9,
  input  MEM_wb__WB_wb,
  input  MEM_wb__rt,
  input  WB_wb__rt,
  input  EX_has_rt,
  output [1:0] choose_A
);

  wire comparator_23_eq, MEM_alu_out, MEM_Mem_out, WB_out;
  wire [5:0] comparator_1_eq, comparator_7_eq;
  wire [5:4] and_1_out;
  wire [9:0] comparator_13_eq;

  and and_1 (and_1_out[4], MEM_wb__rt, EX_has_rt);
  and and_2 (and_1_out[5], WB_wb__rt, EX_has_rt);
  Comparator #(.width(6)) comparator_1 (
    .a({and_1_out, MEM_wb__WB_wb, op_9, ex_wb_conf, ex_mem_conf}), .b(6'b100010), .eq(comparator_1_eq[0]));  // open: gt, lt
  Comparator #(.width(6)) comparator_2 (
    .a({and_1_out, MEM_wb__WB_wb, op_9, ex_wb_conf, ex_mem_conf}), .b(6'b100011), .eq(comparator_1_eq[1]));  // open: gt, lt
  Comparator #(.width(6)) comparator_3 (
    .a({and_1_out, MEM_wb__WB_wb, op_9, ex_wb_conf, ex_mem_conf}), .b(6'b100110), .eq(comparator_1_eq[2]));  // open: gt, lt
  Comparator #(.width(6)) comparator_4 (
    .a({and_1_out, MEM_wb__WB_wb, op_9, ex_wb_conf, ex_mem_conf}), .b(6'b100111), .eq(comparator_1_eq[3]));  // open: gt, lt
  Comparator #(.width(6)) comparator_5 (
    .a({and_1_out, MEM_wb__WB_wb, op_9, ex_wb_conf, ex_mem_conf}), .b(6'b110110), .eq(comparator_1_eq[4]));  // open: gt, lt
  Comparator #(.width(6)) comparator_6 (
    .a({and_1_out, MEM_wb__WB_wb, op_9, ex_wb_conf, ex_mem_conf}), .b(6'b110111), .eq(comparator_1_eq[5]));  // open: gt, lt
  Comparator #(.width(6)) comparator_7 (
    .a({and_1_out, MEM_wb__WB_wb, op_9, ex_wb_conf, ex_mem_conf}), .b(6'b101010), .eq(comparator_7_eq[0]));  // open: gt, lt
  Comparator #(.width(6)) comparator_8 (
    .a({and_1_out, MEM_wb__WB_wb, op_9, ex_wb_conf, ex_mem_conf}), .b(6'b101011), .eq(comparator_7_eq[1]));  // open: gt, lt
  Comparator #(.width(6)) comparator_9 (
    .a({and_1_out, MEM_wb__WB_wb, op_9, ex_wb_conf, ex_mem_conf}), .b(6'b101100), .eq(comparator_7_eq[2]));  // open: gt, lt
  Comparator #(.width(6)) comparator_10 (
    .a({and_1_out, MEM_wb__WB_wb, op_9, ex_wb_conf, ex_mem_conf}), .b(6'b101101), .eq(comparator_7_eq[3]));  // open: gt, lt
  Comparator #(.width(6)) comparator_11 (
    .a({and_1_out, MEM_wb__WB_wb, op_9, ex_wb_conf, ex_mem_conf}), .b(6'b111110), .eq(comparator_7_eq[4]));  // open: gt, lt
  Comparator #(.width(6)) comparator_12 (
    .a({and_1_out, MEM_wb__WB_wb, op_9, ex_wb_conf, ex_mem_conf}), .b({6{1'b1}}), .eq(comparator_7_eq[5]));  // open: gt, lt
  Comparator #(.width(6)) comparator_13 (
    .a({and_1_out, MEM_wb__WB_wb, op_9, ex_wb_conf, ex_mem_conf}), .b(6'b010001), .eq(comparator_13_eq[0]));  // open: gt, lt
  Comparator #(.width(6)) comparator_14 (
    .a({and_1_out, MEM_wb__WB_wb, op_9, ex_wb_conf, ex_mem_conf}), .b(6'b010011), .eq(comparator_13_eq[1]));  // open: gt, lt
  Comparator #(.width(6)) comparator_15 (
    .a({and_1_out, MEM_wb__WB_wb, op_9, ex_wb_conf, ex_mem_conf}), .b(6'b010101), .eq(comparator_13_eq[2]));  // open: gt, lt
  Comparator #(.width(6)) comparator_16 (
    .a({and_1_out, MEM_wb__WB_wb, op_9, ex_wb_conf, ex_mem_conf}), .b(6'b010111), .eq(comparator_13_eq[3]));  // open: gt, lt
  Comparator #(.width(6)) comparator_17 (
    .a({and_1_out, MEM_wb__WB_wb, op_9, ex_wb_conf, ex_mem_conf}), .b(6'b011001), .eq(comparator_13_eq[4]));  // open: gt, lt
  Comparator #(.width(6)) comparator_18 (
    .a({and_1_out, MEM_wb__WB_wb, op_9, ex_wb_conf, ex_mem_conf}), .b(6'b011011), .eq(comparator_13_eq[5]));  // open: gt, lt
  Comparator #(.width(6)) comparator_19 (
    .a({and_1_out, MEM_wb__WB_wb, op_9, ex_wb_conf, ex_mem_conf}), .b(6'b011110), .eq(comparator_13_eq[6]));  // open: gt, lt
  Comparator #(.width(6)) comparator_20 (
    .a({and_1_out, MEM_wb__WB_wb, op_9, ex_wb_conf, ex_mem_conf}), .b(6'b011111), .eq(comparator_13_eq[7]));  // open: gt, lt
  Comparator #(.width(6)) comparator_21 (
    .a({and_1_out, MEM_wb__WB_wb, op_9, ex_wb_conf, ex_mem_conf}), .b(6'b110001), .eq(comparator_13_eq[8]));  // open: gt, lt
  Comparator #(.width(6)) comparator_22 (
    .a({and_1_out, MEM_wb__WB_wb, op_9, ex_wb_conf, ex_mem_conf}), .b(6'b111001), .eq(comparator_13_eq[9]));  // open: gt, lt
  or u_MEM_alu_out (MEM_alu_out, comparator_1_eq[0], comparator_1_eq[1], comparator_1_eq[2], comparator_1_eq[3], comparator_1_eq[4], comparator_1_eq[5]);
  or u_MEM_Mem_out (MEM_Mem_out, comparator_7_eq[0], comparator_7_eq[1], comparator_7_eq[2], comparator_7_eq[3], comparator_7_eq[4], comparator_7_eq[5]);
  or u_WB_out (WB_out, comparator_13_eq[0], comparator_13_eq[1], comparator_13_eq[2], comparator_13_eq[3], comparator_13_eq[4], comparator_13_eq[5], comparator_13_eq[6], comparator_13_eq[7], comparator_13_eq[8], comparator_13_eq[9]);
  Comparator #(.width(3)) comparator_23 (
    .a({WB_out, MEM_Mem_out, MEM_alu_out}), .b(3'b000), .eq(comparator_23_eq));  // open: gt, lt
  Priority_Encoder #(.select(2)) priority_encoder_1 (
    .in0(comparator_23_eq), .in1(MEM_alu_out), .in2(MEM_Mem_out), .in3(WB_out), .out(choose_A), .en_in(1'b1));  // open: gs, en_out
endmodule

// sw-con
module \sw_重定向  (
  input  [15:0] MEM,
  input  [15:0] WB,
  output sw_con
);

  wire comparator_1_eq, comparator_2_eq, comparator_3_eq, comparator_4_eq, comparator_5_eq, comparator_6_eq,
       comparator_7_eq, comparator_8_eq, or_1_out;
  wire [1:0] \idecoder_指令译码器_1_rt , \idecoder_指令译码器_2_rd , \idecoder_指令译码器_2_rt , multiplexer_1_out;
  wire [3:0] \idecoder_指令译码器_1_op , \idecoder_指令译码器_2_op ;

  \IDecoder_指令译码器  \idecoder_指令译码器_1  (
    .\Instruction_指令 (MEM), .rt(\idecoder_指令译码器_1_rt ), .OP(\idecoder_指令译码器_1_op ));  // open: Funct, P, rd, rs, immediate, jump_address
  \IDecoder_指令译码器  \idecoder_指令译码器_2  (
    .\Instruction_指令 (WB), .rd(\idecoder_指令译码器_2_rd ), .rt(\idecoder_指令译码器_2_rt ), .OP(\idecoder_指令译码器_2_op ));  // open: Funct, P, rs, immediate, jump_address
  Comparator #(.width(4)) comparator_1 (.a(\idecoder_指令译码器_1_op ), .b(4'b1010), .eq(comparator_1_eq));  // open: gt, lt
  Multiplexer #(.width(2), .enable("false")) multiplexer_1 (
    .in0(\idecoder_指令译码器_2_rt ), .in1(\idecoder_指令译码器_2_rd ), .out(multiplexer_1_out), .sel(comparator_2_eq));
  Comparator #(.width(4)) comparator_2 (.a(\idecoder_指令译码器_2_op ), .b(4'b0000), .eq(comparator_2_eq));  // open: gt, lt
  Comparator #(.width(4)) comparator_3 (.a(\idecoder_指令译码器_2_op ), .b(4'b0101), .eq(comparator_3_eq));  // open: gt, lt
  Comparator #(.width(4)) comparator_4 (.a(\idecoder_指令译码器_2_op ), .b(4'b0110), .eq(comparator_4_eq));  // open: gt, lt
  Comparator #(.width(4)) comparator_5 (.a(\idecoder_指令译码器_2_op ), .b(4'b0111), .eq(comparator_5_eq));  // open: gt, lt
  Comparator #(.width(4)) comparator_6 (.a(\idecoder_指令译码器_2_op ), .b(4'b1000), .eq(comparator_6_eq));  // open: gt, lt
  Comparator #(.width(4)) comparator_7 (.a(\idecoder_指令译码器_2_op ), .b(4'b1001), .eq(comparator_7_eq));  // open: gt, lt
  Comparator #(.width(2)) comparator_8 (
    .a(\idecoder_指令译码器_1_rt ), .b(multiplexer_1_out), .eq(comparator_8_eq));  // open: gt, lt
  or or_1 (or_1_out, comparator_2_eq, comparator_3_eq, comparator_4_eq, comparator_5_eq, comparator_6_eq, comparator_7_eq);
  and and_1 (sw_con, comparator_8_eq, comparator_1_eq, or_1_out);
endmodule

module \分支预测  (
  input  \为1时启动 
);

  wire \alu16位运算器_1_溢出 , \alu16位运算器_1_零 , and_1_out, \branch_控制部件_1_branch_是否跳转的控制信号 , CK, clock, clr, color,
       \EX_MEM_over_溢出标志位_2 , \EX_MEM_zero_0标志位_2 , \flag_取一个数的最高位_1_flag_value的最高位 ,
       \flag_取一个数的最高位_2_flag_value的最高位 , MEM_WB_alusrc_2, MEM_WB_disp_2, MEM_WB_halt_2, MEM_WB_lui_2,
       MEM_WB_memtoreg_2, MEM_WB_memwrite_2, MEM_WB_regdst_2, MEM_WB_regwrite_2, MEM_WB_slt_2,
       \MEM_WB_zero_0标志位_2 , not_1_out, \sw_重定向_1_sw_con , \sw_重定向_2_sw_con , undriven, \启停控制电路_1_f_输出时钟 ;
  wire [1:0] \idecoder_指令译码器_1_rd , \idecoder_指令译码器_1_rs , \idecoder_指令译码器_1_rt , \idecoder_指令译码器_3_rd ,
       \idecoder_指令译码器_3_rt , multiplexer_2_out, num;
  wire [2:0] \idecoder_指令译码器_1_funct , \idecoder_指令译码器_2_funct ;
  wire [3:0] EX_MEM_aluop_2, ID_EX_aluop_2, \ID_EX_op_操作码_2 , \idecoder_指令译码器_1_op , \idecoder_指令译码器_2_op ,
       MEM_WB_aluop_2, \控制器_1_aluop ;
  wire [7:0] ID_EX_offset_2, \idecoder_指令译码器_1_immediate , \idecoder_指令译码器_3_immediate ;
  wire [8:0] EX_MEM_alusrc_2, ID_EX_alusrc_2, \控制器_1_alusrc ;
  wire [11:0] counter_1_q, ID_EX_jump_2, \idecoder_指令译码器_1_jump_address , undriven_2;
  wire [15:0] adder_1_out, \alu16位运算器_1_输出f , DISP_0, DISP_1, END_1, END_2, EX, \EX_MEM_jump_address_跳转地址_2 ,
       EX_MEM_pc_2, EX_MEM_rt_2, \extend_立即数符号扩展_1_extended_value_扩展结果 , \ID_EX_immediate_扩展后的立即数_2 ,
       ID_EX_pc_1_2, ID_EX_pc_2, ID_EX_rs_2, \if_id_1_instruction_指令输出 , \if_id_1_instruction_指令输出_2 ,
       \if_id_1_pc_1_输出 , if_id_1_pc_2, MEM, MEM_ALUout, MEM_MEMout, MEM_WB_aluout_2, MEM_WB_memout_2,
       MEM_WB_pc_2, multiplexer_1_out, multiplexer_3_out, multiplexer_6_out, multiplexer_7_out,
       multiplexer_8_out, orig_a, orig_b, PC_q, \rf_寄存器堆_1_do1 , rom_1_data, rt_1, rt_2, slt_0_1_1_slt_0_1,
       TO_A, TO_B, WB, WB_in, \跳转地址形成部件_1_jump_address ;
  wire [31:0] R1R0, R3R2;

  // Probe on R3R2
  // Probe on \跳转地址形成部件_1_jump_address 
  // Probe on R1R0
  // Probe on \跳转地址形成部件_1_jump_address 
  Multiplexer #(.width(16), .enable("false")) multiplexer_1 (
    .in0(adder_1_out), .in1(\跳转地址形成部件_1_jump_address ), .out(multiplexer_1_out), .sel(undriven));
  Counter #(.width(12), .max('hfff), .trigger("falling")) counter_1 (
    .count(1'b1), .Q(counter_1_q), .clk(clock), .clr(clr));  // open: load, D, carry
  DISP u_disp_1 (
    .R3R2(R3R2), .R1R0(R1R0), .\r_num_rs__寄存器编号 (num), .\DISP_disp控制信号_用于更新寄存器的值 (MEM_WB_disp_2),
    .\disp_color_颜色选择信号 (color), .\CLK_时钟信号 (clock), .DISP_0(DISP_0), .DISP1(DISP_1), .\CLR_清零信号 (clr));
  Register #(.width(16)) PC (.D(multiplexer_1_out), .en(1'b1), .Q(PC_q), .clk(clock), .clr(clr));
  // Probe on counter_1_q
  Adder #(.width(16)) adder_1 (.a(16'h1), .b(PC_q), .out(adder_1_out), .cin(1'b0));  // open: cout
  not not_1 (not_1_out, MEM_WB_halt_2);
  // Probe on R3R2
  ROM #(.addrWidth(16), .dataWidth(16)) rom_1 (.addr(PC_q), .data(rom_1_data));  // open: sel
  not not_2 (clock, \启停控制电路_1_f_输出时钟 );
  \启停控制电路  \u_启停控制电路_1  (.\F_输出时钟 (\启停控制电路_1_f_输出时钟 ), .\时钟 (CK), .\启动_为1时启动 (and_1_out), .\重置信号 (clr));
  and and_1 (and_1_out, \为1时启动 , not_1_out);
  Button \u_重置信号  (.out(clr));
  // Probe on R1R0
  IF_ID if_id_1 (
    .PC_1(adder_1_out), .\instruction_指令 (rom_1_data), .\clock_时钟信号 (clock), .\clear_清零信号 (clr),
    .\PC_1_输出 (\if_id_1_pc_1_输出 ), .\instruction_指令输出_2 (\if_id_1_instruction_指令输出_2 ), .\en_使能信号 (1'b1),
    .PC(PC_q), .PC_2(if_id_1_pc_2), .\instruction_指令输出 (\if_id_1_instruction_指令输出 ));  // open: 同步清零
  \IDecoder_指令译码器  \idecoder_指令译码器_1  (
    .\Instruction_指令 (\if_id_1_instruction_指令输出_2 ), .Funct(\idecoder_指令译码器_1_funct ),
    .rd(\idecoder_指令译码器_1_rd ), .rt(\idecoder_指令译码器_1_rt ), .rs(\idecoder_指令译码器_1_rs ),
    .OP(\idecoder_指令译码器_1_op ), .immediate(\idecoder_指令译码器_1_immediate ),
    .jump_address(\idecoder_指令译码器_1_jump_address ));  // open: P
  \控制器  \u_控制器_1  (
    .\OP_操作码 (\idecoder_指令译码器_1_op ), .Funct(\idecoder_指令译码器_1_funct ), .RegDst(\控制器_1_alusrc [8]),
    .\lui_lui指令产生的单一控制信号 (\控制器_1_alusrc [6]), .MemWrite(\控制器_1_alusrc [4]), .MemtoReg(\控制器_1_alusrc [2]),
    .RegWrite(\控制器_1_alusrc [1]), .ALUSrc(\控制器_1_alusrc [0]), .ALUop(\控制器_1_aluop ),
    .disp(\控制器_1_alusrc [7]), .\halt_停机控制信号 (\控制器_1_alusrc [3]), .\slt_slt控制信号 (\控制器_1_alusrc [5]));
  Hex_Digit_Display hex_digit_display_1 (.value(DISP_0[15:12]));  // open: dp
  Multiplexer #(.width(2), .enable("false")) multiplexer_2 (
    .in0(\idecoder_指令译码器_3_rt ), .in1(\idecoder_指令译码器_3_rd ), .out(multiplexer_2_out), .sel(MEM_WB_regdst_2));
  Hex_Digit_Display hex_digit_display_2 (.value(DISP_0[11:8]));  // open: dp
  Hex_Digit_Display hex_digit_display_3 (.value(DISP_0[7:4]));  // open: dp
  // 完全冲突检测 完全冲突检测_1: pin names not known; wires that end beside it: rom_1_data, MEM, EX, \if_id_1_instruction_指令输出 
  // Probe on \if_id_1_instruction_指令输出 
  \RF_寄存器堆  \rf_寄存器堆_1  (
    .Din(WB_in), .\CP_时钟输入 (clock), .Do1(\rf_寄存器堆_1_do1 ), .rs(\idecoder_指令译码器_1_rs ), .Do2(rt_1),
    .rt(\idecoder_指令译码器_1_rt ), .R1R0(R1R0), .R3R2(R3R2), .W(multiplexer_2_out),
    .\RegWrite_寄存器写控制信号 (MEM_WB_regwrite_2), .\ClR_清零信号 (clr));
  \Extend_立即数符号扩展  \extend_立即数符号扩展_1  (
    .\immidiate_立即数 (\idecoder_指令译码器_1_immediate ), .\OP_操作码 (\idecoder_指令译码器_1_op ),
    .\Extended_value_扩展结果 (\extend_立即数符号扩展_1_extended_value_扩展结果 ));
  // Probe on WB_in
  Hex_Digit_Display hex_digit_display_4 (.value(DISP_0[3:0]));  // open: dp
  Hex_Digit_Display hex_digit_display_5 (.value(DISP_1[15:12]));  // open: dp
  // Probe on if_id_1_pc_2
  Hex_Digit_Display hex_digit_display_6 (.value(DISP_1[11:8]));  // open: dp
  Hex_Digit_Display hex_digit_display_7 (.value(DISP_1[7:4]));  // open: dp
  ID_EX ID_EX (
    .PC(if_id_1_pc_2), .PC_2(ID_EX_pc_2), .instruction(\if_id_1_instruction_指令输出 ), .instruction_2(EX),
    .ALUop(\控制器_1_aluop ), .ALUop_2(ID_EX_aluop_2), .ALUSrc(\控制器_1_alusrc [0]), .ALUSrc_2(ID_EX_alusrc_2[0]),
    .RegWrite(\控制器_1_alusrc [1]), .RegWrite_2(ID_EX_alusrc_2[1]), .MemtoReg(\控制器_1_alusrc [2]),
    .MemtoReg_2(ID_EX_alusrc_2[2]), .halt(\控制器_1_alusrc [3]), .halt_2(ID_EX_alusrc_2[3]),
    .MemWrite(\控制器_1_alusrc [4]), .MemWrite_2(ID_EX_alusrc_2[4]), .slt(\控制器_1_alusrc [5]),
    .slt_2(ID_EX_alusrc_2[5]), .lui(\控制器_1_alusrc [6]), .lui_2(ID_EX_alusrc_2[6]), .disp(\控制器_1_alusrc [7]),
    .disp_2(ID_EX_alusrc_2[7]), .RegDst(\控制器_1_alusrc [8]), .RegDst_2(ID_EX_alusrc_2[8]),
    .offset(\idecoder_指令译码器_1_immediate ), .offset_2(ID_EX_offset_2), .jump(undriven_2),
    .jump_2(ID_EX_jump_2), .\OP_操作码 (\idecoder_指令译码器_1_op ), .\OP_操作码_2 (\ID_EX_op_操作码_2 ),
    .PC_1(\if_id_1_pc_1_输出 ), .PC_1_2(ID_EX_pc_1_2), .rs(\rf_寄存器堆_1_do1 ), .rs_2(ID_EX_rs_2), .rt(rt_1),
    .rt_2(rt_2), .\immediate_扩展后的立即数 (\extend_立即数符号扩展_1_extended_value_扩展结果 ),
    .\immediate_扩展后的立即数_2 (\ID_EX_immediate_扩展后的立即数_2 ), .\en_寄存器使能信号 (1'b1), .\clock_时钟信号 (clock),
    .\clear_清零信号 (clr));  // open: R3R2_2, R1R0, R1R0_2, R3R2, 同步清空
  Hex_Digit_Display hex_digit_display_8 (.value(DISP_1[3:0]));  // open: dp
  Multiplexer #(.width(16), .enable("false")) multiplexer_3 (
    .in0(rt_2), .in1(\ID_EX_immediate_扩展后的立即数_2 ), .out(multiplexer_3_out), .sel(ID_EX_alusrc_2[0]));
  // Probe on MEM_ALUout
  // Probe on MEM_MEMout
  // Probe on multiplexer_3_out
  Multiplexer #(.width(16), .enable("false")) multiplexer_4 (
    .in0(ID_EX_rs_2), .in1(\ID_EX_immediate_扩展后的立即数_2 ), .out(orig_a), .sel(ID_EX_alusrc_2[6]));
  Multiplexer #(.width(16), .enable("false")) multiplexer_5 (
    .in0(multiplexer_3_out), .in1(16'h8), .out(orig_b), .sel(ID_EX_alusrc_2[6]));
  Clock \u_时钟  (.out(CK));
  // Probe on orig_a
  // Probe on orig_b
  // Probe on EX
  // Probe on ID_EX_aluop_2
  // Probe on TO_A
  \Redirect_Unit_重定向单元  \redirect_unit_重定向单元_1  (
    .EX(EX), .MEM(MEM), .original_a(orig_a), .WB(WB), .Mem_ALUout(MEM_ALUout), .Mem_Memout(MEM_MEMout),
    .WB_in(WB_in), .original_b(orig_b), .TO_A(TO_A), .TO_B(TO_B));
  // Probe on TO_B
  \跳转地址形成部件  \u_跳转地址形成部件_1  (
    .\Offset_条件跳转地址_8位 (ID_EX_offset_2), .\PC_1_顺序下地址 (ID_EX_pc_1_2),
    .\jump_address_无条件跳转地址_12位 (ID_EX_jump_2), .\OP_操作码_4位 (\ID_EX_op_操作码_2 ),
    .jump_address(\跳转地址形成部件_1_jump_address ));
  \Flag_取一个数的最高位  \flag_取一个数的最高位_1  (
    .\value_输入的值 (\alu16位运算器_1_输出f ), .\flag_value的最高位 (\flag_取一个数的最高位_1_flag_value的最高位 ));
  \ALU16位运算器  \alu16位运算器_1  (
    .\输入A (TO_A), .\输入B (TO_B), .\控制信息C (ID_EX_aluop_2), .\零 (\alu16位运算器_1_零 ), .\溢出 (\alu16位运算器_1_溢出 ),
    .\输出F (\alu16位运算器_1_输出f ));  // open: 进位
  \Branch_控制部件  \branch_控制部件_1  (.\branch_是否跳转的控制信号 (\branch_控制部件_1_branch_是否跳转的控制信号 ));  // open: OP_操作码, zero_零标志位, 正负性
  circuit part_1 (.\falg_符号位 (\flag_取一个数的最高位_2_flag_value的最高位 ), .\overflow_溢出信号 (\alu16位运算器_1_溢出 ));  // open: out_3
  \IDecoder_指令译码器  \idecoder_指令译码器_2  (
    .\Instruction_指令 (EX), .Funct(\idecoder_指令译码器_2_funct ), .OP(\idecoder_指令译码器_2_op ));  // open: P, rd, rt, rs, immediate, jump_address
  \Flag_取一个数的最高位  \flag_取一个数的最高位_2  (
    .\value_输入的值 (multiplexer_6_out), .\flag_value的最高位 (\flag_取一个数的最高位_2_flag_value的最高位 ));
  slt_0_1_2 slt_0_1_1 (
    .\falg_符号位 (\flag_取一个数的最高位_1_flag_value的最高位 ), .\overflow_溢出信号 (\alu16位运算器_1_溢出 ),
    .\OP_操作码 (\idecoder_指令译码器_2_op ), .\Funct_函数字段 (\idecoder_指令译码器_2_funct ), .slt_0_1(slt_0_1_1_slt_0_1));
  Multiplexer #(.width(16), .enable("false")) multiplexer_6 (
    .in0(\alu16位运算器_1_输出f ), .in1(slt_0_1_1_slt_0_1), .out(multiplexer_6_out), .sel(ID_EX_alusrc_2[5]));
  // Probe on ID_EX_pc_2
  // Probe on multiplexer_6_out
  EX_MEM EX_MEM (
    .PC(ID_EX_pc_2), .PC_2(EX_MEM_pc_2), .instruction(EX), .instruction_2(MEM), .ALUop(ID_EX_aluop_2),
    .ALUop_2(EX_MEM_aluop_2), .ALUSrc(ID_EX_alusrc_2[0]), .ALUSrc_2(EX_MEM_alusrc_2[0]),
    .RegWrite(ID_EX_alusrc_2[1]), .RegWrite_2(EX_MEM_alusrc_2[1]), .MemtoReg(ID_EX_alusrc_2[2]),
    .MemtoReg_2(EX_MEM_alusrc_2[2]), .halt(ID_EX_alusrc_2[3]), .halt_2(EX_MEM_alusrc_2[3]),
    .MemWrite(ID_EX_alusrc_2[4]), .MemWrite_2(EX_MEM_alusrc_2[4]), .slt(ID_EX_alusrc_2[5]),
    .slt_2(EX_MEM_alusrc_2[5]), .lui(ID_EX_alusrc_2[6]), .lui_2(EX_MEM_alusrc_2[6]),
    .disp(ID_EX_alusrc_2[7]), .disp_2(EX_MEM_alusrc_2[7]), .RegDst(ID_EX_alusrc_2[8]),
    .RegDst_2(EX_MEM_alusrc_2[8]), .\jump_address_跳转地址 (\跳转地址形成部件_1_jump_address ),
    .\jump_address_跳转地址_2 (\EX_MEM_jump_address_跳转地址_2 ), .\zero_0标志位 (\alu16位运算器_1_零 ),
    .\zero_0标志位_2 (\EX_MEM_zero_0标志位_2 ), .\over_溢出标志位 (\alu16位运算器_1_溢出 ),
    .\over_溢出标志位_2 (\EX_MEM_over_溢出标志位_2 ), .ALUout(multiplexer_6_out), .ALUout_2(MEM_ALUout), .rt(rt_2),
    .rt_2(EX_MEM_rt_2), .\en_寄存器使能信号 (1'b1), .\clock_时钟信号 (clock), .\clear_清零信号 (clr), .\同步清零 (1'b0));  // open: R3R2, R3R2_2, R1R0, R1R0_2
  Multiplexer #(.width(16), .enable("false")) multiplexer_7 (
    .in0(EX_MEM_rt_2), .in1(rt_1), .out(multiplexer_7_out), .sel(\sw_重定向_1_sw_con ));
  \sw_重定向  \sw_重定向_1  (.MEM(MEM), .WB(END_1), .sw_con(\sw_重定向_1_sw_con ));
  \Flag_取一个数的最高位  \flag_取一个数的最高位_3  (.\value_输入的值 (MEM_ALUout));  // open: flag_value的最高位
  // Probe on MEM_ALUout
  // Probe on MEM
  // Probe on EX_MEM_pc_2
  RAM #(.addrWidth(16), .dataWidth(16), .bus("separate")) ram_1 (
    .addr(MEM_ALUout), .din(multiplexer_8_out), .data(MEM_MEMout), .str(EX_MEM_alusrc_2[4]), .clk(clock),
    .ld(1'b1), .clr(clr));  // open: sel
  MEM_WB MEM_WB (
    .PC(EX_MEM_pc_2), .PC_2(MEM_WB_pc_2), .instruction(MEM), .instruction_2(WB), .ALUop(EX_MEM_aluop_2),
    .ALUop_2(MEM_WB_aluop_2), .ALUSrc(EX_MEM_alusrc_2[0]), .ALUSrc_2(MEM_WB_alusrc_2),
    .RegWrite(EX_MEM_alusrc_2[1]), .RegWrite_2(MEM_WB_regwrite_2), .MemtoReg(EX_MEM_alusrc_2[2]),
    .MemtoReg_2(MEM_WB_memtoreg_2), .halt(EX_MEM_alusrc_2[3]), .halt_2(MEM_WB_halt_2),
    .MemWrite(EX_MEM_alusrc_2[4]), .MemWrite_2(MEM_WB_memwrite_2), .slt(EX_MEM_alusrc_2[5]),
    .slt_2(MEM_WB_slt_2), .lui(EX_MEM_alusrc_2[6]), .lui_2(MEM_WB_lui_2), .disp(EX_MEM_alusrc_2[7]),
    .disp_2(MEM_WB_disp_2), .RegDst(EX_MEM_alusrc_2[8]), .RegDst_2(MEM_WB_regdst_2),
    .\zero_0标志位 (\EX_MEM_zero_0标志位_2 ), .\zero_0标志位_2 (\MEM_WB_zero_0标志位_2 ),
    .\over_溢出标志位 (\EX_MEM_over_溢出标志位_2 ), .ALUout(MEM_ALUout), .ALUout_2(MEM_WB_aluout_2),
    .MemOut(MEM_MEMout), .MemOut_2(MEM_WB_memout_2), .\en_寄存器使能信号 (1'b1), .\clock_时钟信号 (clock),
    .\clear_清零信号 (clr), .\jump_address_跳转地址 (\EX_MEM_jump_address_跳转地址_2 ));  // open: over_溢出标志位_2, jump_address_跳转地址_2, R3R2, R3R2_2, R1R0, R1R0_2
  Multiplexer #(.width(16), .enable("false")) multiplexer_8 (
    .in0(multiplexer_7_out), .in1(WB_in), .out(multiplexer_8_out), .sel(\sw_重定向_2_sw_con ));
  \sw_重定向  \sw_重定向_2  (.MEM(MEM), .WB(WB), .sw_con(\sw_重定向_2_sw_con ));
  // Probe on MEM_WB_pc_2
  // Probe on MEM_WB_halt_2
  Multiplexer #(.width(16), .enable("false")) multiplexer_9 (
    .in0(MEM_WB_aluout_2), .in1(MEM_WB_memout_2), .out(WB_in), .sel(MEM_WB_memtoreg_2));
  // Probe on MEM_WB_aluout_2
  // Probe on WB_in
  // Probe on WB
  Bit_Extender #(.out_width(1)) bit_extender_1 (.in(\idecoder_指令译码器_3_immediate ), .out(color));
  \IDecoder_指令译码器  \idecoder_指令译码器_3  (
    .\Instruction_指令 (WB), .rd(\idecoder_指令译码器_3_rd ), .rt(\idecoder_指令译码器_3_rt ), .rs(num),
    .immediate(\idecoder_指令译码器_3_immediate ));  // open: Funct, P, OP, jump_address
  // Probe on \idecoder_指令译码器_3_rt 
  Register #(.width(16)) register_1 (.D(WB), .Q(END_1), .clk(clock), .clr(clr));  // open: en
  Register #(.width(16)) register_2 (.D(END_1), .Q(END_2), .clk(clock), .clr(clr));  // open: en

  // Other names for the same wires on the sheet: start = \为1时启动 

  // Notes on the sheet:
  //   contents of rom_1 (hex, n*v repeats v):
  //   7000 8001 7500 8501 7f00 8f01 4400 4c01 444 4400 dc2 4c01 487 1801 b008 7000 8001 7500 850f 443 442
  //   1c4 4c00 7500 8503 dc6 4c00 7500 8504 dc6 4c00 dc6 4c00 dc6 4c00 7000 8001 7500 850f 1c4 dc6 7000
  //   8000 7500 8504 520c 985 985 8001 700f dc4 cc0 4c00 dc4 cc0 4c00 dc4 cc0 4c00 dc4 cc0 4c00 8001 700f
  //   204 dc5 cc0 4c00 dc5 cc0 4c00 dc5 cc0 4c00 dc5 cc0 4c00 205 22e1 7000 8000 7500 850f 4000 4401 9200
  //   9700 3b02 a600 a300 85ff 21f7 b05f 0 0 8001 7500 850f 21f0 c000 7000 8400
endmodule

module \分支预测单元  (
  input  [15:0] in_1
);

  wire [15:0] ID;

  // Redirect_Unit_重定向单元 redirect_unit_重定向单元_1: pin names not known; wires that end beside it: ID
endmodule
